// Logisim project cpuprojectworkinprogress.circ as structural Verilog
module main (
  input  [31:0] address_bus_low,
  input  [31:0] data_bus_low,
  input  [31:0] address_bus_high,
  input  [31:0] data_bus_high,
  input  clock,
  input  advance_microinstruction,
  input  manual_control_signals,
  input  [31:0] in_8,
  input  [31:0] upper_control_signals,
  output [31:0] lower_part_of_instruction_pointer,
  output [31:0] higher_part_of_instruction_pointer,
  output [7:0] lower_8_bits_of_instruction,
  output [6:0] current_microinstruction,
  output [31:0] address_bus_high__output,
  output [31:0] data_bus_high__output,
  output [31:0] address_bus_low__output,
  output [31:0] data_bus_low__output,
  output [31:0] current_microinstructions,
  output memory_read_enable,
  output memory_write_enable
);

  wire alu_1_less_than, alu_1_overflow, alu_1_result_is_zero, and_1_out, not_1_out;
  wire [2:0] flag_register_1_output;
  wire [31:0] controlled_buffer_7_out, controlled_buffer_16_out,
       instruction_decoder_1_microinstructions__upper, n64_bit_register_6_higher_32_bits_of_output,
       stack_pointer_1_higher_part_of_output, stack_pointer_1_lower_part_of_output;
  wire [31:8] n64_bit_register_6_lower_32_bits_of_output;

  Pull_Resistor pull_resistor_1 (.node(address_bus_low__output));
  assign address_bus_low__output = controlled_buffer_7_out[0] ? address_bus_low : 32'bz;  // Controlled_Buffer controlled_buffer_1
  assign address_bus_high__output = controlled_buffer_7_out[0] ? address_bus_high : 32'bz;  // Controlled_Buffer controlled_buffer_2
  Pull_Resistor pull_resistor_2 (.node(address_bus_high__output));
  _64_bit_register u_64_bit_register_1 (
    .lower_32_bits_of_input(data_bus_low__output), .higher_32_bits_of_input(data_bus_high__output),
    .write_enable(controlled_buffer_16_out[5]), .clock(clock), .output_enable(controlled_buffer_16_out[6]),
    .higher_32_bits_of_output(address_bus_high__output), .lower_32_bits_of_output(address_bus_low__output));
  assign address_bus_low__output = controlled_buffer_7_out[5] ? lower_part_of_instruction_pointer : 32'bz;  // Controlled_Buffer controlled_buffer_3
  program_counter program_counter_1 (
    .manual_value(controlled_buffer_7_out[2]), .write_enable(controlled_buffer_7_out[4]), .clock(clock),
    .output_enable(1'b1), .lower_manual_value(address_bus_low__output),
    .higher_manual_value(address_bus_high__output),
    .lower_32_bits_of_output(lower_part_of_instruction_pointer),
    .higher_32_bits_of_output(higher_part_of_instruction_pointer));
  assign address_bus_high__output = controlled_buffer_7_out[5] ? higher_part_of_instruction_pointer : 32'bz;  // Controlled_Buffer controlled_buffer_4
  assign data_bus_high__output = controlled_buffer_16_out[4] ? address_bus_high__output : 32'bz;  // Controlled_Buffer controlled_buffer_5
  assign data_bus_low__output = controlled_buffer_16_out[4] ? address_bus_low__output : 32'bz;  // Controlled_Buffer controlled_buffer_6
  assign {controlled_buffer_7_out[31:22], memory_write_enable, memory_read_enable, controlled_buffer_7_out[19:0]} = manual_control_signals ? in_8 : 32'bz;  // Controlled_Buffer controlled_buffer_7
  assign data_bus_low__output = controlled_buffer_7_out[19] ? data_bus_low : 32'bz;  // Controlled_Buffer controlled_buffer_8
  assign address_bus_high__output = controlled_buffer_16_out[2] ? data_bus_high__output : 32'bz;  // Controlled_Buffer controlled_buffer_9
  assign address_bus_low__output = controlled_buffer_16_out[2] ? data_bus_low__output : 32'bz;  // Controlled_Buffer controlled_buffer_10
  assign data_bus_high__output = controlled_buffer_7_out[19] ? data_bus_high : 32'bz;  // Controlled_Buffer controlled_buffer_11
  Pull_Resistor pull_resistor_3 (.node(data_bus_low__output));
  Pull_Resistor pull_resistor_4 (.node(data_bus_high__output));
  assign {controlled_buffer_7_out[31:22], memory_write_enable, memory_read_enable, controlled_buffer_7_out[19:0]} = not_1_out ? current_microinstructions : 32'bz;  // Controlled_Buffer controlled_buffer_12
  not not_1 (not_1_out, manual_control_signals);
  assign data_bus_low__output = controlled_buffer_7_out[23] ? n64_bit_register_6_higher_32_bits_of_output : 32'bz;  // Controlled_Buffer controlled_buffer_13
  ALU alu_1 (
    .lower_32_bits(data_bus_low__output), .higher_32_bits(data_bus_high__output), .overflow(alu_1_overflow),
    .lower_32_bits_of_output(data_bus_low__output), .store_a(controlled_buffer_7_out[8]),
    .subtract(controlled_buffer_7_out[9]), .store_b(controlled_buffer_7_out[10]), .clock(clock),
    .higher_32_bits_of_output(data_bus_high__output), .output_enable(controlled_buffer_7_out[11]),
    .less_than(alu_1_less_than), .result_is_zero(alu_1_result_is_zero),
    .increment(controlled_buffer_16_out[3]));
  Controlled_Buffer controlled_buffer_14 (.in(controlled_buffer_7_out[14]));  // open: out, en
  assign address_bus_low__output = controlled_buffer_7_out[22] ? n64_bit_register_6_higher_32_bits_of_output : 32'bz;  // Controlled_Buffer controlled_buffer_15
  _64_bit_register u_64_bit_register_2 (
    .lower_32_bits_of_input(data_bus_low__output), .higher_32_bits_of_input(data_bus_high__output),
    .write_enable(controlled_buffer_7_out[1]), .clock(clock), .output_enable(controlled_buffer_7_out[3]),
    .higher_32_bits_of_output(data_bus_high__output), .lower_32_bits_of_output(data_bus_low__output));
  _64_bit_register u_64_bit_register_3 (
    .lower_32_bits_of_input(data_bus_low__output), .higher_32_bits_of_input(data_bus_high__output),
    .write_enable(controlled_buffer_7_out[6]), .clock(clock), .output_enable(controlled_buffer_7_out[7]),
    .higher_32_bits_of_output(data_bus_high__output), .lower_32_bits_of_output(data_bus_low__output));
  _64_bit_register u_64_bit_register_4 (
    .lower_32_bits_of_input(data_bus_low__output), .higher_32_bits_of_input(data_bus_high__output),
    .write_enable(controlled_buffer_7_out[15]), .clock(clock), .output_enable(controlled_buffer_7_out[16]),
    .higher_32_bits_of_output(data_bus_high__output), .lower_32_bits_of_output(data_bus_low__output));
  _64_bit_register u_64_bit_register_5 (
    .lower_32_bits_of_input(data_bus_low__output), .higher_32_bits_of_input(data_bus_high__output),
    .write_enable(controlled_buffer_7_out[18]), .clock(clock), .output_enable(controlled_buffer_7_out[17]),
    .higher_32_bits_of_output(data_bus_high__output), .lower_32_bits_of_output(data_bus_low__output));
  assign controlled_buffer_16_out = manual_control_signals ? upper_control_signals : 32'bz;  // Controlled_Buffer controlled_buffer_16
  _64_bit_register u_64_bit_register_6 (
    .lower_32_bits_of_input(data_bus_low__output), .higher_32_bits_of_input(data_bus_high__output),
    .write_enable(controlled_buffer_7_out[12]), .clock(clock), .output_enable(1'b1),
    .higher_32_bits_of_output(n64_bit_register_6_higher_32_bits_of_output),
    .lower_32_bits_of_output({n64_bit_register_6_lower_32_bits_of_output, lower_8_bits_of_instruction}));
  assign data_bus_high__output = controlled_buffer_7_out[29] ? stack_pointer_1_higher_part_of_output : 32'bz;  // Controlled_Buffer controlled_buffer_17
  assign data_bus_low__output = controlled_buffer_7_out[29] ? stack_pointer_1_lower_part_of_output : 32'bz;  // Controlled_Buffer controlled_buffer_18
  assign address_bus_high__output = controlled_buffer_7_out[31] ? stack_pointer_1_higher_part_of_output : 32'bz;  // Controlled_Buffer controlled_buffer_19
  assign address_bus_low__output = controlled_buffer_7_out[31] ? stack_pointer_1_lower_part_of_output : 32'bz;  // Controlled_Buffer controlled_buffer_20
  _64_bit_register u_64_bit_register_7 (
    .lower_32_bits_of_input(data_bus_low__output), .higher_32_bits_of_input(data_bus_high__output),
    .write_enable(controlled_buffer_16_out[7]), .clock(clock), .output_enable(controlled_buffer_16_out[8]),
    .higher_32_bits_of_output(data_bus_high__output), .lower_32_bits_of_output(data_bus_low__output));
  and and_1 (and_1_out, clock, controlled_buffer_7_out[24]);
  microinstruction_counter microinstruction_counter_1 (
    .write_enable(advance_microinstruction), .clock(clock), .output_enable(advance_microinstruction),
    .reset_to_zero(and_1_out), .current_microstep(current_microinstruction));
  Stack_pointer stack_pointer_1 (
    .write_enable__pop_or_push_or_manual_value(controlled_buffer_7_out[26]), .clock(clock),
    .push(controlled_buffer_7_out[27]), .pop(controlled_buffer_7_out[28]), .output_enable(1'b1),
    .lower_part_of_manual_input(data_bus_low__output), .manual_value(controlled_buffer_7_out[30]),
    .higher_part_of_manual_input(data_bus_high__output),
    .lower_part_of_output(stack_pointer_1_lower_part_of_output),
    .higher_part_of_output(stack_pointer_1_higher_part_of_output));
  instruction_decoder instruction_decoder_1 (
    .current_microinstruction(current_microinstruction), .is_microstep_zero(1'b1),
    .current_instruction__lowest_8_bits(lower_8_bits_of_instruction), .clock(clock),
    .flags(flag_register_1_output), .microinstructions(current_microinstructions),
    .microinstructions__upper(instruction_decoder_1_microinstructions__upper));
  Pull_Resistor pull_resistor_5 (.node(current_microinstructions));
  Pull_Resistor pull_resistor_6 (.node(instruction_decoder_1_microinstructions__upper));
  flag_register flag_register_1 (
    .store_flags(controlled_buffer_7_out[25]), .is_zero(alu_1_result_is_zero), .overflow(alu_1_overflow),
    .less_than(alu_1_less_than), .clock(clock), .\output (flag_register_1_output));
  _64_bit_register u_64_bit_register_8 (
    .lower_32_bits_of_input(data_bus_low__output), .higher_32_bits_of_input(data_bus_high__output),
    .write_enable(controlled_buffer_16_out[0]), .clock(clock), .output_enable(controlled_buffer_16_out[1]),
    .higher_32_bits_of_output(data_bus_high__output), .lower_32_bits_of_output(data_bus_low__output));
  assign controlled_buffer_16_out = not_1_out ? instruction_decoder_1_microinstructions__upper : 32'bz;  // Controlled_Buffer controlled_buffer_21
endmodule

module _64_bit_adder__add_and_subtract (
  input  [31:0] lower_32_bits_of_a,
  input  [31:0] upper_32_bits_of_a,
  input  [31:0] lower_32_bits_of_b,
  input  [31:0] upper_32_bits_of_b,
  input  subtract,
  output overflow,
  output [31:0] lower_32_bits_from_output,
  output [31:0] upper_32_bits_from_output
);

  wire n8_bit_adder_2_overflow, n8_bit_adder_3_overflow, n8_bit_adder_4_overflow, n8_bit_adder_5_overflow,
       n8_bit_adder_6_overflow, n8_bit_adder_7_overflow, n8_bit_adder_8_overflow;

  _8_bit_adder u_8_bit_adder_1 (
    .input_a(upper_32_bits_of_a[31:24]), .input_b(upper_32_bits_of_b[31:24]), .subtract(subtract),
    .carry_in(n8_bit_adder_2_overflow), .overflow(overflow), .\output (upper_32_bits_from_output[31:24]));
  _8_bit_adder u_8_bit_adder_2 (
    .input_a(upper_32_bits_of_a[23:16]), .input_b(upper_32_bits_of_b[23:16]), .subtract(subtract),
    .carry_in(n8_bit_adder_3_overflow), .overflow(n8_bit_adder_2_overflow),
    .\output (upper_32_bits_from_output[23:16]));
  _8_bit_adder u_8_bit_adder_3 (
    .input_a(upper_32_bits_of_a[15:8]), .input_b(upper_32_bits_of_b[15:8]), .subtract(subtract),
    .carry_in(n8_bit_adder_4_overflow), .overflow(n8_bit_adder_3_overflow),
    .\output (upper_32_bits_from_output[15:8]));
  _8_bit_adder u_8_bit_adder_4 (
    .input_a(upper_32_bits_of_a[7:0]), .input_b(upper_32_bits_of_b[7:0]), .subtract(subtract),
    .carry_in(n8_bit_adder_5_overflow), .overflow(n8_bit_adder_4_overflow),
    .\output (upper_32_bits_from_output[7:0]));
  _8_bit_adder u_8_bit_adder_5 (
    .input_a(lower_32_bits_of_a[31:24]), .input_b(lower_32_bits_of_b[31:24]), .subtract(subtract),
    .carry_in(n8_bit_adder_6_overflow), .overflow(n8_bit_adder_5_overflow),
    .\output (lower_32_bits_from_output[31:24]));
  _8_bit_adder u_8_bit_adder_6 (
    .input_a(lower_32_bits_of_a[23:16]), .input_b(lower_32_bits_of_b[23:16]), .subtract(subtract),
    .carry_in(n8_bit_adder_7_overflow), .overflow(n8_bit_adder_6_overflow),
    .\output (lower_32_bits_from_output[23:16]));
  _8_bit_adder u_8_bit_adder_7 (
    .input_a(lower_32_bits_of_a[15:8]), .input_b(lower_32_bits_of_b[15:8]), .subtract(subtract),
    .carry_in(n8_bit_adder_8_overflow), .overflow(n8_bit_adder_7_overflow),
    .\output (lower_32_bits_from_output[15:8]));
  _8_bit_adder u_8_bit_adder_8 (
    .input_a(lower_32_bits_of_a[7:0]), .input_b(lower_32_bits_of_b[7:0]), .subtract(subtract),
    .carry_in(subtract), .overflow(n8_bit_adder_8_overflow), .\output (lower_32_bits_from_output[7:0]));
  Pull_Resistor pull_resistor_1 (.node(overflow));
endmodule

module _8_bit_adder (
  input  [7:0] input_a,
  input  [7:0] input_b,
  input  subtract,
  input  carry_in,
  output overflow,
  output [7:0] \output 
);

  wire full_adder_2_carry_out, full_adder_3_carry_out, full_adder_4_carry_out, full_adder_5_carry_out,
       full_adder_6_carry_out, full_adder_7_carry_out, full_adder_8_carry_out;
  wire [7:0] n8_bit_xor_1_output;

  _8_bit_xor u_8_bit_xor_1 (.\input (input_b), .invert(subtract), .\output (n8_bit_xor_1_output));
  full_adder full_adder_1 (
    .input_a(input_a[7]), .input_b(n8_bit_xor_1_output[7]), .carry_in(full_adder_2_carry_out),
    .sum(\output [7]), .carry_out(overflow));
  full_adder full_adder_2 (
    .input_a(input_a[6]), .input_b(n8_bit_xor_1_output[6]), .carry_in(full_adder_3_carry_out),
    .sum(\output [6]), .carry_out(full_adder_2_carry_out));
  full_adder full_adder_3 (
    .input_a(input_a[5]), .input_b(n8_bit_xor_1_output[5]), .carry_in(full_adder_4_carry_out),
    .sum(\output [5]), .carry_out(full_adder_3_carry_out));
  full_adder full_adder_4 (
    .input_a(input_a[4]), .input_b(n8_bit_xor_1_output[4]), .carry_in(full_adder_5_carry_out),
    .sum(\output [4]), .carry_out(full_adder_4_carry_out));
  full_adder full_adder_5 (
    .input_a(input_a[3]), .input_b(n8_bit_xor_1_output[3]), .carry_in(full_adder_6_carry_out),
    .sum(\output [3]), .carry_out(full_adder_5_carry_out));
  full_adder full_adder_6 (
    .input_a(input_a[2]), .input_b(n8_bit_xor_1_output[2]), .carry_in(full_adder_7_carry_out),
    .sum(\output [2]), .carry_out(full_adder_6_carry_out));
  full_adder full_adder_7 (
    .input_a(input_a[1]), .input_b(n8_bit_xor_1_output[1]), .carry_in(full_adder_8_carry_out),
    .sum(\output [1]), .carry_out(full_adder_7_carry_out));
  full_adder full_adder_8 (
    .input_a(input_a[0]), .input_b(n8_bit_xor_1_output[0]), .carry_in(carry_in), .sum(\output [0]),
    .carry_out(full_adder_8_carry_out));
endmodule

module full_adder (
  input  input_a,
  input  input_b,
  input  carry_in,
  output sum,
  output carry_out
);

  wire and_1_out, and_2_out, xor_1_out;

  xor xor_1 (xor_1_out, input_a, input_b);
  and and_1 (and_1_out, input_a, input_b);
  and and_2 (and_2_out, carry_in, xor_1_out);
  xor xor_2 (sum, xor_1_out, carry_in);
  or or_1 (carry_out, and_2_out, and_1_out);
endmodule

module _8_bit_xor (
  input  [7:0] \input ,
  input  invert,
  output [7:0] \output 
);

  xor xor_1 (\output [0], invert, \input [0]);
  xor xor_2 (\output [1], invert, \input [1]);
  xor xor_3 (\output [2], invert, \input [2]);
  xor xor_4 (\output [3], invert, \input [3]);
  xor xor_5 (\output [4], invert, \input [4]);
  xor xor_6 (\output [5], invert, \input [5]);
  xor xor_7 (\output [6], invert, \input [6]);
  xor xor_8 (\output [7], invert, \input [7]);
endmodule

module _64_bit_adder_with_control_signals (
  input  [31:0] lower_32_bit_of_input_a,
  input  overflow_output_enable,
  input  [31:0] higher_32_bit_of_input_a,
  input  [31:0] lower_32_bit_of_input_b,
  input  [31:0] higher_32_bit_of_input_b,
  input  subtract,
  input  output_enable_the_64_bits,
  output overflow,
  output [31:0] lower_32_bits,
  output [31:0] upper_32_bits
);

  wire n64_bit_adder_add_and_subtract_1_overflow;
  wire [31:0] n64_bit_adder_add_and_subtract_1_lower_32_bits_from_output,
       n64_bit_adder_add_and_subtract_1_upper_32_bits_from_output;

  Pull_Resistor pull_resistor_1 (.node(overflow));
  _64_bit_adder__add_and_subtract u_64_bit_adder_add_and_subtract_1 (
    .lower_32_bits_of_a(lower_32_bit_of_input_a), .upper_32_bits_of_a(higher_32_bit_of_input_a),
    .lower_32_bits_of_b(lower_32_bit_of_input_b), .upper_32_bits_of_b(higher_32_bit_of_input_b),
    .subtract(subtract), .overflow(n64_bit_adder_add_and_subtract_1_overflow),
    .lower_32_bits_from_output(n64_bit_adder_add_and_subtract_1_lower_32_bits_from_output),
    .upper_32_bits_from_output(n64_bit_adder_add_and_subtract_1_upper_32_bits_from_output));
  assign overflow = overflow_output_enable ? n64_bit_adder_add_and_subtract_1_overflow : 1'bz;  // Controlled_Buffer controlled_buffer_1
  assign lower_32_bits = output_enable_the_64_bits ? n64_bit_adder_add_and_subtract_1_lower_32_bits_from_output : 32'bz;  // Controlled_Buffer controlled_buffer_2
  assign upper_32_bits = output_enable_the_64_bits ? n64_bit_adder_add_and_subtract_1_upper_32_bits_from_output : 32'bz;  // Controlled_Buffer controlled_buffer_3
  Pull_Resistor pull_resistor_2 (.node(lower_32_bits));
  Pull_Resistor pull_resistor_3 (.node(upper_32_bits));
endmodule

module _64_bit_register (
  input  [31:0] lower_32_bits_of_input,
  input  [31:0] higher_32_bits_of_input,
  input  write_enable,
  input  clock,
  input  output_enable,
  output [31:0] higher_32_bits_of_output,
  output [31:0] lower_32_bits_of_output
);

  wire [7:0] n8_bit_register_1_output, n8_bit_register_2_output, n8_bit_register_3_output,
       n8_bit_register_4_output, n8_bit_register_5_output, n8_bit_register_6_output,
       n8_bit_register_7_output, n8_bit_register_8_output;

  _8_bit_register u_8_bit_register_1 (
    .input_data(higher_32_bits_of_input[31:24]), .output_enable(output_enable), .write_enable(write_enable),
    .clock(clock), .\output (n8_bit_register_1_output));
  _8_bit_register u_8_bit_register_2 (
    .input_data(higher_32_bits_of_input[23:16]), .output_enable(output_enable), .write_enable(write_enable),
    .clock(clock), .\output (n8_bit_register_2_output));
  _8_bit_register u_8_bit_register_3 (
    .input_data(higher_32_bits_of_input[15:8]), .output_enable(output_enable), .write_enable(write_enable),
    .clock(clock), .\output (n8_bit_register_3_output));
  _8_bit_register u_8_bit_register_4 (
    .input_data(higher_32_bits_of_input[7:0]), .output_enable(output_enable), .write_enable(write_enable),
    .clock(clock), .\output (n8_bit_register_4_output));
  _8_bit_register u_8_bit_register_5 (
    .input_data(lower_32_bits_of_input[31:24]), .output_enable(output_enable), .write_enable(write_enable),
    .clock(clock), .\output (n8_bit_register_5_output));
  _8_bit_register u_8_bit_register_6 (
    .input_data(lower_32_bits_of_input[23:16]), .output_enable(output_enable), .write_enable(write_enable),
    .clock(clock), .\output (n8_bit_register_6_output));
  _8_bit_register u_8_bit_register_7 (
    .input_data(lower_32_bits_of_input[15:8]), .output_enable(output_enable), .write_enable(write_enable),
    .clock(clock), .\output (n8_bit_register_7_output));
  _8_bit_register u_8_bit_register_8 (
    .input_data(lower_32_bits_of_input[7:0]), .output_enable(output_enable), .write_enable(write_enable),
    .clock(clock), .\output (n8_bit_register_8_output));
  assign higher_32_bits_of_output = output_enable ? {n8_bit_register_1_output, n8_bit_register_2_output, n8_bit_register_3_output, n8_bit_register_4_output} : 32'bz;  // Controlled_Buffer controlled_buffer_1
  assign lower_32_bits_of_output = output_enable ? {n8_bit_register_5_output, n8_bit_register_6_output, n8_bit_register_7_output, n8_bit_register_8_output} : 32'bz;  // Controlled_Buffer controlled_buffer_2
endmodule

module _8_bit_register (
  input  [7:0] input_data,
  input  output_enable,
  input  write_enable,
  input  clock,
  output [7:0] \output 
);

  wire [7:0] register_1_q;

  Register register_1 (.D(input_data), .en(write_enable), .Q(register_1_q), .clk(clock));  // open: clr
  assign \output  = output_enable ? register_1_q : 8'bz;  // Controlled_Buffer controlled_buffer_1
  Pull_Resistor pull_resistor_1 (.node(\output ));
endmodule

module memory (
  input  [31:0] lower_32_bits_of_value,
  input  [9:0] in_2,
  input  write_enable,
  input  read_enable,
  input  clock,
  input  [31:0] upper_32_bits_of_value,
  output [31:0] lower_32_bits_of_output,
  output [31:0] higher_32_bits_of_output
);

  wire [31:0] n4_rows_1_memory_output, n4_rows_5_memory_output;

  assign lower_32_bits_of_output = read_enable ? n4_rows_1_memory_output : 32'bz;  // Controlled_Buffer controlled_buffer_1
  _4_rows u_4_rows_1 (
    .address(in_2), .data_input(lower_32_bits_of_value[7:0]), .write_enable(write_enable),
    .read_enable(read_enable), .clock(clock), .memory_output(n4_rows_1_memory_output[7:0]));
  _4_rows u_4_rows_2 (
    .address(in_2), .data_input(lower_32_bits_of_value[15:8]), .write_enable(write_enable),
    .read_enable(read_enable), .clock(clock), .memory_output(n4_rows_1_memory_output[15:8]));
  assign higher_32_bits_of_output = read_enable ? n4_rows_5_memory_output : 32'bz;  // Controlled_Buffer controlled_buffer_2
  _4_rows u_4_rows_3 (
    .address(in_2), .data_input(lower_32_bits_of_value[23:16]), .write_enable(write_enable),
    .read_enable(read_enable), .clock(clock), .memory_output(n4_rows_1_memory_output[23:16]));
  _4_rows u_4_rows_4 (
    .address(in_2), .data_input(lower_32_bits_of_value[31:24]), .write_enable(write_enable),
    .read_enable(read_enable), .clock(clock), .memory_output(n4_rows_1_memory_output[31:24]));
  _4_rows u_4_rows_5 (
    .address(in_2), .data_input(upper_32_bits_of_value[7:0]), .write_enable(write_enable),
    .read_enable(read_enable), .clock(clock), .memory_output(n4_rows_5_memory_output[7:0]));
  _4_rows u_4_rows_6 (
    .address(in_2), .data_input(upper_32_bits_of_value[15:8]), .write_enable(write_enable),
    .read_enable(read_enable), .clock(clock), .memory_output(n4_rows_5_memory_output[15:8]));
  _4_rows u_4_rows_7 (
    .address(in_2), .data_input(upper_32_bits_of_value[23:16]), .write_enable(write_enable),
    .read_enable(read_enable), .clock(clock), .memory_output(n4_rows_5_memory_output[23:16]));
  _4_rows u_4_rows_8 (
    .address(in_2), .data_input(upper_32_bits_of_value[31:24]), .write_enable(write_enable),
    .read_enable(read_enable), .clock(clock), .memory_output(n4_rows_5_memory_output[31:24]));
endmodule

module _1_byte_of_memory (
  input  x_select,
  input  y_select,
  input  [7:0] byte_to_be_written,
  input  write_enable,
  input  clock,
  input  output_enable,
  output [7:0] \output 
);

  wire and_1_out, and_2_out, and_3_out;
  wire [7:0] register_1_q;

  and and_1 (and_1_out, write_enable, and_2_out);
  and and_2 (and_2_out, x_select, y_select);
  Register register_1 (.D(byte_to_be_written), .en(and_1_out), .Q(register_1_q), .clk(clock));  // open: clr
  and and_3 (and_3_out, output_enable, and_2_out);
  assign \output  = and_3_out ? register_1_q : 8'bz;  // Controlled_Buffer controlled_buffer_1
endmodule

module _8_in_a_row (
  input  [7:0] data_input,
  input  [7:0] x_select__8_bits,
  input  write_enable,
  input  clock,
  input  read_enable,
  input  [7:0] y_select__8_bits,
  output [7:0] data_output
);

  _1_byte_of_memory u_1_byte_of_memory_1 (
    .x_select(x_select__8_bits[0]), .y_select(y_select__8_bits[0]), .byte_to_be_written(data_input),
    .write_enable(write_enable), .clock(clock), .output_enable(read_enable), .\output (data_output));
  _1_byte_of_memory u_1_byte_of_memory_2 (
    .x_select(x_select__8_bits[1]), .y_select(y_select__8_bits[1]), .byte_to_be_written(data_input),
    .write_enable(write_enable), .clock(clock), .output_enable(read_enable), .\output (data_output));
  _1_byte_of_memory u_1_byte_of_memory_3 (
    .x_select(x_select__8_bits[2]), .y_select(y_select__8_bits[2]), .byte_to_be_written(data_input),
    .write_enable(write_enable), .clock(clock), .output_enable(read_enable), .\output (data_output));
  _1_byte_of_memory u_1_byte_of_memory_4 (
    .x_select(x_select__8_bits[3]), .y_select(y_select__8_bits[3]), .byte_to_be_written(data_input),
    .write_enable(write_enable), .clock(clock), .output_enable(read_enable), .\output (data_output));
  _1_byte_of_memory u_1_byte_of_memory_5 (
    .x_select(x_select__8_bits[4]), .y_select(y_select__8_bits[4]), .byte_to_be_written(data_input),
    .write_enable(write_enable), .clock(clock), .output_enable(read_enable), .\output (data_output));
  _1_byte_of_memory u_1_byte_of_memory_6 (
    .x_select(x_select__8_bits[5]), .y_select(y_select__8_bits[5]), .byte_to_be_written(data_input),
    .write_enable(write_enable), .clock(clock), .output_enable(read_enable), .\output (data_output));
  _1_byte_of_memory u_1_byte_of_memory_7 (
    .x_select(x_select__8_bits[6]), .y_select(y_select__8_bits[6]), .byte_to_be_written(data_input),
    .write_enable(write_enable), .clock(clock), .output_enable(read_enable), .\output (data_output));
  _1_byte_of_memory u_1_byte_of_memory_8 (
    .x_select(x_select__8_bits[7]), .y_select(y_select__8_bits[7]), .byte_to_be_written(data_input),
    .write_enable(write_enable), .clock(clock), .output_enable(read_enable), .\output (data_output));
endmodule

module _64_in_a_row (
  input  write_enable,
  input  [31:0] lower_32_bits_of_x_sel,
  input  [31:0] higher_32_bits_of_x_select,
  input  [7:0] data_input,
  input  clock,
  input  read_enable,
  input  y_sel,
  output [7:0] \output 
);

  _8_in_a_row u_8_in_a_row_1 (
    .data_input(data_input), .x_select__8_bits(lower_32_bits_of_x_sel[7:0]), .write_enable(write_enable),
    .clock(clock), .read_enable(read_enable), .y_select__8_bits({8{y_sel}}), .data_output(\output ));
  _8_in_a_row u_8_in_a_row_2 (
    .data_input(data_input), .x_select__8_bits(lower_32_bits_of_x_sel[15:8]), .write_enable(write_enable),
    .clock(clock), .read_enable(read_enable), .y_select__8_bits({8{y_sel}}), .data_output(\output ));
  _8_in_a_row u_8_in_a_row_3 (
    .data_input(data_input), .x_select__8_bits(lower_32_bits_of_x_sel[23:16]), .write_enable(write_enable),
    .clock(clock), .read_enable(read_enable), .y_select__8_bits({8{y_sel}}), .data_output(\output ));
  _8_in_a_row u_8_in_a_row_4 (
    .data_input(data_input), .x_select__8_bits(lower_32_bits_of_x_sel[31:24]), .write_enable(write_enable),
    .clock(clock), .read_enable(read_enable), .y_select__8_bits({8{y_sel}}), .data_output(\output ));
  _8_in_a_row u_8_in_a_row_5 (
    .data_input(data_input), .x_select__8_bits(higher_32_bits_of_x_select[7:0]), .write_enable(write_enable),
    .clock(clock), .read_enable(read_enable), .y_select__8_bits({8{y_sel}}), .data_output(\output ));
  _8_in_a_row u_8_in_a_row_6 (
    .data_input(data_input), .x_select__8_bits(higher_32_bits_of_x_select[15:8]),
    .write_enable(write_enable), .clock(clock), .read_enable(read_enable), .y_select__8_bits({8{y_sel}}),
    .data_output(\output ));
  _8_in_a_row u_8_in_a_row_7 (
    .data_input(data_input), .x_select__8_bits(higher_32_bits_of_x_select[23:16]),
    .write_enable(write_enable), .clock(clock), .read_enable(read_enable), .y_select__8_bits({8{y_sel}}),
    .data_output(\output ));
  _8_in_a_row u_8_in_a_row_8 (
    .data_input(data_input), .x_select__8_bits(higher_32_bits_of_x_select[31:24]),
    .write_enable(write_enable), .clock(clock), .read_enable(read_enable), .y_select__8_bits({8{y_sel}}),
    .data_output(\output ));
endmodule

module _256_in_a_row (
  input  [31:0] _8,
  input  [31:0] _7,
  input  [31:0] _6,
  input  [31:0] _5,
  input  [31:0] _4,
  input  [31:0] _2,
  input  [31:0] _3,
  input  [31:0] lowest_1,
  input  clock,
  input  [7:0] data_input,
  input  read_enable,
  input  y_select,
  input  write_enable,
  output [7:0] memory_output
);

  wire [7:0] n64_in_a_row_2_output, n64_in_a_row_4_output, n64_in_a_row_6_output, n64_in_a_row_8_output,
       undriven_7;
  wire [31:0] undriven, undriven_2, undriven_3, undriven_4, undriven_5, undriven_6, undriven_8, undriven_9;

  _64_in_a_row u_64_in_a_row_1 (
    .write_enable(write_enable), .lower_32_bits_of_x_sel(lowest_1), .higher_32_bits_of_x_select(_2),
    .data_input(data_input), .clock(clock), .read_enable(read_enable), .y_sel(y_select),
    .\output (memory_output));
  _64_in_a_row u_64_in_a_row_2 (
    .write_enable(write_enable), .lower_32_bits_of_x_sel(undriven), .higher_32_bits_of_x_select(undriven_2),
    .data_input(data_input), .clock(clock), .read_enable(read_enable), .y_sel(y_select),
    .\output (n64_in_a_row_2_output));
  _64_in_a_row u_64_in_a_row_3 (
    .write_enable(write_enable), .lower_32_bits_of_x_sel(_3), .higher_32_bits_of_x_select(_4),
    .data_input(data_input), .clock(clock), .read_enable(read_enable), .y_sel(y_select),
    .\output (memory_output));
  _64_in_a_row u_64_in_a_row_4 (
    .write_enable(write_enable), .lower_32_bits_of_x_sel(undriven_3),
    .higher_32_bits_of_x_select(undriven_4), .data_input(data_input), .clock(clock),
    .read_enable(read_enable), .y_sel(y_select), .\output (n64_in_a_row_4_output));
  _64_in_a_row u_64_in_a_row_5 (
    .write_enable(write_enable), .lower_32_bits_of_x_sel(_5), .higher_32_bits_of_x_select(_6),
    .data_input(data_input), .clock(clock), .read_enable(read_enable), .y_sel(y_select),
    .\output (memory_output));
  _64_in_a_row u_64_in_a_row_6 (
    .write_enable(write_enable), .lower_32_bits_of_x_sel(undriven_5),
    .higher_32_bits_of_x_select(undriven_6), .data_input(data_input), .clock(clock),
    .read_enable(read_enable), .y_sel(y_select), .\output (n64_in_a_row_6_output));
  _64_in_a_row u_64_in_a_row_7 (
    .write_enable(write_enable), .lower_32_bits_of_x_sel(_7), .higher_32_bits_of_x_select(_8),
    .data_input(undriven_7), .clock(clock), .read_enable(read_enable), .y_sel(y_select),
    .\output (memory_output));
  _64_in_a_row u_64_in_a_row_8 (
    .write_enable(write_enable), .lower_32_bits_of_x_sel(undriven_8),
    .higher_32_bits_of_x_select(undriven_9), .data_input(undriven_7), .clock(clock),
    .read_enable(read_enable), .y_sel(y_select), .\output (n64_in_a_row_8_output));
endmodule

module _4_rows (
  input  [9:0] address,
  input  [7:0] data_input,
  input  write_enable,
  input  read_enable,
  input  clock,
  output [7:0] memory_output
);

  wire decoder_1_out0, decoder_1_out1, decoder_1_out2, decoder_1_out3;
  wire [15:0] n8_bits_to_256_outputs_decoder_1_eleventh_set_of_16,
       n8_bits_to_256_outputs_decoder_1_fifth_set_of_16, n8_bits_to_256_outputs_decoder_1_first_set_of_16,
       n8_bits_to_256_outputs_decoder_1_ninth_set_of_16, n8_bits_to_256_outputs_decoder_1_second_set_of_16,
       n8_bits_to_256_outputs_decoder_1_sixth_set_of_16, n8_bits_to_256_outputs_decoder_1_tenth_set_of_16,
       n8_bits_to_256_outputs_decoder_1_twelvth_set_of_16;
  wire [31:0] n8_bits_to_256_outputs_decoder_1_fiftheenth_set_of_16,
       n8_bits_to_256_outputs_decoder_1_seventh_set_of_16, n8_bits_to_256_outputs_decoder_1_third_set_of_16,
       n8_bits_to_256_outputs_decoder_1_thirtheen_set_of_16;

  Decoder #(.select(2)) decoder_1 (
    .out0(decoder_1_out0), .out1(decoder_1_out1), .out2(decoder_1_out2), .out3(decoder_1_out3),
    .sel(address[9:8]), .en(1'b1));
  _8_bits_to_256_outputs_decoder u_8_bits_to_256_outputs_decoder_1 (
    .address__8_lowest_bits(address[7:0]), .chip_enable(1'b1),
    .ninth_set_of_16(n8_bits_to_256_outputs_decoder_1_ninth_set_of_16),
    .tenth_set_of_16(n8_bits_to_256_outputs_decoder_1_tenth_set_of_16),
    .eleventh_set_of_16(n8_bits_to_256_outputs_decoder_1_eleventh_set_of_16),
    .twelvth_set_of_16(n8_bits_to_256_outputs_decoder_1_twelvth_set_of_16),
    .thirtheen_set_of_16(n8_bits_to_256_outputs_decoder_1_thirtheen_set_of_16[15:0]),
    .fourtheenth_set_of_16(n8_bits_to_256_outputs_decoder_1_thirtheen_set_of_16[31:16]),
    .fiftheenth_set_of_16(n8_bits_to_256_outputs_decoder_1_fiftheenth_set_of_16[15:0]),
    .sixteen_set_of_16(n8_bits_to_256_outputs_decoder_1_fiftheenth_set_of_16[31:16]),
    .first_set_of_16(n8_bits_to_256_outputs_decoder_1_first_set_of_16),
    .third_set_of_16(n8_bits_to_256_outputs_decoder_1_third_set_of_16[15:0]),
    .fifth_set_of_16(n8_bits_to_256_outputs_decoder_1_fifth_set_of_16),
    .seventh_set_of_16(n8_bits_to_256_outputs_decoder_1_seventh_set_of_16[15:0]),
    .second_set_of_16(n8_bits_to_256_outputs_decoder_1_second_set_of_16),
    .fourth_set_of_16(n8_bits_to_256_outputs_decoder_1_third_set_of_16[31:16]),
    .sixth_set_of_16(n8_bits_to_256_outputs_decoder_1_sixth_set_of_16),
    .eighth_set_of_16(n8_bits_to_256_outputs_decoder_1_seventh_set_of_16[31:16]));
  _256_in_a_row u_256_in_a_row_1 (
    ._8(n8_bits_to_256_outputs_decoder_1_fiftheenth_set_of_16),
    ._7(n8_bits_to_256_outputs_decoder_1_thirtheen_set_of_16),
    ._6({n8_bits_to_256_outputs_decoder_1_twelvth_set_of_16, n8_bits_to_256_outputs_decoder_1_eleventh_set_of_16}),
    ._5({n8_bits_to_256_outputs_decoder_1_tenth_set_of_16, n8_bits_to_256_outputs_decoder_1_ninth_set_of_16}),
    ._4(n8_bits_to_256_outputs_decoder_1_seventh_set_of_16),
    ._2(n8_bits_to_256_outputs_decoder_1_third_set_of_16),
    ._3({n8_bits_to_256_outputs_decoder_1_sixth_set_of_16, n8_bits_to_256_outputs_decoder_1_fifth_set_of_16}),
    .lowest_1({n8_bits_to_256_outputs_decoder_1_second_set_of_16, n8_bits_to_256_outputs_decoder_1_first_set_of_16}),
    .clock(clock), .data_input(data_input), .read_enable(read_enable), .y_select(decoder_1_out0),
    .write_enable(write_enable), .memory_output(memory_output));
  _256_in_a_row u_256_in_a_row_2 (
    ._8(n8_bits_to_256_outputs_decoder_1_fiftheenth_set_of_16),
    ._7(n8_bits_to_256_outputs_decoder_1_thirtheen_set_of_16),
    ._6({n8_bits_to_256_outputs_decoder_1_twelvth_set_of_16, n8_bits_to_256_outputs_decoder_1_eleventh_set_of_16}),
    ._5({n8_bits_to_256_outputs_decoder_1_tenth_set_of_16, n8_bits_to_256_outputs_decoder_1_ninth_set_of_16}),
    ._4(n8_bits_to_256_outputs_decoder_1_seventh_set_of_16),
    ._2(n8_bits_to_256_outputs_decoder_1_third_set_of_16),
    ._3({n8_bits_to_256_outputs_decoder_1_sixth_set_of_16, n8_bits_to_256_outputs_decoder_1_fifth_set_of_16}),
    .lowest_1({n8_bits_to_256_outputs_decoder_1_second_set_of_16, n8_bits_to_256_outputs_decoder_1_first_set_of_16}),
    .clock(clock), .data_input(data_input), .read_enable(read_enable), .y_select(decoder_1_out1),
    .write_enable(write_enable), .memory_output(memory_output));
  _256_in_a_row u_256_in_a_row_3 (
    ._8(n8_bits_to_256_outputs_decoder_1_fiftheenth_set_of_16),
    ._7(n8_bits_to_256_outputs_decoder_1_thirtheen_set_of_16),
    ._6({n8_bits_to_256_outputs_decoder_1_twelvth_set_of_16, n8_bits_to_256_outputs_decoder_1_eleventh_set_of_16}),
    ._5({n8_bits_to_256_outputs_decoder_1_tenth_set_of_16, n8_bits_to_256_outputs_decoder_1_ninth_set_of_16}),
    ._4(n8_bits_to_256_outputs_decoder_1_seventh_set_of_16),
    ._2(n8_bits_to_256_outputs_decoder_1_third_set_of_16),
    ._3({n8_bits_to_256_outputs_decoder_1_sixth_set_of_16, n8_bits_to_256_outputs_decoder_1_fifth_set_of_16}),
    .lowest_1({n8_bits_to_256_outputs_decoder_1_second_set_of_16, n8_bits_to_256_outputs_decoder_1_first_set_of_16}),
    .clock(clock), .data_input(data_input), .read_enable(read_enable), .y_select(decoder_1_out2),
    .write_enable(write_enable), .memory_output(memory_output));
  _256_in_a_row u_256_in_a_row_4 (
    ._8(n8_bits_to_256_outputs_decoder_1_fiftheenth_set_of_16),
    ._7(n8_bits_to_256_outputs_decoder_1_thirtheen_set_of_16),
    ._6({n8_bits_to_256_outputs_decoder_1_twelvth_set_of_16, n8_bits_to_256_outputs_decoder_1_eleventh_set_of_16}),
    ._5({n8_bits_to_256_outputs_decoder_1_tenth_set_of_16, n8_bits_to_256_outputs_decoder_1_ninth_set_of_16}),
    ._4(n8_bits_to_256_outputs_decoder_1_seventh_set_of_16),
    ._2(n8_bits_to_256_outputs_decoder_1_third_set_of_16),
    ._3({n8_bits_to_256_outputs_decoder_1_sixth_set_of_16, n8_bits_to_256_outputs_decoder_1_fifth_set_of_16}),
    .lowest_1({n8_bits_to_256_outputs_decoder_1_second_set_of_16, n8_bits_to_256_outputs_decoder_1_first_set_of_16}),
    .clock(clock), .data_input(data_input), .read_enable(read_enable), .y_select(decoder_1_out3),
    .write_enable(write_enable), .memory_output(memory_output));
  Pull_Resistor pull_resistor_1 (.node(memory_output));
endmodule

module _8_bits_to_256_outputs_decoder (
  input  [7:0] address__8_lowest_bits,
  input  chip_enable,
  output [15:0] ninth_set_of_16,
  output [15:0] tenth_set_of_16,
  output [15:0] eleventh_set_of_16,
  output [15:0] twelvth_set_of_16,
  output [15:0] thirtheen_set_of_16,
  output [15:0] fourtheenth_set_of_16,
  output [15:0] fiftheenth_set_of_16,
  output [15:0] sixteen_set_of_16,
  output [15:0] first_set_of_16,
  output [15:0] third_set_of_16,
  output [15:0] fifth_set_of_16,
  output [15:0] seventh_set_of_16,
  output [15:0] second_set_of_16,
  output [15:0] fourth_set_of_16,
  output [15:0] sixth_set_of_16,
  output [15:0] eighth_set_of_16
);

  wire demultiplexer_1_out0, demultiplexer_1_out1, demultiplexer_1_out2, demultiplexer_1_out3,
       demultiplexer_1_out4, demultiplexer_1_out5, demultiplexer_1_out6, demultiplexer_1_out7,
       demultiplexer_1_out8, demultiplexer_1_out9, demultiplexer_1_out10, demultiplexer_1_out11,
       demultiplexer_1_out12, demultiplexer_1_out13, demultiplexer_1_out14, demultiplexer_1_out15;
  wire [15:0] demultiplexer_2_out0;

  Demultiplexer #(.select(4)) demultiplexer_1 (
    .out0(demultiplexer_1_out0), .out1(demultiplexer_1_out1), .out2(demultiplexer_1_out2),
    .out3(demultiplexer_1_out3), .out4(demultiplexer_1_out4), .out5(demultiplexer_1_out5),
    .out6(demultiplexer_1_out6), .out7(demultiplexer_1_out7), .out8(demultiplexer_1_out8),
    .out9(demultiplexer_1_out9), .out10(demultiplexer_1_out10), .out11(demultiplexer_1_out11),
    .out12(demultiplexer_1_out12), .out13(demultiplexer_1_out13), .out14(demultiplexer_1_out14),
    .out15(demultiplexer_1_out15), .in(1'b1), .sel(address__8_lowest_bits[7:4]), .en(chip_enable));
  Demultiplexer #(.select(4)) demultiplexer_2 (
    .out0(demultiplexer_2_out0[0]), .out1(demultiplexer_2_out0[1]), .out2(demultiplexer_2_out0[2]),
    .out3(demultiplexer_2_out0[3]), .out4(demultiplexer_2_out0[4]), .out5(demultiplexer_2_out0[5]),
    .out6(demultiplexer_2_out0[6]), .out7(demultiplexer_2_out0[7]), .out8(demultiplexer_2_out0[8]),
    .out9(demultiplexer_2_out0[9]), .out10(demultiplexer_2_out0[10]), .out11(demultiplexer_2_out0[11]),
    .out12(demultiplexer_2_out0[12]), .out13(demultiplexer_2_out0[13]), .out14(demultiplexer_2_out0[14]),
    .out15(demultiplexer_2_out0[15]), .in(1'b1), .sel(address__8_lowest_bits[3:0]), .en(chip_enable));
  Pull_Resistor pull_resistor_1 (.node(first_set_of_16));
  Pull_Resistor pull_resistor_2 (.node(second_set_of_16));
  Pull_Resistor pull_resistor_3 (.node(third_set_of_16));
  Pull_Resistor pull_resistor_4 (.node(fourth_set_of_16));
  Pull_Resistor pull_resistor_5 (.node(fifth_set_of_16));
  Pull_Resistor pull_resistor_6 (.node(sixth_set_of_16));
  Pull_Resistor pull_resistor_7 (.node(seventh_set_of_16));
  Pull_Resistor pull_resistor_8 (.node(eighth_set_of_16));
  decoder_row decoder_row_1 (
    .y_select(demultiplexer_1_out0), .in_2(demultiplexer_2_out0), .decoder_output(first_set_of_16));
  decoder_row decoder_row_2 (
    .y_select(demultiplexer_1_out1), .in_2(demultiplexer_2_out0), .decoder_output(second_set_of_16));
  decoder_row decoder_row_3 (
    .y_select(demultiplexer_1_out2), .in_2(demultiplexer_2_out0), .decoder_output(third_set_of_16));
  decoder_row decoder_row_4 (
    .y_select(demultiplexer_1_out3), .in_2(demultiplexer_2_out0), .decoder_output(fourth_set_of_16));
  decoder_row decoder_row_5 (
    .y_select(demultiplexer_1_out4), .in_2(demultiplexer_2_out0), .decoder_output(fifth_set_of_16));
  decoder_row decoder_row_6 (
    .y_select(demultiplexer_1_out5), .in_2(demultiplexer_2_out0), .decoder_output(sixth_set_of_16));
  decoder_row decoder_row_7 (
    .y_select(demultiplexer_1_out6), .in_2(demultiplexer_2_out0), .decoder_output(seventh_set_of_16));
  decoder_row decoder_row_8 (
    .y_select(demultiplexer_1_out7), .in_2(demultiplexer_2_out0), .decoder_output(eighth_set_of_16));
  decoder_row decoder_row_9 (
    .y_select(demultiplexer_1_out8), .in_2(demultiplexer_2_out0), .decoder_output(ninth_set_of_16));
  Pull_Resistor pull_resistor_9 (.node(ninth_set_of_16));
  decoder_row decoder_row_10 (
    .y_select(demultiplexer_1_out9), .in_2(demultiplexer_2_out0), .decoder_output(tenth_set_of_16));
  decoder_row decoder_row_11 (
    .y_select(demultiplexer_1_out10), .in_2(demultiplexer_2_out0), .decoder_output(eleventh_set_of_16));
  decoder_row decoder_row_12 (
    .y_select(demultiplexer_1_out11), .in_2(demultiplexer_2_out0), .decoder_output(twelvth_set_of_16));
  decoder_row decoder_row_13 (
    .y_select(demultiplexer_1_out12), .in_2(demultiplexer_2_out0), .decoder_output(thirtheen_set_of_16));
  decoder_row decoder_row_14 (
    .y_select(demultiplexer_1_out13), .in_2(demultiplexer_2_out0), .decoder_output(fourtheenth_set_of_16));
  decoder_row decoder_row_15 (
    .y_select(demultiplexer_1_out14), .in_2(demultiplexer_2_out0), .decoder_output(fiftheenth_set_of_16));
  decoder_row decoder_row_16 (
    .y_select(demultiplexer_1_out15), .in_2(demultiplexer_2_out0), .decoder_output(sixteen_set_of_16));
  Pull_Resistor pull_resistor_10 (.node(tenth_set_of_16));
  Pull_Resistor pull_resistor_11 (.node(eleventh_set_of_16));
  Pull_Resistor pull_resistor_12 (.node(twelvth_set_of_16));
  Pull_Resistor pull_resistor_13 (.node(thirtheen_set_of_16));
  Pull_Resistor pull_resistor_14 (.node(fourtheenth_set_of_16));
  Pull_Resistor pull_resistor_15 (.node(fiftheenth_set_of_16));
  Pull_Resistor pull_resistor_16 (.node(sixteen_set_of_16));
endmodule

module decoder_row (
  input  y_select,
  input  [15:0] in_2,
  output [15:0] decoder_output
);

  wire [15:0] and_1_out;

  and and_1 (and_1_out[0], y_select, in_2[0]);
  and and_2 (and_1_out[8], y_select, in_2[8]);
  and and_3 (and_1_out[1], y_select, in_2[1]);
  and and_4 (and_1_out[9], y_select, in_2[9]);
  and and_5 (and_1_out[2], y_select, in_2[2]);
  and and_6 (and_1_out[10], y_select, in_2[10]);
  and and_7 (and_1_out[3], y_select, in_2[3]);
  and and_8 (and_1_out[11], y_select, in_2[11]);
  and and_9 (and_1_out[4], y_select, in_2[4]);
  and and_10 (and_1_out[12], y_select, in_2[12]);
  and and_11 (and_1_out[5], y_select, in_2[5]);
  and and_12 (and_1_out[13], y_select, in_2[13]);
  and and_13 (and_1_out[6], y_select, in_2[6]);
  and and_14 (and_1_out[14], y_select, in_2[14]);
  and and_15 (and_1_out[7], y_select, in_2[7]);
  and and_16 (and_1_out[15], y_select, in_2[15]);
  assign decoder_output = y_select ? and_1_out : 16'bz;  // Controlled_Buffer controlled_buffer_1
endmodule

module microinstruction_counter (
  input  write_enable,
  input  clock,
  input  output_enable,
  input  reset_to_zero,
  output [6:0] current_microstep
);

  wire controlled_buffer_1_out, demultiplexer_1_out7, n8_bit_adder_1_overflow, not_1_out;
  wire [7:0] controlled_buffer_2_out, n8_bit_adder_1_output, pull_resistor_1_node, register_1_q;

  Pull_Resistor #(.pull(1)) pull_resistor_1 (.node(pull_resistor_1_node[0]));
  Pull_Resistor pull_resistor_2 (.node(pull_resistor_1_node[7]));
  _8_bit_adder u_8_bit_adder_1 (
    .input_a({{7{pull_resistor_1_node[7]}}, pull_resistor_1_node[0]}), .input_b(register_1_q),
    .subtract(pull_resistor_1_node[7]), .carry_in(pull_resistor_1_node[7]),
    .overflow(n8_bit_adder_1_overflow), .\output (n8_bit_adder_1_output));
  Register register_1 (
    .D(n8_bit_adder_1_output), .en(write_enable), .Q(register_1_q), .clk(clock), .clr(controlled_buffer_1_out));
  assign controlled_buffer_1_out = reset_to_zero ? 1'b1 : 1'bz;  // Controlled_Buffer controlled_buffer_1
  assign controlled_buffer_2_out = output_enable ? register_1_q : 8'bz;  // Controlled_Buffer controlled_buffer_2
  not not_1 (not_1_out, reset_to_zero);
  Demultiplexer #(.select(4)) demultiplexer_1 (
    .out0(current_microstep[0]), .out1(current_microstep[1]), .out2(current_microstep[2]),
    .out3(current_microstep[3]), .out4(current_microstep[4]), .out5(current_microstep[5]),
    .out6(current_microstep[6]), .out7(demultiplexer_1_out7), .in(1'b1), .sel(controlled_buffer_2_out[3:0]),
    .en(1'b1));  // open: out8, out9, out10, out11, out12, out13, out14, out15
  assign controlled_buffer_1_out = not_1_out ? demultiplexer_1_out7 : 1'bz;  // Controlled_Buffer controlled_buffer_3
  // also tied to GND on the sheet: n8_bit_adder_1_overflow
endmodule

module instruction_decoder (
  input  [6:0] current_microinstruction,
  input  is_microstep_zero,
  input  [7:0] current_instruction__lowest_8_bits,
  input  clock,
  input  [2:0] flags,
  output [31:0] microinstructions,
  output [31:0] microinstructions__upper
);

  wire decoder_1_out0, decoder_1_out1, decoder_1_out2, decoder_1_out3, decoder_1_out4, decoder_1_out5,
       decoder_1_out6, decoder_1_out7, decoder_1_out8, decoder_1_out9, decoder_1_out10, decoder_1_out11,
       decoder_1_out12, decoder_1_out13, decoder_1_out14, decoder_1_out15, decoder_1_out16, decoder_1_out17,
       decoder_1_out18, decoder_1_out19, decoder_1_out20;
  wire [4:0] register_1_q;
  wire [7:0] controlled_buffer_1_out;
  wire [7:5] register_1_q_2;

  Decoder #(.select(5)) decoder_1 (
    .out0(decoder_1_out0), .out1(decoder_1_out1), .out2(decoder_1_out2), .out3(decoder_1_out3),
    .out4(decoder_1_out4), .out5(decoder_1_out5), .out6(decoder_1_out6), .out7(decoder_1_out7),
    .out8(decoder_1_out8), .out9(decoder_1_out9), .out10(decoder_1_out10), .out11(decoder_1_out11),
    .out12(decoder_1_out12), .out13(decoder_1_out13), .out14(decoder_1_out14), .out15(decoder_1_out15),
    .out16(decoder_1_out16), .out17(decoder_1_out17), .out18(decoder_1_out18), .out19(decoder_1_out19),
    .out20(decoder_1_out20), .sel(register_1_q), .en(1'b1));  // open: out21, out22, out23, out24, out25, out26, out27, out28, out29, out30, out31
  microinstruction_decoder__nop microinstruction_decoder_nop_1 (
    .current_microinstruction(current_microinstruction), .chip_select(decoder_1_out0),
    .microinstruction_to_be_executed(microinstructions));
  control_signal_decoder_for_mov_from_address_to_reg_a control_signal_decoder_for_mov_from_address_to_reg_a_1 (
    .current_microinstruction(current_microinstruction), .chip_select(decoder_1_out1),
    .microinstruction_to_be_executed(microinstructions));
  microcode_decoder_for_jump_address microcode_decoder_for_jump_address_1 (
    .current_microinstruction(current_microinstruction), .chip_select(decoder_1_out2),
    .microinstruction_to_be_executed(microinstructions));
  control_signal_decoder_for_jump_if_zero control_signal_decoder_for_jump_if_zero_1 (
    .current_microinstruction(current_microinstruction), .chip_select(decoder_1_out3), .is_zero(flags[0]),
    .microinstruction_to_be_executed(microinstructions));
  microinstruction_decoder_for_sub_value_from_a_register microinstruction_decoder_for_sub_value_from_a_register_1 (
    .current_microinstruction(current_microinstruction), .chip_select(decoder_1_out4),
    .microinstruction_to_be_executed(microinstructions));
  microinstruction_decoder_for_add_value_to_a_register microinstruction_decoder_for_add_value_to_a_register_1 (
    .current_microinstruction(current_microinstruction), .chip_select(decoder_1_out5),
    .microinstruction_to_be_executed(microinstructions));
  microinstruction_decoder_for_test_value_with_a_register microinstruction_decoder_for_test_value_with_a_register_1 (
    .current_microinstruction(current_microinstruction), .chip_select(decoder_1_out6),
    .microinstruction_to_be_executed(microinstructions));
  microinstruction_decoder_for_jump_if_less_than_or_equal_to microinstruction_decoder_for_jump_if_less_than_or_equal_to_1 (
    .current_microinstruction(current_microinstruction), .chip_select(decoder_1_out7), .overflow(flags[1]),
    .microinstruction_to_be_executed(microinstructions));
  microinstruction_decoder_for_write_a_register_to_memory_location microinstruction_decoder_for_write_a_register_to_memory_location_1 (
    .current_microinstruction(current_microinstruction), .chip_select(decoder_1_out8),
    .microinstruction_to_be_executed(microinstructions));
  assign controlled_buffer_1_out = is_microstep_zero ? current_instruction__lowest_8_bits : 8'bz;  // Controlled_Buffer controlled_buffer_1
  microinstruction_decoder_for_jump_if_less_than microinstruction_decoder_for_jump_if_less_than_1 (
    .current_microinstruction(current_microinstruction), .chip_select(decoder_1_out9), .less_than(flags[2]),
    .microinstruction_to_be_executed(microinstructions));
  instruction_decoder_for_mov_address_to_b_register instruction_decoder_for_mov_address_to_b_register_1 (
    .current_microinstruction(current_microinstruction), .chip_select(decoder_1_out10),
    .microinstruction_to_be_executed(microinstructions));
  microinstruction_decoder_for_sub_value_from_reg_b microinstruction_decoder_for_sub_value_from_reg_b_1 (
    .current_microinstruction(current_microinstruction), .chip_select(decoder_1_out11),
    .microinstruction_to_be_executed(microinstructions));
  microinstruction_decoder_for_add_value_to_b_register microinstruction_decoder_for_add_value_to_b_register_1 (
    .current_microinstruction(current_microinstruction), .chip_select(decoder_1_out12),
    .microinstruction_to_be_executed(microinstructions));
  microinstruction_decoder_for_test_value_with_b_register microinstruction_decoder_for_test_value_with_b_register_1 (
    .current_microinstruction(current_microinstruction), .chip_select(decoder_1_out13),
    .microinstruction_to_be_executed(microinstructions));
  microinstruction_decoder_for_write_b_register_to_memory microinstruction_decoder_for_write_b_register_to_memory_1 (
    .current_microinstruction(current_microinstruction), .chip_select(decoder_1_out14),
    .microinstruction_to_be_executed(microinstructions));
  microinstruction_decoder_for_add_register_b_to_register_a_and_store_in_a microinstruction_decoder_for_add_register_b_to_register_a_and_store_in_a_1 (
    .current_microinstruction(current_microinstruction), .chip_select(decoder_1_out15),
    .microinstruction_to_be_executed(microinstructions));
  Register register_1 (
    .D(controlled_buffer_1_out), .en(1'b1), .Q({register_1_q_2, register_1_q}), .clk(clock));  // open: clr
  control_signal_decoder_for_pop_rip__ret control_signal_decoder_for_pop_rip_ret_1 (
    .current_microinstruction(current_microinstruction), .chip_select(decoder_1_out16),
    .microinstruction_to_be_executed(microinstructions),
    .microinstruction_to_be_executed__upper(microinstructions__upper));
  control_signal_decoder_for_call control_signal_decoder_for_call_1 (
    .current_microinstruction(current_microinstruction), .chip_select(decoder_1_out17),
    .microinstruction_to_be_executed(microinstructions),
    .microinstruction_to_be_executed__upper(microinstructions__upper));
  microinstruction_decoder_for_push_rbp microinstruction_decoder_for_push_rbp_1 (
    .current_microinstruction(current_microinstruction), .chip_select(decoder_1_out18),
    .microinstruction_to_be_executed(microinstructions),
    .microinstruction_to_be_executed__upper(microinstructions__upper));
  microinstruction_decoder_for_mov_rsp__rbp microinstruction_decoder_for_mov_rsp_rbp_1 (
    .current_microinstruction(current_microinstruction), .chip_select(decoder_1_out19),
    .microinstruction_to_be_executed(microinstructions),
    .microinstruction_to_be_executed__upper(microinstructions__upper));
  microinstruction_decoder_for_pop_rbp microinstruction_decoder_for_pop_rbp_1 (
    .current_microinstruction(current_microinstruction), .chip_select(decoder_1_out20),
    .microinstruction_to_be_executed(microinstructions),
    .microinstruction_to_be_executed__upper(microinstructions__upper));
endmodule

module control_signal_decoder_for_one_instruction__template (
  input  [6:0] current_microinstruction,
  input  chip_select,
  output [31:0] microinstruction_to_be_executed
);

  wire [6:0] pull_resistor_1_node;
  wire [31:0] microinstruction_list_template_1_fifth_microinstructions,
       microinstruction_list_template_1_fourth_microinstructions,
       microinstruction_list_template_1_second_microinstructions,
       microinstruction_list_template_1_seventh_microinstructions,
       microinstruction_list_template_1_sixth_microinstructions,
       microinstruction_list_template_1_third_microinstructions, pull_resistor_2_node;

  Pull_Resistor pull_resistor_1 (.node(pull_resistor_1_node));
  assign pull_resistor_1_node = chip_select ? current_microinstruction : 7'bz;  // Controlled_Buffer controlled_buffer_1
  Pull_Resistor pull_resistor_2 (.node(pull_resistor_2_node));
  microinstruction_list__template microinstruction_list_template_1 (
    .first_microinstructions(pull_resistor_2_node),
    .third_microinstructions(microinstruction_list_template_1_third_microinstructions),
    .fifth_microinstructions(microinstruction_list_template_1_fifth_microinstructions),
    .seventh_microinstructions(microinstruction_list_template_1_seventh_microinstructions),
    .second_microinstructions(microinstruction_list_template_1_second_microinstructions),
    .fourth_microinstructions(microinstruction_list_template_1_fourth_microinstructions),
    .sixth_microinstructions(microinstruction_list_template_1_sixth_microinstructions));
  Pull_Resistor pull_resistor_3 (.node(microinstruction_list_template_1_sixth_microinstructions));
  Pull_Resistor pull_resistor_4 (.node(microinstruction_list_template_1_third_microinstructions));
  Pull_Resistor pull_resistor_5 (.node(microinstruction_list_template_1_fifth_microinstructions));
  Pull_Resistor pull_resistor_6 (.node(microinstruction_list_template_1_second_microinstructions));
  Pull_Resistor pull_resistor_7 (.node(microinstruction_list_template_1_seventh_microinstructions));
  Pull_Resistor pull_resistor_8 (.node(microinstruction_list_template_1_fourth_microinstructions));
  assign microinstruction_to_be_executed = pull_resistor_1_node[0] ? pull_resistor_2_node : 32'bz;  // Controlled_Buffer controlled_buffer_2
  assign microinstruction_to_be_executed = pull_resistor_1_node[1] ? microinstruction_list_template_1_second_microinstructions : 32'bz;  // Controlled_Buffer controlled_buffer_3
  assign microinstruction_to_be_executed = pull_resistor_1_node[2] ? microinstruction_list_template_1_third_microinstructions : 32'bz;  // Controlled_Buffer controlled_buffer_4
  assign microinstruction_to_be_executed = pull_resistor_1_node[3] ? microinstruction_list_template_1_fourth_microinstructions : 32'bz;  // Controlled_Buffer controlled_buffer_5
  assign microinstruction_to_be_executed = pull_resistor_1_node[4] ? microinstruction_list_template_1_fifth_microinstructions : 32'bz;  // Controlled_Buffer controlled_buffer_6
  assign microinstruction_to_be_executed = pull_resistor_1_node[5] ? microinstruction_list_template_1_sixth_microinstructions : 32'bz;  // Controlled_Buffer controlled_buffer_7
  assign microinstruction_to_be_executed = pull_resistor_1_node[6] ? microinstruction_list_template_1_seventh_microinstructions : 32'bz;  // Controlled_Buffer controlled_buffer_8
endmodule

module microinstruction_list__template (
  output [31:0] first_microinstructions,
  output [31:0] third_microinstructions,
  output [31:0] fifth_microinstructions,
  output [31:0] seventh_microinstructions,
  output [31:0] second_microinstructions,
  output [31:0] fourth_microinstructions,
  output [31:0] sixth_microinstructions
);
endmodule

module program_counter (
  input  manual_value,
  input  write_enable,
  input  clock,
  input  output_enable,
  input  [31:0] lower_manual_value,
  input  [31:0] higher_manual_value,
  output [31:0] lower_32_bits_of_output,
  output [31:0] higher_32_bits_of_output
);

  wire n64_bit_adder_with_control_signals_1_overflow, not_1_out;
  wire [31:0] controlled_buffer_1_out, controlled_buffer_3_out,
       n64_bit_adder_with_control_signals_1_lower_32_bits,
       n64_bit_adder_with_control_signals_1_upper_32_bits, pull_resistor_2_node, register_1_q, register_2_q;

  Pull_Resistor pull_resistor_1 (.node(pull_resistor_2_node[31]));
  Pull_Resistor #(.pull(1)) pull_resistor_2 (.node(pull_resistor_2_node[0]));
  _64_bit_adder_with_control_signals u_64_bit_adder_with_control_signals_1 (
    .lower_32_bit_of_input_a(register_1_q), .overflow_output_enable(pull_resistor_2_node[31]),
    .higher_32_bit_of_input_a(register_2_q),
    .lower_32_bit_of_input_b({{31{pull_resistor_2_node[31]}}, pull_resistor_2_node[0]}),
    .higher_32_bit_of_input_b({32{pull_resistor_2_node[31]}}), .subtract(pull_resistor_2_node[31]),
    .output_enable_the_64_bits(pull_resistor_2_node[0]),
    .overflow(n64_bit_adder_with_control_signals_1_overflow),
    .lower_32_bits(n64_bit_adder_with_control_signals_1_lower_32_bits),
    .upper_32_bits(n64_bit_adder_with_control_signals_1_upper_32_bits));
  assign controlled_buffer_1_out = not_1_out ? n64_bit_adder_with_control_signals_1_upper_32_bits : 32'bz;  // Controlled_Buffer controlled_buffer_1
  assign controlled_buffer_1_out = manual_value ? higher_manual_value : 32'bz;  // Controlled_Buffer controlled_buffer_2
  not not_1 (not_1_out, manual_value);
  assign controlled_buffer_3_out = not_1_out ? n64_bit_adder_with_control_signals_1_lower_32_bits : 32'bz;  // Controlled_Buffer controlled_buffer_3
  Register #(.width(32)) register_1 (
    .D(controlled_buffer_3_out), .en(write_enable), .Q(register_1_q), .clk(clock));  // open: clr
  assign controlled_buffer_3_out = manual_value ? lower_manual_value : 32'bz;  // Controlled_Buffer controlled_buffer_4
  Register #(.width(32)) register_2 (
    .D(controlled_buffer_1_out), .en(write_enable), .Q(register_2_q), .clk(clock));  // open: clr
  assign lower_32_bits_of_output = output_enable ? register_1_q : 32'bz;  // Controlled_Buffer controlled_buffer_5
  assign higher_32_bits_of_output = output_enable ? register_2_q : 32'bz;  // Controlled_Buffer controlled_buffer_6
  // also tied to GND on the sheet: n64_bit_adder_with_control_signals_1_overflow
endmodule

module ALU (
  input  [31:0] lower_32_bits,
  input  [31:0] higher_32_bits,
  input  store_a,
  input  subtract,
  input  store_b,
  input  clock,
  input  output_enable,
  input  increment,
  output less_than,
  output result_is_zero,
  output overflow,
  output [31:0] lower_32_bits_of_output,
  output [31:0] higher_32_bits_of_output
);

  wire and_2_out, nor_1_out, nor_2_out, not_1_out, not_2_out, not_3_out, pull_resistor_1_node;
  wire [31:0] controlled_buffer_1_out, controlled_buffer_2_out, controlled_buffer_9_out,
       n64_bit_adder_with_control_signals_1_lower_32_bits,
       n64_bit_adder_with_control_signals_1_upper_32_bits, n64_bit_register_1_higher_32_bits_of_output,
       n64_bit_register_1_lower_32_bits_of_output, n64_bit_register_2_higher_32_bits_of_output,
       n64_bit_register_2_lower_32_bits_of_output, pull_resistor_3_node;

  not not_1 (not_1_out, increment);
  _64_bit_register u_64_bit_register_1 (
    .lower_32_bits_of_input(lower_32_bits), .higher_32_bits_of_input(higher_32_bits), .write_enable(store_b),
    .clock(clock), .output_enable(1'b1),
    .higher_32_bits_of_output(n64_bit_register_1_higher_32_bits_of_output),
    .lower_32_bits_of_output(n64_bit_register_1_lower_32_bits_of_output));
  Pull_Resistor #(.pull(1)) pull_resistor_1 (.node(pull_resistor_1_node));
  assign controlled_buffer_1_out = not_1_out ? n64_bit_register_1_lower_32_bits_of_output : 32'bz;  // Controlled_Buffer controlled_buffer_1
  assign controlled_buffer_2_out = not_1_out ? n64_bit_register_1_higher_32_bits_of_output : 32'bz;  // Controlled_Buffer controlled_buffer_2
  _64_bit_register u_64_bit_register_2 (
    .lower_32_bits_of_input(lower_32_bits), .higher_32_bits_of_input(higher_32_bits), .write_enable(store_a),
    .clock(clock), .output_enable(1'b1),
    .higher_32_bits_of_output(n64_bit_register_2_higher_32_bits_of_output),
    .lower_32_bits_of_output(n64_bit_register_2_lower_32_bits_of_output));
  _64_bit_adder_with_control_signals u_64_bit_adder_with_control_signals_1 (
    .lower_32_bit_of_input_a(n64_bit_register_2_lower_32_bits_of_output),
    .overflow_output_enable(pull_resistor_1_node),
    .higher_32_bit_of_input_a(n64_bit_register_2_higher_32_bits_of_output),
    .lower_32_bit_of_input_b(controlled_buffer_1_out), .higher_32_bit_of_input_b(controlled_buffer_2_out),
    .subtract(subtract), .output_enable_the_64_bits(output_enable), .overflow(overflow),
    .lower_32_bits(n64_bit_adder_with_control_signals_1_lower_32_bits),
    .upper_32_bits(n64_bit_adder_with_control_signals_1_upper_32_bits));
  assign controlled_buffer_1_out = increment ? 32'h1 : 32'bz;  // Controlled_Buffer controlled_buffer_3
  assign controlled_buffer_2_out = increment ? {32{1'b0}} : 32'bz;  // Controlled_Buffer controlled_buffer_4
  and and_1 (less_than, not_2_out, not_3_out);
  not not_2 (not_2_out, overflow);
  not not_3 (not_3_out, result_is_zero);
  assign lower_32_bits_of_output = output_enable ? n64_bit_adder_with_control_signals_1_lower_32_bits : 32'bz;  // Controlled_Buffer controlled_buffer_5
  assign higher_32_bits_of_output = output_enable ? n64_bit_adder_with_control_signals_1_upper_32_bits : 32'bz;  // Controlled_Buffer controlled_buffer_6
  Pull_Resistor pull_resistor_2 (.node(result_is_zero));
  assign result_is_zero = 1'b1 ? and_2_out : 1'bz;  // Controlled_Buffer controlled_buffer_7
  Pull_Resistor pull_resistor_3 (.node(pull_resistor_3_node));
  assign pull_resistor_3_node = 1'b1 ? lower_32_bits_of_output : 32'bz;  // Controlled_Buffer controlled_buffer_8
  assign controlled_buffer_9_out = 1'b1 ? higher_32_bits_of_output : 32'bz;  // Controlled_Buffer controlled_buffer_9
  Pull_Resistor pull_resistor_4 (.node(controlled_buffer_9_out));
  nor nor_1 (nor_1_out, pull_resistor_3_node[0], pull_resistor_3_node[1], pull_resistor_3_node[2], pull_resistor_3_node[3], pull_resistor_3_node[4], pull_resistor_3_node[5], pull_resistor_3_node[6], pull_resistor_3_node[7], pull_resistor_3_node[8], pull_resistor_3_node[9], pull_resistor_3_node[10], pull_resistor_3_node[11], pull_resistor_3_node[12], pull_resistor_3_node[13], pull_resistor_3_node[14], pull_resistor_3_node[15], pull_resistor_3_node[17], pull_resistor_3_node[18], pull_resistor_3_node[19], pull_resistor_3_node[20], pull_resistor_3_node[21], pull_resistor_3_node[22], pull_resistor_3_node[23], pull_resistor_3_node[24], pull_resistor_3_node[25], pull_resistor_3_node[26], pull_resistor_3_node[27], pull_resistor_3_node[28], pull_resistor_3_node[29], pull_resistor_3_node[30], pull_resistor_3_node[31], pull_resistor_3_node[16]);
  nor nor_2 (nor_2_out, controlled_buffer_9_out[0], controlled_buffer_9_out[1], controlled_buffer_9_out[2], controlled_buffer_9_out[3], controlled_buffer_9_out[4], controlled_buffer_9_out[5], controlled_buffer_9_out[6], controlled_buffer_9_out[7], controlled_buffer_9_out[8], controlled_buffer_9_out[9], controlled_buffer_9_out[10], controlled_buffer_9_out[11], controlled_buffer_9_out[12], controlled_buffer_9_out[13], controlled_buffer_9_out[14], controlled_buffer_9_out[15], controlled_buffer_9_out[17], controlled_buffer_9_out[18], controlled_buffer_9_out[19], controlled_buffer_9_out[20], controlled_buffer_9_out[21], controlled_buffer_9_out[22], controlled_buffer_9_out[23], controlled_buffer_9_out[24], controlled_buffer_9_out[25], controlled_buffer_9_out[26], controlled_buffer_9_out[27], controlled_buffer_9_out[28], controlled_buffer_9_out[29], controlled_buffer_9_out[30], controlled_buffer_9_out[31], controlled_buffer_9_out[16]);
  and and_2 (and_2_out, nor_1_out, nor_2_out);
endmodule

module Complete_computer (
  input  [31:0] in_1,
  input  [31:0] in_2,
  input  [31:0] in_3,
  input  manual_control_signals,
  input  advance_microcode_counter,
  input  [31:0] in_6,
  input  [31:0] in_7,
  input  start_exec,
  output [31:0] lower_part_of_instruction_pointer,
  output [31:0] higher_part_of_instruction_pointer,
  output [31:0] out_11,
  output [31:0] out_12,
  output [6:0] out_13,
  output [31:0] out_14,
  output [7:0] out_15
);

  wire and_1_out, and_2_out, and_3_out, and_4_out, clock_1_out, controlled_buffer_4_out,
       controlled_buffer_15_out, main_1_memory_read_enable, main_1_memory_write_enable, nor_1_out, not_1_out,
       not_2_out, not_3_out, or_1_out, pull_resistor_2_node, pull_resistor_3_node, undriven, undriven_2;
  wire [6:0] bin_to_7_segment_decimal_decoder_1_output;
  wire [9:0] controlled_buffer_8_out, ones_tens_hundreds_to_binary_converter_1_hundreds_2,
       ones_tens_hundreds_to_binary_converter_1_ones_2, ones_tens_hundreds_to_binary_converter_1_tens_2;
  wire [9:4] pull_resistor_1_node;
  wire [11:0] main_1_address_bus_low__output_2;
  wire [31:0] controlled_buffer_7_out, controlled_buffer_17_out, main_1_data_bus_high__output,
       main_1_data_bus_low__output, n64_bit_adder_add_and_subtract_1_lower_32_bits_from_output, ram_2_data;
  wire [31:12] main_1_address_bus_low__output;
  wire [31:31] pull_resistor_6_node;

  Pull_Resistor #(.pull(1)) pull_resistor_1 (.node(pull_resistor_1_node[4]));
  or or_1 (or_1_out, n64_bit_adder_add_and_subtract_1_lower_32_bits_from_output[0], n64_bit_adder_add_and_subtract_1_lower_32_bits_from_output[1], n64_bit_adder_add_and_subtract_1_lower_32_bits_from_output[2], n64_bit_adder_add_and_subtract_1_lower_32_bits_from_output[3], n64_bit_adder_add_and_subtract_1_lower_32_bits_from_output[4], n64_bit_adder_add_and_subtract_1_lower_32_bits_from_output[5], n64_bit_adder_add_and_subtract_1_lower_32_bits_from_output[6], n64_bit_adder_add_and_subtract_1_lower_32_bits_from_output[7], n64_bit_adder_add_and_subtract_1_lower_32_bits_from_output[8], n64_bit_adder_add_and_subtract_1_lower_32_bits_from_output[9], n64_bit_adder_add_and_subtract_1_lower_32_bits_from_output[10], n64_bit_adder_add_and_subtract_1_lower_32_bits_from_output[11], n64_bit_adder_add_and_subtract_1_lower_32_bits_from_output[12], n64_bit_adder_add_and_subtract_1_lower_32_bits_from_output[13], n64_bit_adder_add_and_subtract_1_lower_32_bits_from_output[14], n64_bit_adder_add_and_subtract_1_lower_32_bits_from_output[15], n64_bit_adder_add_and_subtract_1_lower_32_bits_from_output[16], n64_bit_adder_add_and_subtract_1_lower_32_bits_from_output[17], n64_bit_adder_add_and_subtract_1_lower_32_bits_from_output[18], n64_bit_adder_add_and_subtract_1_lower_32_bits_from_output[19], n64_bit_adder_add_and_subtract_1_lower_32_bits_from_output[20], n64_bit_adder_add_and_subtract_1_lower_32_bits_from_output[21], n64_bit_adder_add_and_subtract_1_lower_32_bits_from_output[22], n64_bit_adder_add_and_subtract_1_lower_32_bits_from_output[23], n64_bit_adder_add_and_subtract_1_lower_32_bits_from_output[24], n64_bit_adder_add_and_subtract_1_lower_32_bits_from_output[25], n64_bit_adder_add_and_subtract_1_lower_32_bits_from_output[26], n64_bit_adder_add_and_subtract_1_lower_32_bits_from_output[27], n64_bit_adder_add_and_subtract_1_lower_32_bits_from_output[28], n64_bit_adder_add_and_subtract_1_lower_32_bits_from_output[29], n64_bit_adder_add_and_subtract_1_lower_32_bits_from_output[30], n64_bit_adder_add_and_subtract_1_lower_32_bits_from_output[31]);
  Pull_Resistor pull_resistor_2 (.node(pull_resistor_2_node));
  assign out_12 = manual_control_signals ? in_3 : 32'bz;  // Controlled_Buffer controlled_buffer_1
  Pull_Resistor pull_resistor_3 (.node(pull_resistor_3_node));
  assign pull_resistor_3_node = pull_resistor_2_node ? advance_microcode_counter : 1'bz;  // Controlled_Buffer controlled_buffer_2
  main main_1 (
    .clock(clock_1_out), .advance_microinstruction(pull_resistor_3_node),
    .manual_control_signals(manual_control_signals), .in_8(in_7), .upper_control_signals(in_6),
    .address_bus_low(in_2), .data_bus_low(out_11), .data_bus_high(out_12),
    .lower_part_of_instruction_pointer(lower_part_of_instruction_pointer),
    .higher_part_of_instruction_pointer(higher_part_of_instruction_pointer),
    .lower_8_bits_of_instruction(out_15), .current_microinstruction(out_13),
    .data_bus_high__output(main_1_data_bus_high__output),
    .address_bus_low__output({main_1_address_bus_low__output, main_1_address_bus_low__output_2}),
    .data_bus_low__output(main_1_data_bus_low__output), .current_microinstructions(out_14),
    .memory_read_enable(main_1_memory_read_enable), .memory_write_enable(main_1_memory_write_enable));  // open: address_bus_high, address_bus_high__output
  _64_bit_adder__add_and_subtract u_64_bit_adder_add_and_subtract_1 (
    .lower_32_bits_of_a(32'h3a), .upper_32_bits_of_a({32{1'b0}}),
    .lower_32_bits_of_b({{20{1'b0}}, main_1_address_bus_low__output_2}), .upper_32_bits_of_b({32{1'b0}}),
    .subtract(1'b1), .lower_32_bits_from_output(n64_bit_adder_add_and_subtract_1_lower_32_bits_from_output));  // open: overflow, upper_32_bits_from_output
  assign out_11 = manual_control_signals ? in_1 : 32'bz;  // Controlled_Buffer controlled_buffer_3
  Register #(.width(1)) register_1 (
    .D(controlled_buffer_4_out), .en(out_13[0]), .Q(pull_resistor_2_node), .clk(clock_1_out));  // open: clr
  assign controlled_buffer_4_out = pull_resistor_2_node ? or_1_out : 1'bz;  // Controlled_Buffer controlled_buffer_4
  assign out_11 = and_1_out ? controlled_buffer_7_out : 32'bz;  // Controlled_Buffer controlled_buffer_5
  Pull_Resistor pull_resistor_4 (.node(pull_resistor_1_node[9]));
  assign controlled_buffer_4_out = start_exec ? 1'b1 : 1'bz;  // Controlled_Buffer controlled_buffer_6
  assign controlled_buffer_7_out = main_1_memory_write_enable ? main_1_data_bus_low__output : 32'bz;  // Controlled_Buffer controlled_buffer_7
  and and_1 (and_1_out, main_1_memory_read_enable, not_1_out);
  ones_tens_hundreds_to_binary_converter ones_tens_hundreds_to_binary_converter_1 (
    .ones({{8{pull_resistor_1_node[9]}}, pull_resistor_1_node[4], pull_resistor_1_node[9]}),
    .tens({{8{pull_resistor_1_node[9]}}, pull_resistor_1_node[4], pull_resistor_1_node[9]}),
    .hundreds({{5{pull_resistor_1_node[9]}}, pull_resistor_1_node[4], {4{pull_resistor_1_node[9]}}}),
    .ones_2(ones_tens_hundreds_to_binary_converter_1_ones_2),
    .tens_2(ones_tens_hundreds_to_binary_converter_1_tens_2),
    .hundreds_2(ones_tens_hundreds_to_binary_converter_1_hundreds_2));
  and and_2 (and_2_out, main_1_address_bus_low__output[28], main_1_address_bus_low__output[29], main_1_address_bus_low__output[30], main_1_address_bus_low__output[31]);
  assign controlled_buffer_8_out = main_1_address_bus_low__output[24] ? ones_tens_hundreds_to_binary_converter_1_ones_2 : 10'bz;  // Controlled_Buffer controlled_buffer_8
  assign controlled_buffer_8_out = main_1_address_bus_low__output[23] ? ones_tens_hundreds_to_binary_converter_1_tens_2 : 10'bz;  // Controlled_Buffer controlled_buffer_9
  assign controlled_buffer_8_out = main_1_address_bus_low__output[22] ? ones_tens_hundreds_to_binary_converter_1_hundreds_2 : 10'bz;  // Controlled_Buffer controlled_buffer_10
  nor nor_1 (nor_1_out, bin_to_7_segment_decimal_decoder_1_output[0], bin_to_7_segment_decimal_decoder_1_output[1], bin_to_7_segment_decimal_decoder_1_output[2], bin_to_7_segment_decimal_decoder_1_output[3], bin_to_7_segment_decimal_decoder_1_output[4], bin_to_7_segment_decimal_decoder_1_output[5], bin_to_7_segment_decimal_decoder_1_output[6]);
  bin_to_7_segment_decimal_decoder bin_to_7_segment_decimal_decoder_1 (
    .number(controlled_buffer_7_out[3:0]), .chip_enable(and_2_out),
    .\output (bin_to_7_segment_decimal_decoder_1_output));
  assign out_11 = and_3_out ? {{22{pull_resistor_6_node[31]}}, controlled_buffer_8_out} : 32'bz;  // Controlled_Buffer controlled_buffer_11
  Clock clock_1 (.out(clock_1_out));
  assign main_1_memory_read_enable = manual_control_signals ? undriven : 1'bz;  // Controlled_Buffer controlled_buffer_12
  assign main_1_memory_write_enable = manual_control_signals ? undriven_2 : 1'bz;  // Controlled_Buffer controlled_buffer_13
  RAM #(.addrWidth(12), .dataWidth(32)) ram_1 (
    .addr(main_1_address_bus_low__output_2), .data(controlled_buffer_7_out), .sel(controlled_buffer_15_out),
    .clk(clock_1_out), .ld(main_1_memory_read_enable));  // open: clr
  assign out_12 = and_1_out ? controlled_buffer_17_out : 32'bz;  // Controlled_Buffer controlled_buffer_14
  not not_1 (not_1_out, and_3_out);
  Pull_Resistor pull_resistor_5 (.node(controlled_buffer_8_out));
  Pull_Resistor pull_resistor_6 (.node(pull_resistor_6_node[31]));
  _7_Segment_Display u_7_segment_display_1 (
    .g(bin_to_7_segment_decimal_decoder_1_output[0]), .f(bin_to_7_segment_decimal_decoder_1_output[1]),
    .a(bin_to_7_segment_decimal_decoder_1_output[2]), .b(bin_to_7_segment_decimal_decoder_1_output[3]),
    .e(bin_to_7_segment_decimal_decoder_1_output[4]), .d(bin_to_7_segment_decimal_decoder_1_output[5]),
    .c(bin_to_7_segment_decimal_decoder_1_output[6]));  // open: dp
  assign controlled_buffer_15_out = not_3_out ? main_1_memory_write_enable : 1'bz;  // Controlled_Buffer controlled_buffer_15
  not not_2 (not_2_out, main_1_memory_read_enable);
  and and_3 (and_3_out, main_1_address_bus_low__output[25], main_1_address_bus_low__output[26], main_1_address_bus_low__output[27]);
  RAM #(.addrWidth(12), .dataWidth(32)) ram_2 (
    .addr(main_1_address_bus_low__output_2), .data(ram_2_data), .sel(controlled_buffer_15_out),
    .clk(clock_1_out), .ld(main_1_memory_read_enable));  // open: clr
  assign controlled_buffer_15_out = main_1_memory_read_enable ? main_1_memory_read_enable : 1'bz;  // Controlled_Buffer controlled_buffer_16
  not not_3 (not_3_out, main_1_memory_read_enable);
  assign controlled_buffer_17_out = main_1_memory_read_enable ? ram_2_data : 32'bz;  // Controlled_Buffer controlled_buffer_17
  assign ram_2_data = main_1_memory_write_enable ? main_1_data_bus_high__output : 32'bz;  // Controlled_Buffer controlled_buffer_18
  and and_4 (and_4_out, not_2_out, controlled_buffer_15_out);
endmodule

module microinstruction_list__nop (
  output [31:0] first_microinstructions,
  output [31:0] third_microinstructions,
  output [31:0] fifth_microinstructions,
  output [31:0] seventh_microinstructions,
  output [31:0] second_microinstructions,
  output [31:0] fourth_microinstructions,
  output [31:0] sixth_microinstructions
);

  Pull_Resistor pull_resistor_1 (.node(fifth_microinstructions[31]));
  Pull_Resistor #(.pull(1)) pull_resistor_2 (.node(first_microinstructions[20]));

  assign fifth_microinstructions[30:0] = {31{fifth_microinstructions[31]}};
  assign {first_microinstructions[31:21], first_microinstructions[19:0]} = {{11{fifth_microinstructions[31]}}, first_microinstructions[20], {6{fifth_microinstructions[31]}}, first_microinstructions[20], {6{fifth_microinstructions[31]}}, first_microinstructions[20], {5{fifth_microinstructions[31]}}};
  assign fourth_microinstructions = {32{fifth_microinstructions[31]}};
  assign second_microinstructions = {{27{fifth_microinstructions[31]}}, first_microinstructions[20], {4{fifth_microinstructions[31]}}};
  assign seventh_microinstructions = {32{fifth_microinstructions[31]}};
  assign sixth_microinstructions = {32{fifth_microinstructions[31]}};
  assign third_microinstructions = {32{fifth_microinstructions[31]}};
endmodule

module microinstruction_decoder__nop (
  input  [6:0] current_microinstruction,
  input  chip_select,
  output [31:0] microinstruction_to_be_executed
);

  wire [6:0] pull_resistor_1_node;
  wire [31:0] microinstruction_list_nop_1_fifth_microinstructions,
       microinstruction_list_nop_1_first_microinstructions,
       microinstruction_list_nop_1_fourth_microinstructions,
       microinstruction_list_nop_1_second_microinstructions,
       microinstruction_list_nop_1_seventh_microinstructions,
       microinstruction_list_nop_1_sixth_microinstructions,
       microinstruction_list_nop_1_third_microinstructions;

  Pull_Resistor pull_resistor_1 (.node(pull_resistor_1_node));
  assign pull_resistor_1_node = chip_select ? current_microinstruction : 7'bz;  // Controlled_Buffer controlled_buffer_1
  microinstruction_list__nop microinstruction_list_nop_1 (
    .first_microinstructions(microinstruction_list_nop_1_first_microinstructions),
    .third_microinstructions(microinstruction_list_nop_1_third_microinstructions),
    .fifth_microinstructions(microinstruction_list_nop_1_fifth_microinstructions),
    .seventh_microinstructions(microinstruction_list_nop_1_seventh_microinstructions),
    .second_microinstructions(microinstruction_list_nop_1_second_microinstructions),
    .fourth_microinstructions(microinstruction_list_nop_1_fourth_microinstructions),
    .sixth_microinstructions(microinstruction_list_nop_1_sixth_microinstructions));
  Pull_Resistor pull_resistor_2 (.node(microinstruction_list_nop_1_first_microinstructions));
  Pull_Resistor pull_resistor_3 (.node(microinstruction_list_nop_1_sixth_microinstructions));
  Pull_Resistor pull_resistor_4 (.node(microinstruction_list_nop_1_third_microinstructions));
  Pull_Resistor pull_resistor_5 (.node(microinstruction_list_nop_1_fifth_microinstructions));
  Pull_Resistor pull_resistor_6 (.node(microinstruction_list_nop_1_second_microinstructions));
  Pull_Resistor pull_resistor_7 (.node(microinstruction_list_nop_1_seventh_microinstructions));
  Pull_Resistor pull_resistor_8 (.node(microinstruction_list_nop_1_fourth_microinstructions));
  assign microinstruction_to_be_executed = pull_resistor_1_node[0] ? microinstruction_list_nop_1_first_microinstructions : 32'bz;  // Controlled_Buffer controlled_buffer_2
  assign microinstruction_to_be_executed = pull_resistor_1_node[1] ? microinstruction_list_nop_1_second_microinstructions : 32'bz;  // Controlled_Buffer controlled_buffer_3
  assign microinstruction_to_be_executed = pull_resistor_1_node[2] ? microinstruction_list_nop_1_third_microinstructions : 32'bz;  // Controlled_Buffer controlled_buffer_4
  assign microinstruction_to_be_executed = pull_resistor_1_node[3] ? microinstruction_list_nop_1_fourth_microinstructions : 32'bz;  // Controlled_Buffer controlled_buffer_5
  assign microinstruction_to_be_executed = pull_resistor_1_node[4] ? microinstruction_list_nop_1_fifth_microinstructions : 32'bz;  // Controlled_Buffer controlled_buffer_6
  assign microinstruction_to_be_executed = pull_resistor_1_node[5] ? microinstruction_list_nop_1_sixth_microinstructions : 32'bz;  // Controlled_Buffer controlled_buffer_7
  assign microinstruction_to_be_executed = pull_resistor_1_node[6] ? microinstruction_list_nop_1_seventh_microinstructions : 32'bz;  // Controlled_Buffer controlled_buffer_8
endmodule

module control_signal_decoder_for_mov_from_address_to_reg_a (
  input  [6:0] current_microinstruction,
  input  chip_select,
  output [31:0] microinstruction_to_be_executed
);

  wire [6:0] pull_resistor_1_node;
  wire [31:0] microinstruction_list_mov_address_to_reg_a_1_fifth_microinstructions,
       microinstruction_list_mov_address_to_reg_a_1_first_microinstructions,
       microinstruction_list_mov_address_to_reg_a_1_fourth_microinstructions,
       microinstruction_list_mov_address_to_reg_a_1_second_microinstructions,
       microinstruction_list_mov_address_to_reg_a_1_seventh_microinstructions,
       microinstruction_list_mov_address_to_reg_a_1_sixth_microinstructions,
       microinstruction_list_mov_address_to_reg_a_1_third_microinstructions;

  Pull_Resistor pull_resistor_1 (.node(pull_resistor_1_node));
  microinstruction_list_mov_address_to_reg_a microinstruction_list_mov_address_to_reg_a_1 (
    .first_microinstructions(microinstruction_list_mov_address_to_reg_a_1_first_microinstructions),
    .third_microinstructions(microinstruction_list_mov_address_to_reg_a_1_third_microinstructions),
    .fifth_microinstructions(microinstruction_list_mov_address_to_reg_a_1_fifth_microinstructions),
    .seventh_microinstructions(microinstruction_list_mov_address_to_reg_a_1_seventh_microinstructions),
    .second_microinstructions(microinstruction_list_mov_address_to_reg_a_1_second_microinstructions),
    .fourth_microinstructions(microinstruction_list_mov_address_to_reg_a_1_fourth_microinstructions),
    .sixth_microinstructions(microinstruction_list_mov_address_to_reg_a_1_sixth_microinstructions));
  assign pull_resistor_1_node = chip_select ? current_microinstruction : 7'bz;  // Controlled_Buffer controlled_buffer_1
  Pull_Resistor pull_resistor_2 (.node(microinstruction_list_mov_address_to_reg_a_1_second_microinstructions));
  Pull_Resistor pull_resistor_3 (.node(microinstruction_list_mov_address_to_reg_a_1_third_microinstructions));
  Pull_Resistor pull_resistor_4 (.node(microinstruction_list_mov_address_to_reg_a_1_fifth_microinstructions));
  Pull_Resistor pull_resistor_5 (.node(microinstruction_list_mov_address_to_reg_a_1_first_microinstructions));
  Pull_Resistor pull_resistor_6 (.node(microinstruction_list_mov_address_to_reg_a_1_sixth_microinstructions));
  Pull_Resistor pull_resistor_7 (.node(microinstruction_list_mov_address_to_reg_a_1_seventh_microinstructions));
  Pull_Resistor pull_resistor_8 (.node(microinstruction_list_mov_address_to_reg_a_1_seventh_microinstructions));
  Pull_Resistor pull_resistor_9 (.node(microinstruction_list_mov_address_to_reg_a_1_fourth_microinstructions));
  assign microinstruction_to_be_executed = pull_resistor_1_node[0] ? microinstruction_list_mov_address_to_reg_a_1_second_microinstructions : 32'bz;  // Controlled_Buffer controlled_buffer_2
  assign microinstruction_to_be_executed = pull_resistor_1_node[1] ? microinstruction_list_mov_address_to_reg_a_1_first_microinstructions : 32'bz;  // Controlled_Buffer controlled_buffer_3
  assign microinstruction_to_be_executed = pull_resistor_1_node[2] ? microinstruction_list_mov_address_to_reg_a_1_third_microinstructions : 32'bz;  // Controlled_Buffer controlled_buffer_4
  assign microinstruction_to_be_executed = pull_resistor_1_node[3] ? microinstruction_list_mov_address_to_reg_a_1_fourth_microinstructions : 32'bz;  // Controlled_Buffer controlled_buffer_5
  assign microinstruction_to_be_executed = pull_resistor_1_node[4] ? microinstruction_list_mov_address_to_reg_a_1_fifth_microinstructions : 32'bz;  // Controlled_Buffer controlled_buffer_6
  assign microinstruction_to_be_executed = pull_resistor_1_node[5] ? microinstruction_list_mov_address_to_reg_a_1_sixth_microinstructions : 32'bz;  // Controlled_Buffer controlled_buffer_7
  assign microinstruction_to_be_executed = pull_resistor_1_node[6] ? microinstruction_list_mov_address_to_reg_a_1_seventh_microinstructions : 32'bz;  // Controlled_Buffer controlled_buffer_8
endmodule

module microinstruction_list_mov_address_to_reg_a (
  output [31:0] first_microinstructions,
  output [31:0] third_microinstructions,
  output [31:0] fifth_microinstructions,
  output [31:0] seventh_microinstructions,
  output [31:0] second_microinstructions,
  output [31:0] fourth_microinstructions,
  output [31:0] sixth_microinstructions
);

  Pull_Resistor pull_resistor_1 (.node(fifth_microinstructions[31]));
  Pull_Resistor #(.pull(1)) pull_resistor_2 (.node(first_microinstructions[4]));

  assign fifth_microinstructions[30:0] = {31{fifth_microinstructions[31]}};
  assign {first_microinstructions[31:5], first_microinstructions[3:0]} = {31{fifth_microinstructions[31]}};
  assign fourth_microinstructions = {32{fifth_microinstructions[31]}};
  assign second_microinstructions = {{11{fifth_microinstructions[31]}}, {2{first_microinstructions[4]}}, {6{fifth_microinstructions[31]}}, first_microinstructions[4], {6{fifth_microinstructions[31]}}, first_microinstructions[4], {5{fifth_microinstructions[31]}}};
  assign seventh_microinstructions = {32{fifth_microinstructions[31]}};
  assign sixth_microinstructions = {32{fifth_microinstructions[31]}};
  assign third_microinstructions = {{9{fifth_microinstructions[31]}}, first_microinstructions[4], fifth_microinstructions[31], {2{first_microinstructions[4]}}, {17{fifth_microinstructions[31]}}, first_microinstructions[4], fifth_microinstructions[31]};
endmodule

module delay_thingy (
  input  \input ,
  output \output 
);

  wire not_1_out, not_3_out, not_4_out, not_5_out, not_6_out, not_7_out, not_8_out, not_9_out, not_10_out,
       not_11_out, not_12_out, not_13_out, not_14_out, not_15_out, not_16_out, not_17_out, not_18_out,
       not_19_out, not_20_out, not_21_out, not_22_out, not_23_out, not_24_out, not_25_out, not_26_out,
       not_27_out, not_28_out, not_29_out, not_30_out, not_31_out, not_32_out, not_33_out, not_34_out,
       not_35_out, not_36_out, not_37_out, not_38_out, not_39_out, not_40_out, not_41_out, not_42_out,
       not_43_out, not_44_out, not_45_out, not_46_out, not_47_out, not_48_out, not_49_out, not_50_out,
       not_51_out, not_52_out, not_53_out, not_54_out, not_55_out, not_56_out, not_57_out, not_58_out,
       not_59_out, not_60_out, not_61_out, not_62_out, not_63_out, not_64_out;

  not not_1 (not_1_out, not_4_out);
  not not_2 (\output , not_3_out);
  not not_3 (not_3_out, not_5_out);
  not not_4 (not_4_out, not_6_out);
  not not_5 (not_5_out, not_8_out);
  not not_6 (not_6_out, not_7_out);
  not not_7 (not_7_out, not_9_out);
  not not_8 (not_8_out, not_1_out);
  not not_9 (not_9_out, not_12_out);
  not not_10 (not_10_out, not_11_out);
  not not_11 (not_11_out, not_13_out);
  not not_12 (not_12_out, not_14_out);
  not not_13 (not_13_out, not_16_out);
  not not_14 (not_14_out, not_15_out);
  not not_15 (not_15_out, not_10_out);
  not not_16 (not_16_out, not_17_out);
  not not_17 (not_17_out, not_20_out);
  not not_18 (not_18_out, not_19_out);
  not not_19 (not_19_out, not_21_out);
  not not_20 (not_20_out, not_22_out);
  not not_21 (not_21_out, not_24_out);
  not not_22 (not_22_out, not_23_out);
  not not_23 (not_23_out, not_18_out);
  not not_24 (not_24_out, not_27_out);
  not not_25 (not_25_out, not_28_out);
  not not_26 (not_26_out, not_30_out);
  not not_27 (not_27_out, not_29_out);
  not not_28 (not_28_out, not_32_out);
  not not_29 (not_29_out, not_31_out);
  not not_30 (not_30_out, not_33_out);
  not not_31 (not_31_out, not_35_out);
  not not_32 (not_32_out, not_34_out);
  not not_33 (not_33_out, not_36_out);
  not not_34 (not_34_out, not_37_out);
  not not_35 (not_35_out, not_26_out);
  not not_36 (not_36_out, not_25_out);
  not not_37 (not_37_out, not_39_out);
  not not_38 (not_38_out, not_40_out);
  not not_39 (not_39_out, not_41_out);
  not not_40 (not_40_out, not_42_out);
  not not_41 (not_41_out, not_43_out);
  not not_42 (not_42_out, not_44_out);
  not not_43 (not_43_out, not_38_out);
  not not_44 (not_44_out, not_46_out);
  not not_45 (not_45_out, not_47_out);
  not not_46 (not_46_out, not_48_out);
  not not_47 (not_47_out, not_49_out);
  not not_48 (not_48_out, not_50_out);
  not not_49 (not_49_out, not_52_out);
  not not_50 (not_50_out, not_51_out);
  not not_51 (not_51_out, not_45_out);
  not not_52 (not_52_out, not_53_out);
  not not_53 (not_53_out, not_55_out);
  not not_54 (not_54_out, not_56_out);
  not not_55 (not_55_out, not_57_out);
  not not_56 (not_56_out, not_58_out);
  not not_57 (not_57_out, not_59_out);
  not not_58 (not_58_out, not_60_out);
  not not_59 (not_59_out, not_54_out);
  not not_60 (not_60_out, not_61_out);
  not not_61 (not_61_out, not_62_out);
  not not_62 (not_62_out, not_63_out);
  not not_63 (not_63_out, not_64_out);
  not not_64 (not_64_out, \input );
endmodule

module mega_delay_thingy (
  input  \input ,
  output \output 
);

  wire delay_thingy_1_output, delay_thingy_2_output, delay_thingy_3_output, delay_thingy_4_output,
       delay_thingy_5_output, delay_thingy_6_output, delay_thingy_7_output, delay_thingy_8_output,
       delay_thingy_9_output, delay_thingy_10_output, delay_thingy_11_output, delay_thingy_12_output,
       delay_thingy_13_output, delay_thingy_15_output;

  delay_thingy delay_thingy_1 (.\input (\input ), .\output (delay_thingy_1_output));
  delay_thingy delay_thingy_2 (.\input (delay_thingy_1_output), .\output (delay_thingy_2_output));
  delay_thingy delay_thingy_3 (.\input (delay_thingy_2_output), .\output (delay_thingy_3_output));
  delay_thingy delay_thingy_4 (.\input (delay_thingy_3_output), .\output (delay_thingy_4_output));
  delay_thingy delay_thingy_5 (.\input (delay_thingy_4_output), .\output (delay_thingy_5_output));
  delay_thingy delay_thingy_6 (.\input (delay_thingy_5_output), .\output (delay_thingy_6_output));
  delay_thingy delay_thingy_7 (.\input (delay_thingy_6_output), .\output (delay_thingy_7_output));
  delay_thingy delay_thingy_8 (.\input (delay_thingy_7_output), .\output (delay_thingy_8_output));
  delay_thingy delay_thingy_9 (.\input (delay_thingy_10_output), .\output (delay_thingy_9_output));
  delay_thingy delay_thingy_10 (.\input (delay_thingy_8_output), .\output (delay_thingy_10_output));
  delay_thingy delay_thingy_11 (.\input (delay_thingy_9_output), .\output (delay_thingy_11_output));
  delay_thingy delay_thingy_12 (.\input (delay_thingy_11_output), .\output (delay_thingy_12_output));
  delay_thingy delay_thingy_13 (.\input (delay_thingy_12_output), .\output (delay_thingy_13_output));
  delay_thingy delay_thingy_14 (.\input (delay_thingy_15_output), .\output (\output ));
  delay_thingy delay_thingy_15 (.\input (delay_thingy_13_output), .\output (delay_thingy_15_output));
endmodule

module microcode_decoder_for_jump_address (
  input  [6:0] current_microinstruction,
  input  chip_select,
  output [31:0] microinstruction_to_be_executed
);

  wire [6:0] pull_resistor_1_node;
  wire [31:0] microinstruction_list_for_unconditional_jump_1_fifth_microinstructions,
       microinstruction_list_for_unconditional_jump_1_first_microinstructions,
       microinstruction_list_for_unconditional_jump_1_fourth_microinstructions,
       microinstruction_list_for_unconditional_jump_1_second_microinstructions,
       microinstruction_list_for_unconditional_jump_1_seventh_microinstructions,
       microinstruction_list_for_unconditional_jump_1_sixth_microinstructions,
       microinstruction_list_for_unconditional_jump_1_third_microinstructions;

  Pull_Resistor pull_resistor_1 (.node(pull_resistor_1_node));
  microinstruction_list_for_unconditional_jump microinstruction_list_for_unconditional_jump_1 (
    .first_microinstructions(microinstruction_list_for_unconditional_jump_1_first_microinstructions),
    .third_microinstructions(microinstruction_list_for_unconditional_jump_1_third_microinstructions),
    .fifth_microinstructions(microinstruction_list_for_unconditional_jump_1_fifth_microinstructions),
    .seventh_microinstructions(microinstruction_list_for_unconditional_jump_1_seventh_microinstructions),
    .second_microinstructions(microinstruction_list_for_unconditional_jump_1_second_microinstructions),
    .fourth_microinstructions(microinstruction_list_for_unconditional_jump_1_fourth_microinstructions),
    .sixth_microinstructions(microinstruction_list_for_unconditional_jump_1_sixth_microinstructions));
  assign pull_resistor_1_node = chip_select ? current_microinstruction : 7'bz;  // Controlled_Buffer controlled_buffer_1
  Pull_Resistor pull_resistor_2 (.node(microinstruction_list_for_unconditional_jump_1_second_microinstructions));
  Pull_Resistor pull_resistor_3 (.node(microinstruction_list_for_unconditional_jump_1_third_microinstructions));
  Pull_Resistor pull_resistor_4 (.node(microinstruction_list_for_unconditional_jump_1_fifth_microinstructions));
  Pull_Resistor pull_resistor_5 (.node(microinstruction_list_for_unconditional_jump_1_first_microinstructions));
  Pull_Resistor pull_resistor_6 (.node(microinstruction_list_for_unconditional_jump_1_sixth_microinstructions));
  Pull_Resistor pull_resistor_7 (.node(microinstruction_list_for_unconditional_jump_1_seventh_microinstructions));
  Pull_Resistor pull_resistor_8 (.node(microinstruction_list_for_unconditional_jump_1_seventh_microinstructions));
  Pull_Resistor pull_resistor_9 (.node(microinstruction_list_for_unconditional_jump_1_fourth_microinstructions));
  assign microinstruction_to_be_executed = pull_resistor_1_node[0] ? microinstruction_list_for_unconditional_jump_1_second_microinstructions : 32'bz;  // Controlled_Buffer controlled_buffer_2
  assign microinstruction_to_be_executed = pull_resistor_1_node[1] ? microinstruction_list_for_unconditional_jump_1_first_microinstructions : 32'bz;  // Controlled_Buffer controlled_buffer_3
  assign microinstruction_to_be_executed = pull_resistor_1_node[2] ? microinstruction_list_for_unconditional_jump_1_third_microinstructions : 32'bz;  // Controlled_Buffer controlled_buffer_4
  assign microinstruction_to_be_executed = pull_resistor_1_node[3] ? microinstruction_list_for_unconditional_jump_1_fourth_microinstructions : 32'bz;  // Controlled_Buffer controlled_buffer_5
  assign microinstruction_to_be_executed = pull_resistor_1_node[4] ? microinstruction_list_for_unconditional_jump_1_fifth_microinstructions : 32'bz;  // Controlled_Buffer controlled_buffer_6
  assign microinstruction_to_be_executed = pull_resistor_1_node[5] ? microinstruction_list_for_unconditional_jump_1_sixth_microinstructions : 32'bz;  // Controlled_Buffer controlled_buffer_7
  assign microinstruction_to_be_executed = pull_resistor_1_node[6] ? microinstruction_list_for_unconditional_jump_1_seventh_microinstructions : 32'bz;  // Controlled_Buffer controlled_buffer_8
endmodule

module microinstruction_list_for_unconditional_jump (
  output [31:0] first_microinstructions,
  output [31:0] third_microinstructions,
  output [31:0] fifth_microinstructions,
  output [31:0] seventh_microinstructions,
  output [31:0] second_microinstructions,
  output [31:0] fourth_microinstructions,
  output [31:0] sixth_microinstructions
);

  Pull_Resistor pull_resistor_1 (.node(fifth_microinstructions[31]));
  Pull_Resistor #(.pull(1)) pull_resistor_2 (.node(first_microinstructions[4]));

  assign fifth_microinstructions[30:0] = {31{fifth_microinstructions[31]}};
  assign {first_microinstructions[31:5], first_microinstructions[3:0]} = {31{fifth_microinstructions[31]}};
  assign fourth_microinstructions = {{7{fifth_microinstructions[31]}}, first_microinstructions[4], {24{fifth_microinstructions[31]}}};
  assign second_microinstructions = {{11{fifth_microinstructions[31]}}, {2{first_microinstructions[4]}}, {6{fifth_microinstructions[31]}}, first_microinstructions[4], {6{fifth_microinstructions[31]}}, first_microinstructions[4], {5{fifth_microinstructions[31]}}};
  assign seventh_microinstructions = {32{fifth_microinstructions[31]}};
  assign sixth_microinstructions = {32{fifth_microinstructions[31]}};
  assign third_microinstructions = {{9{fifth_microinstructions[31]}}, first_microinstructions[4], {17{fifth_microinstructions[31]}}, first_microinstructions[4], fifth_microinstructions[31], first_microinstructions[4], {2{fifth_microinstructions[31]}}};
endmodule

module control_signal_decoder_for_jump_if_zero (
  input  [6:0] current_microinstruction,
  input  chip_select,
  input  is_zero,
  output [31:0] microinstruction_to_be_executed
);

  wire [6:0] pull_resistor_1_node;
  wire [31:0] microinstruction_list_for_jump_if_zero_1_fifth_microinstructions,
       microinstruction_list_for_jump_if_zero_1_first_microinstructions,
       microinstruction_list_for_jump_if_zero_1_fourth_microinstructions,
       microinstruction_list_for_jump_if_zero_1_seventh_microinstructions,
       microinstruction_list_for_jump_if_zero_1_sixth_microinstructions,
       microinstruction_list_for_jump_if_zero_1_third_microinstructions, pull_resistor_2_node;

  Pull_Resistor pull_resistor_1 (.node(pull_resistor_1_node));
  assign pull_resistor_1_node = chip_select ? current_microinstruction : 7'bz;  // Controlled_Buffer controlled_buffer_1
  Pull_Resistor pull_resistor_2 (.node(pull_resistor_2_node));
  microinstruction_list_for_jump_if_zero microinstruction_list_for_jump_if_zero_1 (
    .is_zero(is_zero),
    .first_microinstructions(microinstruction_list_for_jump_if_zero_1_first_microinstructions),
    .third_microinstructions(microinstruction_list_for_jump_if_zero_1_third_microinstructions),
    .fifth_microinstructions(microinstruction_list_for_jump_if_zero_1_fifth_microinstructions),
    .seventh_microinstructions(microinstruction_list_for_jump_if_zero_1_seventh_microinstructions),
    .second_microinstructions(pull_resistor_2_node),
    .fourth_microinstructions(microinstruction_list_for_jump_if_zero_1_fourth_microinstructions),
    .sixth_microinstructions(microinstruction_list_for_jump_if_zero_1_sixth_microinstructions));
  Pull_Resistor pull_resistor_3 (.node(microinstruction_list_for_jump_if_zero_1_sixth_microinstructions));
  Pull_Resistor pull_resistor_4 (.node(microinstruction_list_for_jump_if_zero_1_third_microinstructions));
  Pull_Resistor pull_resistor_5 (.node(microinstruction_list_for_jump_if_zero_1_fifth_microinstructions));
  Pull_Resistor pull_resistor_6 (.node(microinstruction_list_for_jump_if_zero_1_first_microinstructions));
  Pull_Resistor pull_resistor_7 (.node(microinstruction_list_for_jump_if_zero_1_seventh_microinstructions));
  Pull_Resistor pull_resistor_8 (.node(microinstruction_list_for_jump_if_zero_1_fourth_microinstructions));
  assign microinstruction_to_be_executed = pull_resistor_1_node[0] ? pull_resistor_2_node : 32'bz;  // Controlled_Buffer controlled_buffer_2
  assign microinstruction_to_be_executed = pull_resistor_1_node[1] ? microinstruction_list_for_jump_if_zero_1_first_microinstructions : 32'bz;  // Controlled_Buffer controlled_buffer_3
  assign microinstruction_to_be_executed = pull_resistor_1_node[2] ? microinstruction_list_for_jump_if_zero_1_third_microinstructions : 32'bz;  // Controlled_Buffer controlled_buffer_4
  assign microinstruction_to_be_executed = pull_resistor_1_node[3] ? microinstruction_list_for_jump_if_zero_1_fourth_microinstructions : 32'bz;  // Controlled_Buffer controlled_buffer_5
  assign microinstruction_to_be_executed = pull_resistor_1_node[4] ? microinstruction_list_for_jump_if_zero_1_fifth_microinstructions : 32'bz;  // Controlled_Buffer controlled_buffer_6
  assign microinstruction_to_be_executed = pull_resistor_1_node[5] ? microinstruction_list_for_jump_if_zero_1_sixth_microinstructions : 32'bz;  // Controlled_Buffer controlled_buffer_7
  assign microinstruction_to_be_executed = pull_resistor_1_node[6] ? microinstruction_list_for_jump_if_zero_1_seventh_microinstructions : 32'bz;  // Controlled_Buffer controlled_buffer_8
endmodule
module microinstruction_list_for_jump_if_zero (
  input  is_zero,
  output [31:0] first_microinstructions,
  output [31:0] third_microinstructions,
  output [31:0] fifth_microinstructions,
  output [31:0] seventh_microinstructions,
  output [31:0] second_microinstructions,
  output [31:0] fourth_microinstructions,
  output [31:0] sixth_microinstructions
);

  Pull_Resistor pull_resistor_1 (.node(fifth_microinstructions[31]));
  Pull_Resistor #(.pull(1)) pull_resistor_2 (.node(first_microinstructions[4]));
  assign third_microinstructions = is_zero ? {{9{fifth_microinstructions[31]}}, first_microinstructions[4], {17{fifth_microinstructions[31]}}, first_microinstructions[4], fifth_microinstructions[31], first_microinstructions[4], {2{fifth_microinstructions[31]}}} : 32'bz;  // Controlled_Buffer controlled_buffer_1
  Pull_Resistor pull_resistor_3 (.node(third_microinstructions));
  assign fourth_microinstructions = is_zero ? {{7{fifth_microinstructions[31]}}, first_microinstructions[4], {24{fifth_microinstructions[31]}}} : 32'bz;  // Controlled_Buffer controlled_buffer_2
  Pull_Resistor pull_resistor_4 (.node(fourth_microinstructions));

  assign fifth_microinstructions[30:0] = {31{fifth_microinstructions[31]}};
  assign {first_microinstructions[31:5], first_microinstructions[3:0]} = {31{fifth_microinstructions[31]}};
  assign second_microinstructions = {{11{fifth_microinstructions[31]}}, {2{first_microinstructions[4]}}, {6{fifth_microinstructions[31]}}, first_microinstructions[4], {6{fifth_microinstructions[31]}}, first_microinstructions[4], {5{fifth_microinstructions[31]}}};
  assign seventh_microinstructions = {32{fifth_microinstructions[31]}};
  assign sixth_microinstructions = {32{fifth_microinstructions[31]}};
endmodule

module microinstruction_decoder_for_sub_value_from_a_register (
  input  [6:0] current_microinstruction,
  input  chip_select,
  output [31:0] microinstruction_to_be_executed
);

  wire [6:0] pull_resistor_1_node;
  wire [31:0] microinstruction_list_for_sub_value_from_a_register_1_fifth_microinstructions,
       microinstruction_list_for_sub_value_from_a_register_1_first_microinstructions,
       microinstruction_list_for_sub_value_from_a_register_1_fourth_microinstructions,
       microinstruction_list_for_sub_value_from_a_register_1_second_microinstructions,
       microinstruction_list_for_sub_value_from_a_register_1_seventh_microinstructions,
       microinstruction_list_for_sub_value_from_a_register_1_sixth_microinstructions,
       microinstruction_list_for_sub_value_from_a_register_1_third_microinstructions;

  Pull_Resistor pull_resistor_1 (.node(pull_resistor_1_node));
  assign pull_resistor_1_node = chip_select ? current_microinstruction : 7'bz;  // Controlled_Buffer controlled_buffer_1
  microinstruction_list_for_sub_value_from_a_register microinstruction_list_for_sub_value_from_a_register_1 (
    .first_microinstructions(microinstruction_list_for_sub_value_from_a_register_1_first_microinstructions),
    .third_microinstructions(microinstruction_list_for_sub_value_from_a_register_1_third_microinstructions),
    .fifth_microinstructions(microinstruction_list_for_sub_value_from_a_register_1_fifth_microinstructions),
    .seventh_microinstructions(microinstruction_list_for_sub_value_from_a_register_1_seventh_microinstructions),
    .second_microinstructions(microinstruction_list_for_sub_value_from_a_register_1_second_microinstructions),
    .fourth_microinstructions(microinstruction_list_for_sub_value_from_a_register_1_fourth_microinstructions),
    .sixth_microinstructions(microinstruction_list_for_sub_value_from_a_register_1_sixth_microinstructions));
  Pull_Resistor pull_resistor_2 (.node(microinstruction_list_for_sub_value_from_a_register_1_second_microinstructions));
  Pull_Resistor pull_resistor_3 (.node(microinstruction_list_for_sub_value_from_a_register_1_sixth_microinstructions));
  Pull_Resistor pull_resistor_4 (.node(microinstruction_list_for_sub_value_from_a_register_1_third_microinstructions));
  Pull_Resistor pull_resistor_5 (.node(microinstruction_list_for_sub_value_from_a_register_1_fifth_microinstructions));
  Pull_Resistor pull_resistor_6 (.node(microinstruction_list_for_sub_value_from_a_register_1_first_microinstructions));
  Pull_Resistor pull_resistor_7 (.node(microinstruction_list_for_sub_value_from_a_register_1_seventh_microinstructions));
  Pull_Resistor pull_resistor_8 (.node(microinstruction_list_for_sub_value_from_a_register_1_fourth_microinstructions));
  assign microinstruction_to_be_executed = pull_resistor_1_node[0] ? microinstruction_list_for_sub_value_from_a_register_1_second_microinstructions : 32'bz;  // Controlled_Buffer controlled_buffer_2
  assign microinstruction_to_be_executed = pull_resistor_1_node[1] ? microinstruction_list_for_sub_value_from_a_register_1_first_microinstructions : 32'bz;  // Controlled_Buffer controlled_buffer_3
  assign microinstruction_to_be_executed = pull_resistor_1_node[2] ? microinstruction_list_for_sub_value_from_a_register_1_third_microinstructions : 32'bz;  // Controlled_Buffer controlled_buffer_4
  assign microinstruction_to_be_executed = pull_resistor_1_node[3] ? microinstruction_list_for_sub_value_from_a_register_1_fourth_microinstructions : 32'bz;  // Controlled_Buffer controlled_buffer_5
  assign microinstruction_to_be_executed = pull_resistor_1_node[4] ? microinstruction_list_for_sub_value_from_a_register_1_fifth_microinstructions : 32'bz;  // Controlled_Buffer controlled_buffer_6
  assign microinstruction_to_be_executed = pull_resistor_1_node[5] ? microinstruction_list_for_sub_value_from_a_register_1_sixth_microinstructions : 32'bz;  // Controlled_Buffer controlled_buffer_7
  assign microinstruction_to_be_executed = pull_resistor_1_node[6] ? microinstruction_list_for_sub_value_from_a_register_1_seventh_microinstructions : 32'bz;  // Controlled_Buffer controlled_buffer_8
endmodule

module microinstruction_list_for_sub_value_from_a_register (
  output [31:0] first_microinstructions,
  output [31:0] third_microinstructions,
  output [31:0] fifth_microinstructions,
  output [31:0] seventh_microinstructions,
  output [31:0] second_microinstructions,
  output [31:0] fourth_microinstructions,
  output [31:0] sixth_microinstructions
);

  Pull_Resistor pull_resistor_1 (.node(fifth_microinstructions[31]));
  Pull_Resistor #(.pull(1)) pull_resistor_2 (.node(second_microinstructions[20]));
  Pull_Resistor #(.pull(1)) pull_resistor_3 (.node(first_microinstructions[4]));
  Pull_Resistor #(.pull(1)) pull_resistor_4 (.node(third_microinstructions[8]));
  Pull_Resistor #(.pull(1)) pull_resistor_5 (.node(fifth_microinstructions[25]));

  assign {fifth_microinstructions[30:26], fifth_microinstructions[24:0]} = {{18{fifth_microinstructions[31]}}, fifth_microinstructions[25], fifth_microinstructions[31], fifth_microinstructions[25], {7{fifth_microinstructions[31]}}, fifth_microinstructions[25], fifth_microinstructions[31]};
  assign {first_microinstructions[31:5], first_microinstructions[3:0]} = {31{fifth_microinstructions[31]}};
  assign fourth_microinstructions = {{8{fifth_microinstructions[31]}}, fifth_microinstructions[25], {12{fifth_microinstructions[31]}}, fifth_microinstructions[25], {10{fifth_microinstructions[31]}}};
  assign {second_microinstructions[31:21], second_microinstructions[19:0]} = {{11{fifth_microinstructions[31]}}, second_microinstructions[20], {6{fifth_microinstructions[31]}}, second_microinstructions[20], {6{fifth_microinstructions[31]}}, second_microinstructions[20], {5{fifth_microinstructions[31]}}};
  assign seventh_microinstructions = {32{fifth_microinstructions[31]}};
  assign sixth_microinstructions = {32{fifth_microinstructions[31]}};
  assign {third_microinstructions[31:9], third_microinstructions[7:0]} = {{27{fifth_microinstructions[31]}}, third_microinstructions[8], {3{fifth_microinstructions[31]}}};
endmodule

module microinstruction_decoder_for_add_value_to_a_register (
  input  [6:0] current_microinstruction,
  input  chip_select,
  output [31:0] microinstruction_to_be_executed
);

  wire [6:0] pull_resistor_1_node;
  wire [31:0] microinstruction_list_for_add_value_to_a_register_1_fifth_microinstructions,
       microinstruction_list_for_add_value_to_a_register_1_first_microinstructions,
       microinstruction_list_for_add_value_to_a_register_1_fourth_microinstructions,
       microinstruction_list_for_add_value_to_a_register_1_second_microinstructions,
       microinstruction_list_for_add_value_to_a_register_1_seventh_microinstructions,
       microinstruction_list_for_add_value_to_a_register_1_sixth_microinstructions,
       microinstruction_list_for_add_value_to_a_register_1_third_microinstructions;

  Pull_Resistor pull_resistor_1 (.node(pull_resistor_1_node));
  assign pull_resistor_1_node = chip_select ? current_microinstruction : 7'bz;  // Controlled_Buffer controlled_buffer_1
  microinstruction_list_for_add_value_to_a_register microinstruction_list_for_add_value_to_a_register_1 (
    .first_microinstructions(microinstruction_list_for_add_value_to_a_register_1_first_microinstructions),
    .third_microinstructions(microinstruction_list_for_add_value_to_a_register_1_third_microinstructions),
    .fifth_microinstructions(microinstruction_list_for_add_value_to_a_register_1_fifth_microinstructions),
    .seventh_microinstructions(microinstruction_list_for_add_value_to_a_register_1_seventh_microinstructions),
    .second_microinstructions(microinstruction_list_for_add_value_to_a_register_1_second_microinstructions),
    .fourth_microinstructions(microinstruction_list_for_add_value_to_a_register_1_fourth_microinstructions),
    .sixth_microinstructions(microinstruction_list_for_add_value_to_a_register_1_sixth_microinstructions));
  Pull_Resistor pull_resistor_2 (.node(microinstruction_list_for_add_value_to_a_register_1_second_microinstructions));
  Pull_Resistor pull_resistor_3 (.node(microinstruction_list_for_add_value_to_a_register_1_sixth_microinstructions));
  Pull_Resistor pull_resistor_4 (.node(microinstruction_list_for_add_value_to_a_register_1_third_microinstructions));
  Pull_Resistor pull_resistor_5 (.node(microinstruction_list_for_add_value_to_a_register_1_fifth_microinstructions));
  Pull_Resistor pull_resistor_6 (.node(microinstruction_list_for_add_value_to_a_register_1_first_microinstructions));
  Pull_Resistor pull_resistor_7 (.node(microinstruction_list_for_add_value_to_a_register_1_seventh_microinstructions));
  Pull_Resistor pull_resistor_8 (.node(microinstruction_list_for_add_value_to_a_register_1_fourth_microinstructions));
  assign microinstruction_to_be_executed = pull_resistor_1_node[0] ? microinstruction_list_for_add_value_to_a_register_1_second_microinstructions : 32'bz;  // Controlled_Buffer controlled_buffer_2
  assign microinstruction_to_be_executed = pull_resistor_1_node[1] ? microinstruction_list_for_add_value_to_a_register_1_first_microinstructions : 32'bz;  // Controlled_Buffer controlled_buffer_3
  assign microinstruction_to_be_executed = pull_resistor_1_node[2] ? microinstruction_list_for_add_value_to_a_register_1_third_microinstructions : 32'bz;  // Controlled_Buffer controlled_buffer_4
  assign microinstruction_to_be_executed = pull_resistor_1_node[3] ? microinstruction_list_for_add_value_to_a_register_1_fourth_microinstructions : 32'bz;  // Controlled_Buffer controlled_buffer_5
  assign microinstruction_to_be_executed = pull_resistor_1_node[4] ? microinstruction_list_for_add_value_to_a_register_1_fifth_microinstructions : 32'bz;  // Controlled_Buffer controlled_buffer_6
  assign microinstruction_to_be_executed = pull_resistor_1_node[5] ? microinstruction_list_for_add_value_to_a_register_1_sixth_microinstructions : 32'bz;  // Controlled_Buffer controlled_buffer_7
  assign microinstruction_to_be_executed = pull_resistor_1_node[6] ? microinstruction_list_for_add_value_to_a_register_1_seventh_microinstructions : 32'bz;  // Controlled_Buffer controlled_buffer_8
endmodule

module microinstruction_list_for_add_value_to_a_register (
  output [31:0] first_microinstructions,
  output [31:0] third_microinstructions,
  output [31:0] fifth_microinstructions,
  output [31:0] seventh_microinstructions,
  output [31:0] second_microinstructions,
  output [31:0] fourth_microinstructions,
  output [31:0] sixth_microinstructions
);

  Pull_Resistor #(.pull(1)) pull_resistor_1 (.node(first_microinstructions[4]));
  Pull_Resistor #(.pull(1)) pull_resistor_2 (.node(second_microinstructions[20]));
  Pull_Resistor pull_resistor_3 (.node(fifth_microinstructions[31]));
  Pull_Resistor #(.pull(1)) pull_resistor_4 (.node(third_microinstructions[8]));
  Pull_Resistor #(.pull(1)) pull_resistor_5 (.node(fifth_microinstructions[25]));

  assign {fifth_microinstructions[30:26], fifth_microinstructions[24:0]} = {{18{fifth_microinstructions[31]}}, fifth_microinstructions[25], {9{fifth_microinstructions[31]}}, fifth_microinstructions[25], fifth_microinstructions[31]};
  assign {first_microinstructions[31:5], first_microinstructions[3:0]} = {31{fifth_microinstructions[31]}};
  assign fourth_microinstructions = {{8{fifth_microinstructions[31]}}, fifth_microinstructions[25], {12{fifth_microinstructions[31]}}, fifth_microinstructions[25], {10{fifth_microinstructions[31]}}};
  assign {second_microinstructions[31:21], second_microinstructions[19:0]} = {{11{fifth_microinstructions[31]}}, second_microinstructions[20], {6{fifth_microinstructions[31]}}, second_microinstructions[20], {6{fifth_microinstructions[31]}}, second_microinstructions[20], {5{fifth_microinstructions[31]}}};
  assign seventh_microinstructions = {32{fifth_microinstructions[31]}};
  assign sixth_microinstructions = {32{fifth_microinstructions[31]}};
  assign {third_microinstructions[31:9], third_microinstructions[7:0]} = {{27{fifth_microinstructions[31]}}, third_microinstructions[8], {3{fifth_microinstructions[31]}}};
endmodule

module microinstruction_list_for_test_value_with_a_register (
  output [31:0] first_microinstructions,
  output [31:0] third_microinstructions,
  output [31:0] fifth_microinstructions,
  output [31:0] seventh_microinstructions,
  output [31:0] second_microinstructions,
  output [31:0] fourth_microinstructions,
  output [31:0] sixth_microinstructions
);

  Pull_Resistor #(.pull(1)) pull_resistor_1 (.node(first_microinstructions[4]));
  Pull_Resistor #(.pull(1)) pull_resistor_2 (.node(second_microinstructions[20]));
  Pull_Resistor pull_resistor_3 (.node(fifth_microinstructions[31]));
  Pull_Resistor #(.pull(1)) pull_resistor_4 (.node(third_microinstructions[8]));
  Pull_Resistor #(.pull(1)) pull_resistor_5 (.node(fifth_microinstructions[25]));

  assign {fifth_microinstructions[30:26], fifth_microinstructions[24:0]} = {{18{fifth_microinstructions[31]}}, fifth_microinstructions[25], fifth_microinstructions[31], fifth_microinstructions[25], {9{fifth_microinstructions[31]}}};
  assign {first_microinstructions[31:5], first_microinstructions[3:0]} = {31{fifth_microinstructions[31]}};
  assign fourth_microinstructions = {{8{fifth_microinstructions[31]}}, fifth_microinstructions[25], {12{fifth_microinstructions[31]}}, fifth_microinstructions[25], {10{fifth_microinstructions[31]}}};
  assign {second_microinstructions[31:21], second_microinstructions[19:0]} = {{11{fifth_microinstructions[31]}}, second_microinstructions[20], {6{fifth_microinstructions[31]}}, second_microinstructions[20], {6{fifth_microinstructions[31]}}, second_microinstructions[20], {5{fifth_microinstructions[31]}}};
  assign seventh_microinstructions = {32{fifth_microinstructions[31]}};
  assign sixth_microinstructions = {32{fifth_microinstructions[31]}};
  assign {third_microinstructions[31:9], third_microinstructions[7:0]} = {{27{fifth_microinstructions[31]}}, third_microinstructions[8], {3{fifth_microinstructions[31]}}};
endmodule

module microinstruction_decoder_for_test_value_with_a_register (
  input  [6:0] current_microinstruction,
  input  chip_select,
  output [31:0] microinstruction_to_be_executed
);

  wire [6:0] pull_resistor_1_node;
  wire [31:0] microinstruction_list_for_test_value_with_a_register_1_fifth_microinstructions,
       microinstruction_list_for_test_value_with_a_register_1_first_microinstructions,
       microinstruction_list_for_test_value_with_a_register_1_fourth_microinstructions,
       microinstruction_list_for_test_value_with_a_register_1_second_microinstructions,
       microinstruction_list_for_test_value_with_a_register_1_seventh_microinstructions,
       microinstruction_list_for_test_value_with_a_register_1_sixth_microinstructions,
       microinstruction_list_for_test_value_with_a_register_1_third_microinstructions;

  Pull_Resistor pull_resistor_1 (.node(pull_resistor_1_node));
  assign pull_resistor_1_node = chip_select ? current_microinstruction : 7'bz;  // Controlled_Buffer controlled_buffer_1
  microinstruction_list_for_test_value_with_a_register microinstruction_list_for_test_value_with_a_register_1 (
    .first_microinstructions(microinstruction_list_for_test_value_with_a_register_1_first_microinstructions),
    .third_microinstructions(microinstruction_list_for_test_value_with_a_register_1_third_microinstructions),
    .fifth_microinstructions(microinstruction_list_for_test_value_with_a_register_1_fifth_microinstructions),
    .seventh_microinstructions(microinstruction_list_for_test_value_with_a_register_1_seventh_microinstructions),
    .second_microinstructions(microinstruction_list_for_test_value_with_a_register_1_second_microinstructions),
    .fourth_microinstructions(microinstruction_list_for_test_value_with_a_register_1_fourth_microinstructions),
    .sixth_microinstructions(microinstruction_list_for_test_value_with_a_register_1_sixth_microinstructions));
  Pull_Resistor pull_resistor_2 (.node(microinstruction_list_for_test_value_with_a_register_1_second_microinstructions));
  Pull_Resistor pull_resistor_3 (.node(microinstruction_list_for_test_value_with_a_register_1_sixth_microinstructions));
  Pull_Resistor pull_resistor_4 (.node(microinstruction_list_for_test_value_with_a_register_1_third_microinstructions));
  Pull_Resistor pull_resistor_5 (.node(microinstruction_list_for_test_value_with_a_register_1_fifth_microinstructions));
  Pull_Resistor pull_resistor_6 (.node(microinstruction_list_for_test_value_with_a_register_1_first_microinstructions));
  Pull_Resistor pull_resistor_7 (.node(microinstruction_list_for_test_value_with_a_register_1_seventh_microinstructions));
  Pull_Resistor pull_resistor_8 (.node(microinstruction_list_for_test_value_with_a_register_1_fourth_microinstructions));
  assign microinstruction_to_be_executed = pull_resistor_1_node[0] ? microinstruction_list_for_test_value_with_a_register_1_second_microinstructions : 32'bz;  // Controlled_Buffer controlled_buffer_2
  assign microinstruction_to_be_executed = pull_resistor_1_node[1] ? microinstruction_list_for_test_value_with_a_register_1_first_microinstructions : 32'bz;  // Controlled_Buffer controlled_buffer_3
  assign microinstruction_to_be_executed = pull_resistor_1_node[2] ? microinstruction_list_for_test_value_with_a_register_1_third_microinstructions : 32'bz;  // Controlled_Buffer controlled_buffer_4
  assign microinstruction_to_be_executed = pull_resistor_1_node[3] ? microinstruction_list_for_test_value_with_a_register_1_fourth_microinstructions : 32'bz;  // Controlled_Buffer controlled_buffer_5
  assign microinstruction_to_be_executed = pull_resistor_1_node[4] ? microinstruction_list_for_test_value_with_a_register_1_fifth_microinstructions : 32'bz;  // Controlled_Buffer controlled_buffer_6
  assign microinstruction_to_be_executed = pull_resistor_1_node[5] ? microinstruction_list_for_test_value_with_a_register_1_sixth_microinstructions : 32'bz;  // Controlled_Buffer controlled_buffer_7
  assign microinstruction_to_be_executed = pull_resistor_1_node[6] ? microinstruction_list_for_test_value_with_a_register_1_seventh_microinstructions : 32'bz;  // Controlled_Buffer controlled_buffer_8
endmodule

module microinstruction_decoder_for_jump_if_less_than_or_equal_to (
  input  [6:0] current_microinstruction,
  input  chip_select,
  input  overflow,
  output [31:0] microinstruction_to_be_executed
);

  wire not_1_out;
  wire [6:0] pull_resistor_1_node;
  wire [31:0] microinstruction_list_for_jump_if_less_than_or_equal_to_1_fifth_microinstructions,
       microinstruction_list_for_jump_if_less_than_or_equal_to_1_first_microinstructions,
       microinstruction_list_for_jump_if_less_than_or_equal_to_1_fourth_microinstructions,
       microinstruction_list_for_jump_if_less_than_or_equal_to_1_second_microinstructions,
       microinstruction_list_for_jump_if_less_than_or_equal_to_1_seventh_microinstructions,
       microinstruction_list_for_jump_if_less_than_or_equal_to_1_sixth_microinstructions,
       microinstruction_list_for_jump_if_less_than_or_equal_to_1_third_microinstructions;

  Pull_Resistor pull_resistor_1 (.node(pull_resistor_1_node));
  assign pull_resistor_1_node = chip_select ? current_microinstruction : 7'bz;  // Controlled_Buffer controlled_buffer_1
  not not_1 (not_1_out, overflow);
  microinstruction_list_for_jump_if_less_than_or_equal_to microinstruction_list_for_jump_if_less_than_or_equal_to_1 (
    .overflow(not_1_out),
    .first_microinstructions(microinstruction_list_for_jump_if_less_than_or_equal_to_1_first_microinstructions),
    .third_microinstructions(microinstruction_list_for_jump_if_less_than_or_equal_to_1_third_microinstructions),
    .fifth_microinstructions(microinstruction_list_for_jump_if_less_than_or_equal_to_1_fifth_microinstructions),
    .seventh_microinstructions(microinstruction_list_for_jump_if_less_than_or_equal_to_1_seventh_microinstructions),
    .second_microinstructions(microinstruction_list_for_jump_if_less_than_or_equal_to_1_second_microinstructions),
    .fourth_microinstructions(microinstruction_list_for_jump_if_less_than_or_equal_to_1_fourth_microinstructions),
    .sixth_microinstructions(microinstruction_list_for_jump_if_less_than_or_equal_to_1_sixth_microinstructions));
  Pull_Resistor pull_resistor_2 (.node(microinstruction_list_for_jump_if_less_than_or_equal_to_1_second_microinstructions));
  Pull_Resistor pull_resistor_3 (.node(microinstruction_list_for_jump_if_less_than_or_equal_to_1_sixth_microinstructions));
  Pull_Resistor pull_resistor_4 (.node(microinstruction_list_for_jump_if_less_than_or_equal_to_1_third_microinstructions));
  Pull_Resistor pull_resistor_5 (.node(microinstruction_list_for_jump_if_less_than_or_equal_to_1_fifth_microinstructions));
  Pull_Resistor pull_resistor_6 (.node(microinstruction_list_for_jump_if_less_than_or_equal_to_1_first_microinstructions));
  Pull_Resistor pull_resistor_7 (.node(microinstruction_list_for_jump_if_less_than_or_equal_to_1_seventh_microinstructions));
  Pull_Resistor pull_resistor_8 (.node(microinstruction_list_for_jump_if_less_than_or_equal_to_1_fourth_microinstructions));
  assign microinstruction_to_be_executed = pull_resistor_1_node[0] ? microinstruction_list_for_jump_if_less_than_or_equal_to_1_second_microinstructions : 32'bz;  // Controlled_Buffer controlled_buffer_2
  assign microinstruction_to_be_executed = pull_resistor_1_node[1] ? microinstruction_list_for_jump_if_less_than_or_equal_to_1_first_microinstructions : 32'bz;  // Controlled_Buffer controlled_buffer_3
  assign microinstruction_to_be_executed = pull_resistor_1_node[2] ? microinstruction_list_for_jump_if_less_than_or_equal_to_1_third_microinstructions : 32'bz;  // Controlled_Buffer controlled_buffer_4
  assign microinstruction_to_be_executed = pull_resistor_1_node[3] ? microinstruction_list_for_jump_if_less_than_or_equal_to_1_fourth_microinstructions : 32'bz;  // Controlled_Buffer controlled_buffer_5
  assign microinstruction_to_be_executed = pull_resistor_1_node[4] ? microinstruction_list_for_jump_if_less_than_or_equal_to_1_fifth_microinstructions : 32'bz;  // Controlled_Buffer controlled_buffer_6
  assign microinstruction_to_be_executed = pull_resistor_1_node[5] ? microinstruction_list_for_jump_if_less_than_or_equal_to_1_sixth_microinstructions : 32'bz;  // Controlled_Buffer controlled_buffer_7
  assign microinstruction_to_be_executed = pull_resistor_1_node[6] ? microinstruction_list_for_jump_if_less_than_or_equal_to_1_seventh_microinstructions : 32'bz;  // Controlled_Buffer controlled_buffer_8
endmodule

module microinstruction_list_for_jump_if_less_than_or_equal_to (
  input  overflow,
  output [31:0] first_microinstructions,
  output [31:0] third_microinstructions,
  output [31:0] fifth_microinstructions,
  output [31:0] seventh_microinstructions,
  output [31:0] second_microinstructions,
  output [31:0] fourth_microinstructions,
  output [31:0] sixth_microinstructions
);

  Pull_Resistor pull_resistor_1 (.node(fifth_microinstructions[31]));
  Pull_Resistor #(.pull(1)) pull_resistor_2 (.node(first_microinstructions[4]));
  assign third_microinstructions = overflow ? {{9{fifth_microinstructions[31]}}, first_microinstructions[4], {17{fifth_microinstructions[31]}}, first_microinstructions[4], fifth_microinstructions[31], first_microinstructions[4], {2{fifth_microinstructions[31]}}} : 32'bz;  // Controlled_Buffer controlled_buffer_1
  Pull_Resistor pull_resistor_3 (.node(third_microinstructions));
  assign fourth_microinstructions = overflow ? {{7{fifth_microinstructions[31]}}, first_microinstructions[4], {24{fifth_microinstructions[31]}}} : 32'bz;  // Controlled_Buffer controlled_buffer_2
  Pull_Resistor pull_resistor_4 (.node(fourth_microinstructions));

  assign fifth_microinstructions[30:0] = {31{fifth_microinstructions[31]}};
  assign {first_microinstructions[31:5], first_microinstructions[3:0]} = {31{fifth_microinstructions[31]}};
  assign second_microinstructions = {{11{fifth_microinstructions[31]}}, {2{first_microinstructions[4]}}, {6{fifth_microinstructions[31]}}, first_microinstructions[4], {6{fifth_microinstructions[31]}}, first_microinstructions[4], {5{fifth_microinstructions[31]}}};
  assign seventh_microinstructions = {32{fifth_microinstructions[31]}};
  assign sixth_microinstructions = {32{fifth_microinstructions[31]}};
endmodule

module microinstruction_decoder_for_write_a_register_to_memory_location (
  input  [6:0] current_microinstruction,
  input  chip_select,
  output [31:0] microinstruction_to_be_executed
);

  wire [6:0] pull_resistor_1_node;
  wire [31:0] microinstruction_list_for_write_a_register_to_memory_location_1_fifth_microinstructions,
       microinstruction_list_for_write_a_register_to_memory_location_1_first_microinstructions,
       microinstruction_list_for_write_a_register_to_memory_location_1_fourth_microinstructions,
       microinstruction_list_for_write_a_register_to_memory_location_1_second_microinstructions,
       microinstruction_list_for_write_a_register_to_memory_location_1_seventh_microinstructions,
       microinstruction_list_for_write_a_register_to_memory_location_1_sixth_microinstructions,
       microinstruction_list_for_write_a_register_to_memory_location_1_third_microinstructions;

  Pull_Resistor pull_resistor_1 (.node(pull_resistor_1_node));
  microinstruction_list_for_write_a_register_to_memory_location microinstruction_list_for_write_a_register_to_memory_location_1 (
    .first_microinstructions(microinstruction_list_for_write_a_register_to_memory_location_1_first_microinstructions),
    .third_microinstructions(microinstruction_list_for_write_a_register_to_memory_location_1_third_microinstructions),
    .fifth_microinstructions(microinstruction_list_for_write_a_register_to_memory_location_1_fifth_microinstructions),
    .seventh_microinstructions(microinstruction_list_for_write_a_register_to_memory_location_1_seventh_microinstructions),
    .second_microinstructions(microinstruction_list_for_write_a_register_to_memory_location_1_second_microinstructions),
    .fourth_microinstructions(microinstruction_list_for_write_a_register_to_memory_location_1_fourth_microinstructions),
    .sixth_microinstructions(microinstruction_list_for_write_a_register_to_memory_location_1_sixth_microinstructions));
  assign pull_resistor_1_node = chip_select ? current_microinstruction : 7'bz;  // Controlled_Buffer controlled_buffer_1
  Pull_Resistor pull_resistor_2 (.node(microinstruction_list_for_write_a_register_to_memory_location_1_second_microinstructions));
  Pull_Resistor pull_resistor_3 (.node(microinstruction_list_for_write_a_register_to_memory_location_1_third_microinstructions));
  Pull_Resistor pull_resistor_4 (.node(microinstruction_list_for_write_a_register_to_memory_location_1_fifth_microinstructions));
  Pull_Resistor pull_resistor_5 (.node(microinstruction_list_for_write_a_register_to_memory_location_1_first_microinstructions));
  Pull_Resistor pull_resistor_6 (.node(microinstruction_list_for_write_a_register_to_memory_location_1_sixth_microinstructions));
  Pull_Resistor pull_resistor_7 (.node(microinstruction_list_for_write_a_register_to_memory_location_1_seventh_microinstructions));
  Pull_Resistor pull_resistor_8 (.node(microinstruction_list_for_write_a_register_to_memory_location_1_seventh_microinstructions));
  Pull_Resistor pull_resistor_9 (.node(microinstruction_list_for_write_a_register_to_memory_location_1_fourth_microinstructions));
  assign microinstruction_to_be_executed = pull_resistor_1_node[0] ? microinstruction_list_for_write_a_register_to_memory_location_1_second_microinstructions : 32'bz;  // Controlled_Buffer controlled_buffer_2
  assign microinstruction_to_be_executed = pull_resistor_1_node[1] ? microinstruction_list_for_write_a_register_to_memory_location_1_first_microinstructions : 32'bz;  // Controlled_Buffer controlled_buffer_3
  assign microinstruction_to_be_executed = pull_resistor_1_node[2] ? microinstruction_list_for_write_a_register_to_memory_location_1_third_microinstructions : 32'bz;  // Controlled_Buffer controlled_buffer_4
  assign microinstruction_to_be_executed = pull_resistor_1_node[3] ? microinstruction_list_for_write_a_register_to_memory_location_1_fourth_microinstructions : 32'bz;  // Controlled_Buffer controlled_buffer_5
  assign microinstruction_to_be_executed = pull_resistor_1_node[4] ? microinstruction_list_for_write_a_register_to_memory_location_1_fifth_microinstructions : 32'bz;  // Controlled_Buffer controlled_buffer_6
  assign microinstruction_to_be_executed = pull_resistor_1_node[5] ? microinstruction_list_for_write_a_register_to_memory_location_1_sixth_microinstructions : 32'bz;  // Controlled_Buffer controlled_buffer_7
  assign microinstruction_to_be_executed = pull_resistor_1_node[6] ? microinstruction_list_for_write_a_register_to_memory_location_1_seventh_microinstructions : 32'bz;  // Controlled_Buffer controlled_buffer_8
endmodule

module microinstruction_list_for_write_a_register_to_memory_location (
  output [31:0] first_microinstructions,
  output [31:0] third_microinstructions,
  output [31:0] fifth_microinstructions,
  output [31:0] seventh_microinstructions,
  output [31:0] second_microinstructions,
  output [31:0] fourth_microinstructions,
  output [31:0] sixth_microinstructions
);

  Pull_Resistor pull_resistor_1 (.node(fifth_microinstructions[31]));
  Pull_Resistor #(.pull(1)) pull_resistor_2 (.node(first_microinstructions[4]));

  assign fifth_microinstructions[30:0] = {31{fifth_microinstructions[31]}};
  assign {first_microinstructions[31:5], first_microinstructions[3:0]} = {31{fifth_microinstructions[31]}};
  assign fourth_microinstructions = {32{fifth_microinstructions[31]}};
  assign second_microinstructions = {{11{fifth_microinstructions[31]}}, {2{first_microinstructions[4]}}, {6{fifth_microinstructions[31]}}, first_microinstructions[4], {6{fifth_microinstructions[31]}}, first_microinstructions[4], {5{fifth_microinstructions[31]}}};
  assign seventh_microinstructions = {32{fifth_microinstructions[31]}};
  assign sixth_microinstructions = {32{fifth_microinstructions[31]}};
  assign third_microinstructions = {{9{fifth_microinstructions[31]}}, {2{first_microinstructions[4]}}, {17{fifth_microinstructions[31]}}, first_microinstructions[4], {3{fifth_microinstructions[31]}}};
endmodule

module microinstruction_decoder_for_jump_if_less_than (
  input  [6:0] current_microinstruction,
  input  chip_select,
  input  less_than,
  output [31:0] microinstruction_to_be_executed
);

  wire [6:0] pull_resistor_1_node;
  wire [31:0] microinstruction_list_for_jump_if_less_than_or_equal_to_1_fifth_microinstructions,
       microinstruction_list_for_jump_if_less_than_or_equal_to_1_first_microinstructions,
       microinstruction_list_for_jump_if_less_than_or_equal_to_1_fourth_microinstructions,
       microinstruction_list_for_jump_if_less_than_or_equal_to_1_second_microinstructions,
       microinstruction_list_for_jump_if_less_than_or_equal_to_1_seventh_microinstructions,
       microinstruction_list_for_jump_if_less_than_or_equal_to_1_sixth_microinstructions,
       microinstruction_list_for_jump_if_less_than_or_equal_to_1_third_microinstructions;

  Pull_Resistor pull_resistor_1 (.node(pull_resistor_1_node));
  assign pull_resistor_1_node = chip_select ? current_microinstruction : 7'bz;  // Controlled_Buffer controlled_buffer_1
  microinstruction_list_for_jump_if_less_than_or_equal_to microinstruction_list_for_jump_if_less_than_or_equal_to_1 (
    .overflow(less_than),
    .first_microinstructions(microinstruction_list_for_jump_if_less_than_or_equal_to_1_first_microinstructions),
    .third_microinstructions(microinstruction_list_for_jump_if_less_than_or_equal_to_1_third_microinstructions),
    .fifth_microinstructions(microinstruction_list_for_jump_if_less_than_or_equal_to_1_fifth_microinstructions),
    .seventh_microinstructions(microinstruction_list_for_jump_if_less_than_or_equal_to_1_seventh_microinstructions),
    .second_microinstructions(microinstruction_list_for_jump_if_less_than_or_equal_to_1_second_microinstructions),
    .fourth_microinstructions(microinstruction_list_for_jump_if_less_than_or_equal_to_1_fourth_microinstructions),
    .sixth_microinstructions(microinstruction_list_for_jump_if_less_than_or_equal_to_1_sixth_microinstructions));
  Pull_Resistor pull_resistor_2 (.node(microinstruction_list_for_jump_if_less_than_or_equal_to_1_second_microinstructions));
  Pull_Resistor pull_resistor_3 (.node(microinstruction_list_for_jump_if_less_than_or_equal_to_1_sixth_microinstructions));
  Pull_Resistor pull_resistor_4 (.node(microinstruction_list_for_jump_if_less_than_or_equal_to_1_third_microinstructions));
  Pull_Resistor pull_resistor_5 (.node(microinstruction_list_for_jump_if_less_than_or_equal_to_1_fifth_microinstructions));
  Pull_Resistor pull_resistor_6 (.node(microinstruction_list_for_jump_if_less_than_or_equal_to_1_first_microinstructions));
  Pull_Resistor pull_resistor_7 (.node(microinstruction_list_for_jump_if_less_than_or_equal_to_1_seventh_microinstructions));
  Pull_Resistor pull_resistor_8 (.node(microinstruction_list_for_jump_if_less_than_or_equal_to_1_fourth_microinstructions));
  assign microinstruction_to_be_executed = pull_resistor_1_node[0] ? microinstruction_list_for_jump_if_less_than_or_equal_to_1_second_microinstructions : 32'bz;  // Controlled_Buffer controlled_buffer_2
  assign microinstruction_to_be_executed = pull_resistor_1_node[1] ? microinstruction_list_for_jump_if_less_than_or_equal_to_1_first_microinstructions : 32'bz;  // Controlled_Buffer controlled_buffer_3
  assign microinstruction_to_be_executed = pull_resistor_1_node[2] ? microinstruction_list_for_jump_if_less_than_or_equal_to_1_third_microinstructions : 32'bz;  // Controlled_Buffer controlled_buffer_4
  assign microinstruction_to_be_executed = pull_resistor_1_node[3] ? microinstruction_list_for_jump_if_less_than_or_equal_to_1_fourth_microinstructions : 32'bz;  // Controlled_Buffer controlled_buffer_5
  assign microinstruction_to_be_executed = pull_resistor_1_node[4] ? microinstruction_list_for_jump_if_less_than_or_equal_to_1_fifth_microinstructions : 32'bz;  // Controlled_Buffer controlled_buffer_6
  assign microinstruction_to_be_executed = pull_resistor_1_node[5] ? microinstruction_list_for_jump_if_less_than_or_equal_to_1_sixth_microinstructions : 32'bz;  // Controlled_Buffer controlled_buffer_7
  assign microinstruction_to_be_executed = pull_resistor_1_node[6] ? microinstruction_list_for_jump_if_less_than_or_equal_to_1_seventh_microinstructions : 32'bz;  // Controlled_Buffer controlled_buffer_8
endmodule

module microinstruction_list_for_jump_if_less_than (
  input  less_than,
  output [31:0] first_microinstructions,
  output [31:0] third_microinstructions,
  output [31:0] fifth_microinstructions,
  output [31:0] seventh_microinstructions,
  output [31:0] second_microinstructions,
  output [31:0] fourth_microinstructions,
  output [31:0] sixth_microinstructions
);

  Pull_Resistor pull_resistor_1 (.node(fifth_microinstructions[31]));
  Pull_Resistor #(.pull(1)) pull_resistor_2 (.node(first_microinstructions[4]));
  assign third_microinstructions = less_than ? {{9{fifth_microinstructions[31]}}, first_microinstructions[4], {17{fifth_microinstructions[31]}}, first_microinstructions[4], fifth_microinstructions[31], first_microinstructions[4], {2{fifth_microinstructions[31]}}} : 32'bz;  // Controlled_Buffer controlled_buffer_1
  Pull_Resistor pull_resistor_3 (.node(third_microinstructions));
  assign fourth_microinstructions = less_than ? {{7{fifth_microinstructions[31]}}, first_microinstructions[4], {24{fifth_microinstructions[31]}}} : 32'bz;  // Controlled_Buffer controlled_buffer_2
  Pull_Resistor pull_resistor_4 (.node(fourth_microinstructions));

  assign fifth_microinstructions[30:0] = {31{fifth_microinstructions[31]}};
  assign {first_microinstructions[31:5], first_microinstructions[3:0]} = {31{fifth_microinstructions[31]}};
  assign second_microinstructions = {{11{fifth_microinstructions[31]}}, {2{first_microinstructions[4]}}, {6{fifth_microinstructions[31]}}, first_microinstructions[4], {6{fifth_microinstructions[31]}}, first_microinstructions[4], {5{fifth_microinstructions[31]}}};
  assign seventh_microinstructions = {32{fifth_microinstructions[31]}};
  assign sixth_microinstructions = {32{fifth_microinstructions[31]}};
endmodule

module flag_register (
  input  store_flags,
  input  is_zero,
  input  overflow,
  input  less_than,
  input  clock,
  output [2:0] \output 
);

  Register #(.width(3)) register_1 (
    .D({less_than, overflow, is_zero}), .en(store_flags), .Q(\output ), .clk(clock));  // open: clr
endmodule

module bin_to_7_segment_decimal_decoder (
  input  [3:0] number,
  input  chip_enable,
  output [6:0] \output 
);

  wire decoder_1_out1, decoder_1_out2, decoder_1_out3, decoder_1_out4, decoder_1_out5, decoder_1_out6,
       decoder_1_out7, decoder_1_out8, decoder_1_out9, pull_resistor_1_node;
  wire [6:0] decimal_table_1_eight, decimal_table_1_five, decimal_table_1_four, decimal_table_1_nine,
       decimal_table_1_one, decimal_table_1_seven, decimal_table_1_six, decimal_table_1_three,
       decimal_table_1_two, decimal_table_1_zero;

  decimal_table decimal_table_1 (
    .zero(decimal_table_1_zero), .one(decimal_table_1_one), .two(decimal_table_1_two),
    .three(decimal_table_1_three), .four(decimal_table_1_four), .five(decimal_table_1_five),
    .six(decimal_table_1_six), .seven(decimal_table_1_seven), .eight(decimal_table_1_eight),
    .nine(decimal_table_1_nine));
  Pull_Resistor pull_resistor_1 (.node(pull_resistor_1_node));
  Decoder #(.select(4)) decoder_1 (
    .out0(pull_resistor_1_node), .out1(decoder_1_out1), .out2(decoder_1_out2), .out3(decoder_1_out3),
    .out4(decoder_1_out4), .out5(decoder_1_out5), .out6(decoder_1_out6), .out7(decoder_1_out7),
    .out8(decoder_1_out8), .out9(decoder_1_out9), .sel(number), .en(chip_enable));  // open: out10, out11, out12, out13, out14, out15
  Pull_Resistor pull_resistor_2 (.node(decoder_1_out8));
  assign \output  = pull_resistor_1_node ? decimal_table_1_zero : 7'bz;  // Controlled_Buffer controlled_buffer_1
  Pull_Resistor pull_resistor_3 (.node(decoder_1_out1));
  assign \output  = decoder_1_out1 ? decimal_table_1_one : 7'bz;  // Controlled_Buffer controlled_buffer_2
  Pull_Resistor pull_resistor_4 (.node(decoder_1_out2));
  assign \output  = decoder_1_out2 ? decimal_table_1_two : 7'bz;  // Controlled_Buffer controlled_buffer_3
  Pull_Resistor pull_resistor_5 (.node(decoder_1_out3));
  assign \output  = decoder_1_out3 ? decimal_table_1_three : 7'bz;  // Controlled_Buffer controlled_buffer_4
  Pull_Resistor pull_resistor_6 (.node(decoder_1_out4));
  assign \output  = decoder_1_out4 ? decimal_table_1_four : 7'bz;  // Controlled_Buffer controlled_buffer_5
  Pull_Resistor pull_resistor_7 (.node(decoder_1_out5));
  assign \output  = decoder_1_out5 ? decimal_table_1_five : 7'bz;  // Controlled_Buffer controlled_buffer_6
  Pull_Resistor pull_resistor_8 (.node(decoder_1_out6));
  assign \output  = decoder_1_out6 ? decimal_table_1_six : 7'bz;  // Controlled_Buffer controlled_buffer_7
  Pull_Resistor pull_resistor_9 (.node(decoder_1_out7));
  assign \output  = decoder_1_out7 ? decimal_table_1_seven : 7'bz;  // Controlled_Buffer controlled_buffer_8
  Pull_Resistor pull_resistor_10 (.node(decimal_table_1_eight));
  assign \output  = decoder_1_out8 ? decimal_table_1_eight : 7'bz;  // Controlled_Buffer controlled_buffer_9
  Pull_Resistor pull_resistor_11 (.node(decoder_1_out9));
  assign \output  = decoder_1_out9 ? decimal_table_1_nine : 7'bz;  // Controlled_Buffer controlled_buffer_10
  Pull_Resistor pull_resistor_12 (.node(\output ));
endmodule

module decimal_table (
  output [6:0] zero,
  output [6:0] one,
  output [6:0] two,
  output [6:0] three,
  output [6:0] four,
  output [6:0] five,
  output [6:0] six,
  output [6:0] seven,
  output [6:0] eight,
  output [6:0] nine
);

  wire pull_resistor_10_node;

  Pull_Resistor pull_resistor_1 (.node(zero[0]));
  Pull_Resistor #(.pull(1)) pull_resistor_2 (.node(six[6]));
  Pull_Resistor pull_resistor_3 (.node(six[3]));
  Pull_Resistor #(.pull(1)) pull_resistor_4 (.node(zero[6]));
  Pull_Resistor pull_resistor_5 (.node(one[5]));
  Pull_Resistor pull_resistor_6 (.node(seven[5]));
  Pull_Resistor #(.pull(1)) pull_resistor_7 (.node(one[6]));
  Pull_Resistor #(.pull(1)) pull_resistor_8 (.node(seven[6]));
  Pull_Resistor pull_resistor_9 (.node(two[6]));
  Pull_Resistor pull_resistor_10 (.node(pull_resistor_10_node));
  Pull_Resistor #(.pull(1)) pull_resistor_11 (.node(two[5]));
  Pull_Resistor pull_resistor_12 (.node(three[4]));
  Pull_Resistor #(.pull(1)) pull_resistor_13 (.node(eight[6]));
  Pull_Resistor #(.pull(1)) pull_resistor_14 (.node(three[6]));
  Pull_Resistor pull_resistor_15 (.node(nine[4]));
  Pull_Resistor pull_resistor_16 (.node(four[5]));
  Pull_Resistor #(.pull(1)) pull_resistor_17 (.node(four[6]));
  Pull_Resistor #(.pull(1)) pull_resistor_18 (.node(nine[6]));
  Pull_Resistor pull_resistor_19 (.node(five[4]));
  Pull_Resistor #(.pull(1)) pull_resistor_20 (.node(five[6]));

  assign eight[5:0] = {6{eight[6]}};
  assign {five[5], five[3:0]} = {five[6], five[4], {3{five[6]}}};
  assign four[4:0] = {four[5], four[6:5], {2{four[6]}}};
  assign {nine[5], nine[3:0]} = {5{nine[6]}};
  assign one[4:0] = {one[5], one[6:5], {2{one[5]}}};
  assign seven[4:0] = {seven[5], {2{seven[6]}}, {2{seven[5]}}};
  assign {six[5:4], six[2:0]} = {5{six[6]}};
  assign {three[5], three[3:0]} = {{3{three[6]}}, three[4], three[6]};
  assign two[4:0] = {{3{two[5]}}, two[6:5]};
  assign zero[5:1] = {5{zero[6]}};
endmodule

module ones_tens_hundreds_to_binary_converter (
  input  [9:0] ones,
  input  [9:0] tens,
  input  [9:0] hundreds,
  output [9:0] ones_2,
  output [9:0] tens_2,
  output [9:0] hundreds_2
);

  tens_converter tens_converter_1 (.in_1(ones), .out_2(ones_2));
  tens_converter tens_converter_2 (.in_1(tens), .out_2(tens_2));
  tens_converter tens_converter_3 (.in_1(hundreds), .out_2(hundreds_2));
endmodule

module tens_converter (
  input  [9:0] in_1,
  output [9:0] out_2
);

  wire [9:0] binary_rom_thingy_1_eight, binary_rom_thingy_1_five, binary_rom_thingy_1_four,
       binary_rom_thingy_1_nine, binary_rom_thingy_1_one, binary_rom_thingy_1_seven, binary_rom_thingy_1_six,
       binary_rom_thingy_1_three, binary_rom_thingy_1_two, binary_rom_thingy_1_zero;

  binary_rom_thingy binary_rom_thingy_1 (
    .zero(binary_rom_thingy_1_zero), .two(binary_rom_thingy_1_two), .three(binary_rom_thingy_1_three),
    .one(binary_rom_thingy_1_one), .four(binary_rom_thingy_1_four), .five(binary_rom_thingy_1_five),
    .six(binary_rom_thingy_1_six), .seven(binary_rom_thingy_1_seven), .eight(binary_rom_thingy_1_eight),
    .nine(binary_rom_thingy_1_nine));
  assign out_2 = in_1[0] ? binary_rom_thingy_1_zero : 10'bz;  // Controlled_Buffer controlled_buffer_1
  assign out_2 = in_1[1] ? binary_rom_thingy_1_one : 10'bz;  // Controlled_Buffer controlled_buffer_2
  assign out_2 = in_1[2] ? binary_rom_thingy_1_two : 10'bz;  // Controlled_Buffer controlled_buffer_3
  assign out_2 = in_1[3] ? binary_rom_thingy_1_three : 10'bz;  // Controlled_Buffer controlled_buffer_4
  assign out_2 = in_1[4] ? binary_rom_thingy_1_four : 10'bz;  // Controlled_Buffer controlled_buffer_5
  assign out_2 = in_1[5] ? binary_rom_thingy_1_five : 10'bz;  // Controlled_Buffer controlled_buffer_6
  assign out_2 = in_1[6] ? binary_rom_thingy_1_six : 10'bz;  // Controlled_Buffer controlled_buffer_7
  assign out_2 = in_1[7] ? binary_rom_thingy_1_seven : 10'bz;  // Controlled_Buffer controlled_buffer_8
  assign out_2 = in_1[8] ? binary_rom_thingy_1_eight : 10'bz;  // Controlled_Buffer controlled_buffer_9
  assign out_2 = in_1[9] ? binary_rom_thingy_1_nine : 10'bz;  // Controlled_Buffer controlled_buffer_10
  Pull_Resistor pull_resistor_1 (.node(out_2));
endmodule

module binary_rom_thingy (
  output [9:0] zero,
  output [9:0] two,
  output [9:0] three,
  output [9:0] one,
  output [9:0] four,
  output [9:0] five,
  output [9:0] six,
  output [9:0] seven,
  output [9:0] eight,
  output [9:0] nine
);

  Pull_Resistor pull_resistor_1 (.node(five[9]));
  Pull_Resistor pull_resistor_2 (.node(zero[9]));
  Pull_Resistor #(.pull(1)) pull_resistor_3 (.node(five[2]));
  Pull_Resistor pull_resistor_4 (.node(one[9]));
  Pull_Resistor pull_resistor_5 (.node(six[9]));
  Pull_Resistor #(.pull(1)) pull_resistor_6 (.node(six[2]));
  Pull_Resistor #(.pull(1)) pull_resistor_7 (.node(one[0]));
  Pull_Resistor pull_resistor_8 (.node(seven[9]));
  Pull_Resistor #(.pull(1)) pull_resistor_9 (.node(seven[2]));
  Pull_Resistor pull_resistor_10 (.node(two[9]));
  Pull_Resistor #(.pull(1)) pull_resistor_11 (.node(two[1]));
  Pull_Resistor pull_resistor_12 (.node(eight[9]));
  Pull_Resistor pull_resistor_13 (.node(three[9]));
  Pull_Resistor #(.pull(1)) pull_resistor_14 (.node(eight[3]));
  Pull_Resistor #(.pull(1)) pull_resistor_15 (.node(three[1]));
  Pull_Resistor pull_resistor_16 (.node(nine[9]));
  Pull_Resistor #(.pull(1)) pull_resistor_17 (.node(nine[3]));
  Pull_Resistor pull_resistor_18 (.node(four[9]));
  Pull_Resistor #(.pull(1)) pull_resistor_19 (.node(four[2]));

  assign {eight[8:4], eight[2:0]} = {8{eight[9]}};
  assign {five[8:3], five[1:0]} = {{7{five[9]}}, five[2]};
  assign {four[8:3], four[1:0]} = {8{four[9]}};
  assign {nine[8:4], nine[2:0]} = {{7{nine[9]}}, nine[3]};
  assign one[8:1] = {8{one[9]}};
  assign {seven[8:3], seven[1:0]} = {{6{seven[9]}}, {2{seven[2]}}};
  assign {six[8:3], six[1:0]} = {{6{six[9]}}, six[2], six[9]};
  assign {three[8:2], three[0]} = {{7{three[9]}}, three[1]};
  assign {two[8:2], two[0]} = {8{two[9]}};
  assign zero[8:0] = {9{zero[9]}};
endmodule

module instruction_decoder_for_mov_address_to_b_register (
  input  [6:0] current_microinstruction,
  input  chip_select,
  output [31:0] microinstruction_to_be_executed
);

  wire [6:0] pull_resistor_1_node;
  wire [31:0] microinstruction_list_for_mov_address_to_reg_b_1_fifth_microinstructions,
       microinstruction_list_for_mov_address_to_reg_b_1_first_microinstructions,
       microinstruction_list_for_mov_address_to_reg_b_1_fourth_microinstructions,
       microinstruction_list_for_mov_address_to_reg_b_1_second_microinstructions,
       microinstruction_list_for_mov_address_to_reg_b_1_seventh_microinstructions,
       microinstruction_list_for_mov_address_to_reg_b_1_sixth_microinstructions,
       microinstruction_list_for_mov_address_to_reg_b_1_third_microinstructions;

  Pull_Resistor pull_resistor_1 (.node(pull_resistor_1_node));
  microinstruction_list_for_mov_address_to_reg_b microinstruction_list_for_mov_address_to_reg_b_1 (
    .first_microinstructions(microinstruction_list_for_mov_address_to_reg_b_1_first_microinstructions),
    .third_microinstructions(microinstruction_list_for_mov_address_to_reg_b_1_third_microinstructions),
    .fifth_microinstructions(microinstruction_list_for_mov_address_to_reg_b_1_fifth_microinstructions),
    .seventh_microinstructions(microinstruction_list_for_mov_address_to_reg_b_1_seventh_microinstructions),
    .second_microinstructions(microinstruction_list_for_mov_address_to_reg_b_1_second_microinstructions),
    .fourth_microinstructions(microinstruction_list_for_mov_address_to_reg_b_1_fourth_microinstructions),
    .sixth_microinstructions(microinstruction_list_for_mov_address_to_reg_b_1_sixth_microinstructions));
  assign pull_resistor_1_node = chip_select ? current_microinstruction : 7'bz;  // Controlled_Buffer controlled_buffer_1
  Pull_Resistor pull_resistor_2 (.node(microinstruction_list_for_mov_address_to_reg_b_1_second_microinstructions));
  Pull_Resistor pull_resistor_3 (.node(microinstruction_list_for_mov_address_to_reg_b_1_third_microinstructions));
  Pull_Resistor pull_resistor_4 (.node(microinstruction_list_for_mov_address_to_reg_b_1_fifth_microinstructions));
  Pull_Resistor pull_resistor_5 (.node(microinstruction_list_for_mov_address_to_reg_b_1_first_microinstructions));
  Pull_Resistor pull_resistor_6 (.node(microinstruction_list_for_mov_address_to_reg_b_1_sixth_microinstructions));
  Pull_Resistor pull_resistor_7 (.node(microinstruction_list_for_mov_address_to_reg_b_1_seventh_microinstructions));
  Pull_Resistor pull_resistor_8 (.node(microinstruction_list_for_mov_address_to_reg_b_1_seventh_microinstructions));
  Pull_Resistor pull_resistor_9 (.node(microinstruction_list_for_mov_address_to_reg_b_1_fourth_microinstructions));
  assign microinstruction_to_be_executed = pull_resistor_1_node[0] ? microinstruction_list_for_mov_address_to_reg_b_1_second_microinstructions : 32'bz;  // Controlled_Buffer controlled_buffer_2
  assign microinstruction_to_be_executed = pull_resistor_1_node[1] ? microinstruction_list_for_mov_address_to_reg_b_1_first_microinstructions : 32'bz;  // Controlled_Buffer controlled_buffer_3
  assign microinstruction_to_be_executed = pull_resistor_1_node[2] ? microinstruction_list_for_mov_address_to_reg_b_1_third_microinstructions : 32'bz;  // Controlled_Buffer controlled_buffer_4
  assign microinstruction_to_be_executed = pull_resistor_1_node[3] ? microinstruction_list_for_mov_address_to_reg_b_1_fourth_microinstructions : 32'bz;  // Controlled_Buffer controlled_buffer_5
  assign microinstruction_to_be_executed = pull_resistor_1_node[4] ? microinstruction_list_for_mov_address_to_reg_b_1_fifth_microinstructions : 32'bz;  // Controlled_Buffer controlled_buffer_6
  assign microinstruction_to_be_executed = pull_resistor_1_node[5] ? microinstruction_list_for_mov_address_to_reg_b_1_sixth_microinstructions : 32'bz;  // Controlled_Buffer controlled_buffer_7
  assign microinstruction_to_be_executed = pull_resistor_1_node[6] ? microinstruction_list_for_mov_address_to_reg_b_1_seventh_microinstructions : 32'bz;  // Controlled_Buffer controlled_buffer_8
endmodule

module microinstruction_list_for_mov_address_to_reg_b (
  output [31:0] first_microinstructions,
  output [31:0] third_microinstructions,
  output [31:0] fifth_microinstructions,
  output [31:0] seventh_microinstructions,
  output [31:0] second_microinstructions,
  output [31:0] fourth_microinstructions,
  output [31:0] sixth_microinstructions
);

  Pull_Resistor pull_resistor_1 (.node(fifth_microinstructions[31]));
  Pull_Resistor #(.pull(1)) pull_resistor_2 (.node(first_microinstructions[4]));

  assign fifth_microinstructions[30:0] = {31{fifth_microinstructions[31]}};
  assign {first_microinstructions[31:5], first_microinstructions[3:0]} = {31{fifth_microinstructions[31]}};
  assign fourth_microinstructions = {32{fifth_microinstructions[31]}};
  assign second_microinstructions = {{11{fifth_microinstructions[31]}}, {2{first_microinstructions[4]}}, {6{fifth_microinstructions[31]}}, first_microinstructions[4], {6{fifth_microinstructions[31]}}, first_microinstructions[4], {5{fifth_microinstructions[31]}}};
  assign seventh_microinstructions = {32{fifth_microinstructions[31]}};
  assign sixth_microinstructions = {32{fifth_microinstructions[31]}};
  assign third_microinstructions = {{9{fifth_microinstructions[31]}}, first_microinstructions[4], fifth_microinstructions[31], {2{first_microinstructions[4]}}, {12{fifth_microinstructions[31]}}, first_microinstructions[4], {6{fifth_microinstructions[31]}}};
endmodule

module microinstruction_decoder_for_sub_value_from_reg_b (
  input  [6:0] current_microinstruction,
  input  chip_select,
  output [31:0] microinstruction_to_be_executed
);

  wire [6:0] pull_resistor_1_node;
  wire [31:0] microinstruction_list_for_sub_value_from_reg_b_1_fifth_microinstructions,
       microinstruction_list_for_sub_value_from_reg_b_1_first_microinstructions,
       microinstruction_list_for_sub_value_from_reg_b_1_fourth_microinstructions,
       microinstruction_list_for_sub_value_from_reg_b_1_second_microinstructions,
       microinstruction_list_for_sub_value_from_reg_b_1_seventh_microinstructions,
       microinstruction_list_for_sub_value_from_reg_b_1_sixth_microinstructions,
       microinstruction_list_for_sub_value_from_reg_b_1_third_microinstructions;

  Pull_Resistor pull_resistor_1 (.node(pull_resistor_1_node));
  assign pull_resistor_1_node = chip_select ? current_microinstruction : 7'bz;  // Controlled_Buffer controlled_buffer_1
  microinstruction_list_for_sub_value_from_reg_b microinstruction_list_for_sub_value_from_reg_b_1 (
    .first_microinstructions(microinstruction_list_for_sub_value_from_reg_b_1_first_microinstructions),
    .third_microinstructions(microinstruction_list_for_sub_value_from_reg_b_1_third_microinstructions),
    .fifth_microinstructions(microinstruction_list_for_sub_value_from_reg_b_1_fifth_microinstructions),
    .seventh_microinstructions(microinstruction_list_for_sub_value_from_reg_b_1_seventh_microinstructions),
    .second_microinstructions(microinstruction_list_for_sub_value_from_reg_b_1_second_microinstructions),
    .fourth_microinstructions(microinstruction_list_for_sub_value_from_reg_b_1_fourth_microinstructions),
    .sixth_microinstructions(microinstruction_list_for_sub_value_from_reg_b_1_sixth_microinstructions));
  Pull_Resistor pull_resistor_2 (.node(microinstruction_list_for_sub_value_from_reg_b_1_second_microinstructions));
  Pull_Resistor pull_resistor_3 (.node(microinstruction_list_for_sub_value_from_reg_b_1_sixth_microinstructions));
  Pull_Resistor pull_resistor_4 (.node(microinstruction_list_for_sub_value_from_reg_b_1_third_microinstructions));
  Pull_Resistor pull_resistor_5 (.node(microinstruction_list_for_sub_value_from_reg_b_1_fifth_microinstructions));
  Pull_Resistor pull_resistor_6 (.node(microinstruction_list_for_sub_value_from_reg_b_1_first_microinstructions));
  Pull_Resistor pull_resistor_7 (.node(microinstruction_list_for_sub_value_from_reg_b_1_seventh_microinstructions));
  Pull_Resistor pull_resistor_8 (.node(microinstruction_list_for_sub_value_from_reg_b_1_fourth_microinstructions));
  assign microinstruction_to_be_executed = pull_resistor_1_node[0] ? microinstruction_list_for_sub_value_from_reg_b_1_second_microinstructions : 32'bz;  // Controlled_Buffer controlled_buffer_2
  assign microinstruction_to_be_executed = pull_resistor_1_node[1] ? microinstruction_list_for_sub_value_from_reg_b_1_first_microinstructions : 32'bz;  // Controlled_Buffer controlled_buffer_3
  assign microinstruction_to_be_executed = pull_resistor_1_node[2] ? microinstruction_list_for_sub_value_from_reg_b_1_third_microinstructions : 32'bz;  // Controlled_Buffer controlled_buffer_4
  assign microinstruction_to_be_executed = pull_resistor_1_node[3] ? microinstruction_list_for_sub_value_from_reg_b_1_fourth_microinstructions : 32'bz;  // Controlled_Buffer controlled_buffer_5
  assign microinstruction_to_be_executed = pull_resistor_1_node[4] ? microinstruction_list_for_sub_value_from_reg_b_1_fifth_microinstructions : 32'bz;  // Controlled_Buffer controlled_buffer_6
  assign microinstruction_to_be_executed = pull_resistor_1_node[5] ? microinstruction_list_for_sub_value_from_reg_b_1_sixth_microinstructions : 32'bz;  // Controlled_Buffer controlled_buffer_7
  assign microinstruction_to_be_executed = pull_resistor_1_node[6] ? microinstruction_list_for_sub_value_from_reg_b_1_seventh_microinstructions : 32'bz;  // Controlled_Buffer controlled_buffer_8
endmodule

module microinstruction_list_for_sub_value_from_reg_b (
  output [31:0] first_microinstructions,
  output [31:0] third_microinstructions,
  output [31:0] fifth_microinstructions,
  output [31:0] seventh_microinstructions,
  output [31:0] second_microinstructions,
  output [31:0] fourth_microinstructions,
  output [31:0] sixth_microinstructions
);

  Pull_Resistor #(.pull(1)) pull_resistor_1 (.node(second_microinstructions[20]));
  Pull_Resistor #(.pull(1)) pull_resistor_2 (.node(first_microinstructions[4]));
  Pull_Resistor pull_resistor_3 (.node(fifth_microinstructions[31]));
  Pull_Resistor #(.pull(1)) pull_resistor_4 (.node(third_microinstructions[8]));
  Pull_Resistor #(.pull(1)) pull_resistor_5 (.node(fifth_microinstructions[25]));

  assign {fifth_microinstructions[30:26], fifth_microinstructions[24:0]} = {{18{fifth_microinstructions[31]}}, fifth_microinstructions[25], fifth_microinstructions[31], fifth_microinstructions[25], {2{fifth_microinstructions[31]}}, fifth_microinstructions[25], {6{fifth_microinstructions[31]}}};
  assign {first_microinstructions[31:5], first_microinstructions[3:0]} = {31{fifth_microinstructions[31]}};
  assign fourth_microinstructions = {{8{fifth_microinstructions[31]}}, fifth_microinstructions[25], {12{fifth_microinstructions[31]}}, fifth_microinstructions[25], {10{fifth_microinstructions[31]}}};
  assign {second_microinstructions[31:21], second_microinstructions[19:0]} = {{11{fifth_microinstructions[31]}}, second_microinstructions[20], {6{fifth_microinstructions[31]}}, second_microinstructions[20], {6{fifth_microinstructions[31]}}, second_microinstructions[20], {5{fifth_microinstructions[31]}}};
  assign seventh_microinstructions = {32{fifth_microinstructions[31]}};
  assign sixth_microinstructions = {32{fifth_microinstructions[31]}};
  assign {third_microinstructions[31:9], third_microinstructions[7:0]} = {{23{fifth_microinstructions[31]}}, third_microinstructions[8], {7{fifth_microinstructions[31]}}};
endmodule

module microinstruction_decoder_for_add_value_to_b_register (
  input  [6:0] current_microinstruction,
  input  chip_select,
  output [31:0] microinstruction_to_be_executed
);

  wire [6:0] pull_resistor_1_node;
  wire [31:0] microinstruction_list_for_add_value_to_b_register_1_fifth_microinstructions,
       microinstruction_list_for_add_value_to_b_register_1_first_microinstructions,
       microinstruction_list_for_add_value_to_b_register_1_fourth_microinstructions,
       microinstruction_list_for_add_value_to_b_register_1_second_microinstructions,
       microinstruction_list_for_add_value_to_b_register_1_seventh_microinstructions,
       microinstruction_list_for_add_value_to_b_register_1_sixth_microinstructions,
       microinstruction_list_for_add_value_to_b_register_1_third_microinstructions;

  Pull_Resistor pull_resistor_1 (.node(pull_resistor_1_node));
  assign pull_resistor_1_node = chip_select ? current_microinstruction : 7'bz;  // Controlled_Buffer controlled_buffer_1
  microinstruction_list_for_add_value_to_b_register microinstruction_list_for_add_value_to_b_register_1 (
    .first_microinstructions(microinstruction_list_for_add_value_to_b_register_1_first_microinstructions),
    .third_microinstructions(microinstruction_list_for_add_value_to_b_register_1_third_microinstructions),
    .fifth_microinstructions(microinstruction_list_for_add_value_to_b_register_1_fifth_microinstructions),
    .seventh_microinstructions(microinstruction_list_for_add_value_to_b_register_1_seventh_microinstructions),
    .second_microinstructions(microinstruction_list_for_add_value_to_b_register_1_second_microinstructions),
    .fourth_microinstructions(microinstruction_list_for_add_value_to_b_register_1_fourth_microinstructions),
    .sixth_microinstructions(microinstruction_list_for_add_value_to_b_register_1_sixth_microinstructions));
  Pull_Resistor pull_resistor_2 (.node(microinstruction_list_for_add_value_to_b_register_1_second_microinstructions));
  Pull_Resistor pull_resistor_3 (.node(microinstruction_list_for_add_value_to_b_register_1_sixth_microinstructions));
  Pull_Resistor pull_resistor_4 (.node(microinstruction_list_for_add_value_to_b_register_1_third_microinstructions));
  Pull_Resistor pull_resistor_5 (.node(microinstruction_list_for_add_value_to_b_register_1_fifth_microinstructions));
  Pull_Resistor pull_resistor_6 (.node(microinstruction_list_for_add_value_to_b_register_1_first_microinstructions));
  Pull_Resistor pull_resistor_7 (.node(microinstruction_list_for_add_value_to_b_register_1_seventh_microinstructions));
  Pull_Resistor pull_resistor_8 (.node(microinstruction_list_for_add_value_to_b_register_1_fourth_microinstructions));
  assign microinstruction_to_be_executed = pull_resistor_1_node[0] ? microinstruction_list_for_add_value_to_b_register_1_second_microinstructions : 32'bz;  // Controlled_Buffer controlled_buffer_2
  assign microinstruction_to_be_executed = pull_resistor_1_node[1] ? microinstruction_list_for_add_value_to_b_register_1_first_microinstructions : 32'bz;  // Controlled_Buffer controlled_buffer_3
  assign microinstruction_to_be_executed = pull_resistor_1_node[2] ? microinstruction_list_for_add_value_to_b_register_1_third_microinstructions : 32'bz;  // Controlled_Buffer controlled_buffer_4
  assign microinstruction_to_be_executed = pull_resistor_1_node[3] ? microinstruction_list_for_add_value_to_b_register_1_fourth_microinstructions : 32'bz;  // Controlled_Buffer controlled_buffer_5
  assign microinstruction_to_be_executed = pull_resistor_1_node[4] ? microinstruction_list_for_add_value_to_b_register_1_fifth_microinstructions : 32'bz;  // Controlled_Buffer controlled_buffer_6
  assign microinstruction_to_be_executed = pull_resistor_1_node[5] ? microinstruction_list_for_add_value_to_b_register_1_sixth_microinstructions : 32'bz;  // Controlled_Buffer controlled_buffer_7
  assign microinstruction_to_be_executed = pull_resistor_1_node[6] ? microinstruction_list_for_add_value_to_b_register_1_seventh_microinstructions : 32'bz;  // Controlled_Buffer controlled_buffer_8
endmodule

module microinstruction_list_for_add_value_to_b_register (
  output [31:0] first_microinstructions,
  output [31:0] third_microinstructions,
  output [31:0] fifth_microinstructions,
  output [31:0] seventh_microinstructions,
  output [31:0] second_microinstructions,
  output [31:0] fourth_microinstructions,
  output [31:0] sixth_microinstructions
);

  Pull_Resistor #(.pull(1)) pull_resistor_1 (.node(first_microinstructions[4]));
  Pull_Resistor #(.pull(1)) pull_resistor_2 (.node(second_microinstructions[20]));
  Pull_Resistor pull_resistor_3 (.node(fifth_microinstructions[31]));
  Pull_Resistor #(.pull(1)) pull_resistor_4 (.node(third_microinstructions[8]));
  Pull_Resistor #(.pull(1)) pull_resistor_5 (.node(fifth_microinstructions[25]));

  assign {fifth_microinstructions[30:26], fifth_microinstructions[24:0]} = {{18{fifth_microinstructions[31]}}, fifth_microinstructions[25], {4{fifth_microinstructions[31]}}, fifth_microinstructions[25], {6{fifth_microinstructions[31]}}};
  assign {first_microinstructions[31:5], first_microinstructions[3:0]} = {31{fifth_microinstructions[31]}};
  assign fourth_microinstructions = {{8{fifth_microinstructions[31]}}, fifth_microinstructions[25], {12{fifth_microinstructions[31]}}, fifth_microinstructions[25], {10{fifth_microinstructions[31]}}};
  assign {second_microinstructions[31:21], second_microinstructions[19:0]} = {{11{fifth_microinstructions[31]}}, second_microinstructions[20], {6{fifth_microinstructions[31]}}, second_microinstructions[20], {6{fifth_microinstructions[31]}}, second_microinstructions[20], {5{fifth_microinstructions[31]}}};
  assign seventh_microinstructions = {32{fifth_microinstructions[31]}};
  assign sixth_microinstructions = {32{fifth_microinstructions[31]}};
  assign {third_microinstructions[31:9], third_microinstructions[7:0]} = {{23{fifth_microinstructions[31]}}, third_microinstructions[8], {7{fifth_microinstructions[31]}}};
endmodule

module microinstruction_decoder_for_test_value_with_b_register (
  input  [6:0] current_microinstruction,
  input  chip_select,
  output [31:0] microinstruction_to_be_executed
);

  wire [6:0] pull_resistor_1_node;
  wire [31:0] microinstruction_list_for_test_value_with_b_register_1_fifth_microinstructions,
       microinstruction_list_for_test_value_with_b_register_1_first_microinstructions,
       microinstruction_list_for_test_value_with_b_register_1_fourth_microinstructions,
       microinstruction_list_for_test_value_with_b_register_1_second_microinstructions,
       microinstruction_list_for_test_value_with_b_register_1_seventh_microinstructions,
       microinstruction_list_for_test_value_with_b_register_1_sixth_microinstructions,
       microinstruction_list_for_test_value_with_b_register_1_third_microinstructions;

  Pull_Resistor pull_resistor_1 (.node(pull_resistor_1_node));
  assign pull_resistor_1_node = chip_select ? current_microinstruction : 7'bz;  // Controlled_Buffer controlled_buffer_1
  microinstruction_list_for_test_value_with_b_register microinstruction_list_for_test_value_with_b_register_1 (
    .first_microinstructions(microinstruction_list_for_test_value_with_b_register_1_first_microinstructions),
    .third_microinstructions(microinstruction_list_for_test_value_with_b_register_1_third_microinstructions),
    .fifth_microinstructions(microinstruction_list_for_test_value_with_b_register_1_fifth_microinstructions),
    .seventh_microinstructions(microinstruction_list_for_test_value_with_b_register_1_seventh_microinstructions),
    .second_microinstructions(microinstruction_list_for_test_value_with_b_register_1_second_microinstructions),
    .fourth_microinstructions(microinstruction_list_for_test_value_with_b_register_1_fourth_microinstructions),
    .sixth_microinstructions(microinstruction_list_for_test_value_with_b_register_1_sixth_microinstructions));
  Pull_Resistor pull_resistor_2 (.node(microinstruction_list_for_test_value_with_b_register_1_second_microinstructions));
  Pull_Resistor pull_resistor_3 (.node(microinstruction_list_for_test_value_with_b_register_1_sixth_microinstructions));
  Pull_Resistor pull_resistor_4 (.node(microinstruction_list_for_test_value_with_b_register_1_third_microinstructions));
  Pull_Resistor pull_resistor_5 (.node(microinstruction_list_for_test_value_with_b_register_1_fifth_microinstructions));
  Pull_Resistor pull_resistor_6 (.node(microinstruction_list_for_test_value_with_b_register_1_first_microinstructions));
  Pull_Resistor pull_resistor_7 (.node(microinstruction_list_for_test_value_with_b_register_1_seventh_microinstructions));
  Pull_Resistor pull_resistor_8 (.node(microinstruction_list_for_test_value_with_b_register_1_fourth_microinstructions));
  assign microinstruction_to_be_executed = pull_resistor_1_node[0] ? microinstruction_list_for_test_value_with_b_register_1_second_microinstructions : 32'bz;  // Controlled_Buffer controlled_buffer_2
  assign microinstruction_to_be_executed = pull_resistor_1_node[1] ? microinstruction_list_for_test_value_with_b_register_1_first_microinstructions : 32'bz;  // Controlled_Buffer controlled_buffer_3
  assign microinstruction_to_be_executed = pull_resistor_1_node[2] ? microinstruction_list_for_test_value_with_b_register_1_third_microinstructions : 32'bz;  // Controlled_Buffer controlled_buffer_4
  assign microinstruction_to_be_executed = pull_resistor_1_node[3] ? microinstruction_list_for_test_value_with_b_register_1_fourth_microinstructions : 32'bz;  // Controlled_Buffer controlled_buffer_5
  assign microinstruction_to_be_executed = pull_resistor_1_node[4] ? microinstruction_list_for_test_value_with_b_register_1_fifth_microinstructions : 32'bz;  // Controlled_Buffer controlled_buffer_6
  assign microinstruction_to_be_executed = pull_resistor_1_node[5] ? microinstruction_list_for_test_value_with_b_register_1_sixth_microinstructions : 32'bz;  // Controlled_Buffer controlled_buffer_7
  assign microinstruction_to_be_executed = pull_resistor_1_node[6] ? microinstruction_list_for_test_value_with_b_register_1_seventh_microinstructions : 32'bz;  // Controlled_Buffer controlled_buffer_8
endmodule

module microinstruction_list_for_test_value_with_b_register (
  output [31:0] first_microinstructions,
  output [31:0] third_microinstructions,
  output [31:0] fifth_microinstructions,
  output [31:0] seventh_microinstructions,
  output [31:0] second_microinstructions,
  output [31:0] fourth_microinstructions,
  output [31:0] sixth_microinstructions
);

  Pull_Resistor #(.pull(1)) pull_resistor_1 (.node(first_microinstructions[4]));
  Pull_Resistor #(.pull(1)) pull_resistor_2 (.node(second_microinstructions[20]));
  Pull_Resistor pull_resistor_3 (.node(fifth_microinstructions[31]));
  Pull_Resistor #(.pull(1)) pull_resistor_4 (.node(third_microinstructions[8]));
  Pull_Resistor #(.pull(1)) pull_resistor_5 (.node(fifth_microinstructions[25]));

  assign {fifth_microinstructions[30:26], fifth_microinstructions[24:0]} = {{18{fifth_microinstructions[31]}}, fifth_microinstructions[25], fifth_microinstructions[31], fifth_microinstructions[25], {9{fifth_microinstructions[31]}}};
  assign {first_microinstructions[31:5], first_microinstructions[3:0]} = {31{fifth_microinstructions[31]}};
  assign fourth_microinstructions = {{8{fifth_microinstructions[31]}}, fifth_microinstructions[25], {12{fifth_microinstructions[31]}}, fifth_microinstructions[25], {10{fifth_microinstructions[31]}}};
  assign {second_microinstructions[31:21], second_microinstructions[19:0]} = {{11{fifth_microinstructions[31]}}, second_microinstructions[20], {6{fifth_microinstructions[31]}}, second_microinstructions[20], {6{fifth_microinstructions[31]}}, second_microinstructions[20], {5{fifth_microinstructions[31]}}};
  assign seventh_microinstructions = {32{fifth_microinstructions[31]}};
  assign sixth_microinstructions = {32{fifth_microinstructions[31]}};
  assign {third_microinstructions[31:9], third_microinstructions[7:0]} = {{23{fifth_microinstructions[31]}}, third_microinstructions[8], {7{fifth_microinstructions[31]}}};
endmodule

module microinstruction_decoder_for_write_b_register_to_memory (
  input  [6:0] current_microinstruction,
  input  chip_select,
  output [31:0] microinstruction_to_be_executed
);

  wire [6:0] pull_resistor_1_node;
  wire [31:0] microinstruction_list_for_write_b_register_to_memory_1_fifth_microinstructions,
       microinstruction_list_for_write_b_register_to_memory_1_first_microinstructions,
       microinstruction_list_for_write_b_register_to_memory_1_fourth_microinstructions,
       microinstruction_list_for_write_b_register_to_memory_1_second_microinstructions,
       microinstruction_list_for_write_b_register_to_memory_1_seventh_microinstructions,
       microinstruction_list_for_write_b_register_to_memory_1_sixth_microinstructions,
       microinstruction_list_for_write_b_register_to_memory_1_third_microinstructions;

  Pull_Resistor pull_resistor_1 (.node(pull_resistor_1_node));
  microinstruction_list_for_write_b_register_to_memory microinstruction_list_for_write_b_register_to_memory_1 (
    .first_microinstructions(microinstruction_list_for_write_b_register_to_memory_1_first_microinstructions),
    .third_microinstructions(microinstruction_list_for_write_b_register_to_memory_1_third_microinstructions),
    .fifth_microinstructions(microinstruction_list_for_write_b_register_to_memory_1_fifth_microinstructions),
    .seventh_microinstructions(microinstruction_list_for_write_b_register_to_memory_1_seventh_microinstructions),
    .second_microinstructions(microinstruction_list_for_write_b_register_to_memory_1_second_microinstructions),
    .fourth_microinstructions(microinstruction_list_for_write_b_register_to_memory_1_fourth_microinstructions),
    .sixth_microinstructions(microinstruction_list_for_write_b_register_to_memory_1_sixth_microinstructions));
  assign pull_resistor_1_node = chip_select ? current_microinstruction : 7'bz;  // Controlled_Buffer controlled_buffer_1
  Pull_Resistor pull_resistor_2 (.node(microinstruction_list_for_write_b_register_to_memory_1_second_microinstructions));
  Pull_Resistor pull_resistor_3 (.node(microinstruction_list_for_write_b_register_to_memory_1_third_microinstructions));
  Pull_Resistor pull_resistor_4 (.node(microinstruction_list_for_write_b_register_to_memory_1_fifth_microinstructions));
  Pull_Resistor pull_resistor_5 (.node(microinstruction_list_for_write_b_register_to_memory_1_first_microinstructions));
  Pull_Resistor pull_resistor_6 (.node(microinstruction_list_for_write_b_register_to_memory_1_sixth_microinstructions));
  Pull_Resistor pull_resistor_7 (.node(microinstruction_list_for_write_b_register_to_memory_1_seventh_microinstructions));
  Pull_Resistor pull_resistor_8 (.node(microinstruction_list_for_write_b_register_to_memory_1_seventh_microinstructions));
  Pull_Resistor pull_resistor_9 (.node(microinstruction_list_for_write_b_register_to_memory_1_fourth_microinstructions));
  assign microinstruction_to_be_executed = pull_resistor_1_node[0] ? microinstruction_list_for_write_b_register_to_memory_1_second_microinstructions : 32'bz;  // Controlled_Buffer controlled_buffer_2
  assign microinstruction_to_be_executed = pull_resistor_1_node[1] ? microinstruction_list_for_write_b_register_to_memory_1_first_microinstructions : 32'bz;  // Controlled_Buffer controlled_buffer_3
  assign microinstruction_to_be_executed = pull_resistor_1_node[2] ? microinstruction_list_for_write_b_register_to_memory_1_third_microinstructions : 32'bz;  // Controlled_Buffer controlled_buffer_4
  assign microinstruction_to_be_executed = pull_resistor_1_node[3] ? microinstruction_list_for_write_b_register_to_memory_1_fourth_microinstructions : 32'bz;  // Controlled_Buffer controlled_buffer_5
  assign microinstruction_to_be_executed = pull_resistor_1_node[4] ? microinstruction_list_for_write_b_register_to_memory_1_fifth_microinstructions : 32'bz;  // Controlled_Buffer controlled_buffer_6
  assign microinstruction_to_be_executed = pull_resistor_1_node[5] ? microinstruction_list_for_write_b_register_to_memory_1_sixth_microinstructions : 32'bz;  // Controlled_Buffer controlled_buffer_7
  assign microinstruction_to_be_executed = pull_resistor_1_node[6] ? microinstruction_list_for_write_b_register_to_memory_1_seventh_microinstructions : 32'bz;  // Controlled_Buffer controlled_buffer_8
endmodule

module microinstruction_list_for_write_b_register_to_memory (
  output [31:0] first_microinstructions,
  output [31:0] third_microinstructions,
  output [31:0] fifth_microinstructions,
  output [31:0] seventh_microinstructions,
  output [31:0] second_microinstructions,
  output [31:0] fourth_microinstructions,
  output [31:0] sixth_microinstructions
);

  Pull_Resistor pull_resistor_1 (.node(fifth_microinstructions[31]));
  Pull_Resistor #(.pull(1)) pull_resistor_2 (.node(first_microinstructions[4]));

  assign fifth_microinstructions[30:0] = {31{fifth_microinstructions[31]}};
  assign {first_microinstructions[31:5], first_microinstructions[3:0]} = {31{fifth_microinstructions[31]}};
  assign fourth_microinstructions = {32{fifth_microinstructions[31]}};
  assign second_microinstructions = {{11{fifth_microinstructions[31]}}, {2{first_microinstructions[4]}}, {6{fifth_microinstructions[31]}}, first_microinstructions[4], {6{fifth_microinstructions[31]}}, first_microinstructions[4], {5{fifth_microinstructions[31]}}};
  assign seventh_microinstructions = {32{fifth_microinstructions[31]}};
  assign sixth_microinstructions = {32{fifth_microinstructions[31]}};
  assign third_microinstructions = {{9{fifth_microinstructions[31]}}, {2{first_microinstructions[4]}}, {13{fifth_microinstructions[31]}}, first_microinstructions[4], {7{fifth_microinstructions[31]}}};
endmodule

module microinstruction_decoder_for_add_register_b_to_register_a_and_store_in_a (
  input  [6:0] current_microinstruction,
  input  chip_select,
  output [31:0] microinstruction_to_be_executed
);

  wire [6:0] pull_resistor_1_node;
  wire [31:0] microinstruction_list_for_add_register_b_to_reg_a_and_store_in_a_1_fifth_microinstructions,
       microinstruction_list_for_add_register_b_to_reg_a_and_store_in_a_1_first_microinstructions,
       microinstruction_list_for_add_register_b_to_reg_a_and_store_in_a_1_fourth_microinstructions,
       microinstruction_list_for_add_register_b_to_reg_a_and_store_in_a_1_second_microinstructions,
       microinstruction_list_for_add_register_b_to_reg_a_and_store_in_a_1_seventh_microinstructions,
       microinstruction_list_for_add_register_b_to_reg_a_and_store_in_a_1_sixth_microinstructions,
       microinstruction_list_for_add_register_b_to_reg_a_and_store_in_a_1_third_microinstructions;

  Pull_Resistor pull_resistor_1 (.node(pull_resistor_1_node));
  microinstruction_list_for_add_register_b_to_reg_a_and_store_in_a microinstruction_list_for_add_register_b_to_reg_a_and_store_in_a_1 (
    .first_microinstructions(microinstruction_list_for_add_register_b_to_reg_a_and_store_in_a_1_first_microinstructions),
    .third_microinstructions(microinstruction_list_for_add_register_b_to_reg_a_and_store_in_a_1_third_microinstructions),
    .fifth_microinstructions(microinstruction_list_for_add_register_b_to_reg_a_and_store_in_a_1_fifth_microinstructions),
    .seventh_microinstructions(microinstruction_list_for_add_register_b_to_reg_a_and_store_in_a_1_seventh_microinstructions),
    .second_microinstructions(microinstruction_list_for_add_register_b_to_reg_a_and_store_in_a_1_second_microinstructions),
    .fourth_microinstructions(microinstruction_list_for_add_register_b_to_reg_a_and_store_in_a_1_fourth_microinstructions),
    .sixth_microinstructions(microinstruction_list_for_add_register_b_to_reg_a_and_store_in_a_1_sixth_microinstructions));
  assign pull_resistor_1_node = chip_select ? current_microinstruction : 7'bz;  // Controlled_Buffer controlled_buffer_1
  Pull_Resistor pull_resistor_2 (.node(microinstruction_list_for_add_register_b_to_reg_a_and_store_in_a_1_second_microinstructions));
  Pull_Resistor pull_resistor_3 (.node(microinstruction_list_for_add_register_b_to_reg_a_and_store_in_a_1_third_microinstructions));
  Pull_Resistor pull_resistor_4 (.node(microinstruction_list_for_add_register_b_to_reg_a_and_store_in_a_1_fifth_microinstructions));
  Pull_Resistor pull_resistor_5 (.node(microinstruction_list_for_add_register_b_to_reg_a_and_store_in_a_1_first_microinstructions));
  Pull_Resistor pull_resistor_6 (.node(microinstruction_list_for_add_register_b_to_reg_a_and_store_in_a_1_sixth_microinstructions));
  Pull_Resistor pull_resistor_7 (.node(microinstruction_list_for_add_register_b_to_reg_a_and_store_in_a_1_seventh_microinstructions));
  Pull_Resistor pull_resistor_8 (.node(microinstruction_list_for_add_register_b_to_reg_a_and_store_in_a_1_seventh_microinstructions));
  Pull_Resistor pull_resistor_9 (.node(microinstruction_list_for_add_register_b_to_reg_a_and_store_in_a_1_fourth_microinstructions));
  assign microinstruction_to_be_executed = pull_resistor_1_node[0] ? microinstruction_list_for_add_register_b_to_reg_a_and_store_in_a_1_second_microinstructions : 32'bz;  // Controlled_Buffer controlled_buffer_2
  assign microinstruction_to_be_executed = pull_resistor_1_node[1] ? microinstruction_list_for_add_register_b_to_reg_a_and_store_in_a_1_first_microinstructions : 32'bz;  // Controlled_Buffer controlled_buffer_3
  assign microinstruction_to_be_executed = pull_resistor_1_node[2] ? microinstruction_list_for_add_register_b_to_reg_a_and_store_in_a_1_third_microinstructions : 32'bz;  // Controlled_Buffer controlled_buffer_4
  assign microinstruction_to_be_executed = pull_resistor_1_node[3] ? microinstruction_list_for_add_register_b_to_reg_a_and_store_in_a_1_fourth_microinstructions : 32'bz;  // Controlled_Buffer controlled_buffer_5
  assign microinstruction_to_be_executed = pull_resistor_1_node[4] ? microinstruction_list_for_add_register_b_to_reg_a_and_store_in_a_1_fifth_microinstructions : 32'bz;  // Controlled_Buffer controlled_buffer_6
  assign microinstruction_to_be_executed = pull_resistor_1_node[5] ? microinstruction_list_for_add_register_b_to_reg_a_and_store_in_a_1_sixth_microinstructions : 32'bz;  // Controlled_Buffer controlled_buffer_7
  assign microinstruction_to_be_executed = pull_resistor_1_node[6] ? microinstruction_list_for_add_register_b_to_reg_a_and_store_in_a_1_seventh_microinstructions : 32'bz;  // Controlled_Buffer controlled_buffer_8
endmodule

module microinstruction_list_for_add_register_b_to_reg_a_and_store_in_a (
  output [31:0] first_microinstructions,
  output [31:0] third_microinstructions,
  output [31:0] fifth_microinstructions,
  output [31:0] seventh_microinstructions,
  output [31:0] second_microinstructions,
  output [31:0] fourth_microinstructions,
  output [31:0] sixth_microinstructions
);

  Pull_Resistor #(.pull(1)) pull_resistor_1 (.node(second_microinstructions[20]));
  Pull_Resistor #(.pull(1)) pull_resistor_2 (.node(first_microinstructions[4]));
  Pull_Resistor pull_resistor_3 (.node(fifth_microinstructions[31]));
  Pull_Resistor #(.pull(1)) pull_resistor_4 (.node(third_microinstructions[8]));
  Pull_Resistor #(.pull(1)) pull_resistor_5 (.node(fifth_microinstructions[25]));

  assign {fifth_microinstructions[30:26], fifth_microinstructions[24:0]} = {{18{fifth_microinstructions[31]}}, fifth_microinstructions[25], {9{fifth_microinstructions[31]}}, fifth_microinstructions[25], fifth_microinstructions[31]};
  assign {first_microinstructions[31:5], first_microinstructions[3:0]} = {31{fifth_microinstructions[31]}};
  assign fourth_microinstructions = {{21{fifth_microinstructions[31]}}, fifth_microinstructions[25], {2{fifth_microinstructions[31]}}, fifth_microinstructions[25], {7{fifth_microinstructions[31]}}};
  assign {second_microinstructions[31:21], second_microinstructions[19:0]} = {{11{fifth_microinstructions[31]}}, second_microinstructions[20], {6{fifth_microinstructions[31]}}, second_microinstructions[20], {6{fifth_microinstructions[31]}}, second_microinstructions[20], {5{fifth_microinstructions[31]}}};
  assign seventh_microinstructions = {32{fifth_microinstructions[31]}};
  assign sixth_microinstructions = {32{fifth_microinstructions[31]}};
  assign {third_microinstructions[31:9], third_microinstructions[7:0]} = {{27{fifth_microinstructions[31]}}, third_microinstructions[8], {3{fifth_microinstructions[31]}}};
endmodule

module Stack_pointer (
  input  write_enable__pop_or_push_or_manual_value,
  input  clock,
  input  push,
  input  pop,
  input  output_enable,
  input  [31:0] lower_part_of_manual_input,
  input  manual_value,
  input  [31:0] higher_part_of_manual_input,
  output [31:0] lower_part_of_output,
  output [31:0] higher_part_of_output
);

  wire [31:0] controlled_buffer_1_out, controlled_buffer_2_out,
       n64_bit_adder_with_control_signals_1_lower_32_bits,
       n64_bit_adder_with_control_signals_1_upper_32_bits,
       n64_bit_adder_with_control_signals_2_lower_32_bits,
       n64_bit_adder_with_control_signals_2_upper_32_bits, n64_bit_register_1_higher_32_bits_of_output,
       n64_bit_register_1_lower_32_bits_of_output;

  _64_bit_adder_with_control_signals u_64_bit_adder_with_control_signals_1 (
    .lower_32_bit_of_input_a(n64_bit_register_1_lower_32_bits_of_output), .overflow_output_enable(1'b0),
    .higher_32_bit_of_input_a(n64_bit_register_1_higher_32_bits_of_output), .lower_32_bit_of_input_b(32'h1),
    .higher_32_bit_of_input_b({32{1'b0}}), .subtract(1'b0), .output_enable_the_64_bits(pop),
    .lower_32_bits(n64_bit_adder_with_control_signals_1_lower_32_bits),
    .upper_32_bits(n64_bit_adder_with_control_signals_1_upper_32_bits));  // open: overflow
  assign controlled_buffer_1_out = manual_value ? higher_part_of_manual_input : 32'bz;  // Controlled_Buffer controlled_buffer_1
  assign controlled_buffer_2_out = pop ? n64_bit_adder_with_control_signals_1_lower_32_bits : 32'bz;  // Controlled_Buffer controlled_buffer_2
  assign controlled_buffer_1_out = pop ? n64_bit_adder_with_control_signals_1_upper_32_bits : 32'bz;  // Controlled_Buffer controlled_buffer_3
  assign controlled_buffer_2_out = manual_value ? lower_part_of_manual_input : 32'bz;  // Controlled_Buffer controlled_buffer_4
  _64_bit_register u_64_bit_register_1 (
    .lower_32_bits_of_input(controlled_buffer_2_out), .higher_32_bits_of_input(controlled_buffer_1_out),
    .write_enable(write_enable__pop_or_push_or_manual_value), .clock(clock), .output_enable(1'b1),
    .higher_32_bits_of_output(n64_bit_register_1_higher_32_bits_of_output),
    .lower_32_bits_of_output(n64_bit_register_1_lower_32_bits_of_output));
  assign lower_part_of_output = output_enable ? n64_bit_register_1_lower_32_bits_of_output : 32'bz;  // Controlled_Buffer controlled_buffer_5
  assign higher_part_of_output = output_enable ? n64_bit_register_1_higher_32_bits_of_output : 32'bz;  // Controlled_Buffer controlled_buffer_6
  _64_bit_adder_with_control_signals u_64_bit_adder_with_control_signals_2 (
    .lower_32_bit_of_input_a(n64_bit_register_1_lower_32_bits_of_output), .overflow_output_enable(1'b0),
    .higher_32_bit_of_input_a(n64_bit_register_1_higher_32_bits_of_output), .lower_32_bit_of_input_b(32'h1),
    .higher_32_bit_of_input_b({32{1'b0}}), .subtract(1'b1), .output_enable_the_64_bits(push),
    .lower_32_bits(n64_bit_adder_with_control_signals_2_lower_32_bits),
    .upper_32_bits(n64_bit_adder_with_control_signals_2_upper_32_bits));  // open: overflow
  assign controlled_buffer_2_out = push ? n64_bit_adder_with_control_signals_2_lower_32_bits : 32'bz;  // Controlled_Buffer controlled_buffer_7
  assign controlled_buffer_1_out = push ? n64_bit_adder_with_control_signals_2_upper_32_bits : 32'bz;  // Controlled_Buffer controlled_buffer_8
endmodule

module control_signal_decoder_for_pop_rip__ret (
  input  [6:0] current_microinstruction,
  input  chip_select,
  output [31:0] microinstruction_to_be_executed,
  output [31:0] microinstruction_to_be_executed__upper
);

  wire [6:0] pull_resistor_1_node;
  wire [31:0] microinstruction_list_for_ret_pop_rip_1_fifth_microinstructions,
       microinstruction_list_for_ret_pop_rip_1_first_microinstructions,
       microinstruction_list_for_ret_pop_rip_1_fourth_microinstructions,
       microinstruction_list_for_ret_pop_rip_1_fourth_microinstructions__upper,
       microinstruction_list_for_ret_pop_rip_1_second_microinstructions,
       microinstruction_list_for_ret_pop_rip_1_seventh_microinstructions,
       microinstruction_list_for_ret_pop_rip_1_sixth_microinstructions,
       microinstruction_list_for_ret_pop_rip_1_third_microinstructions,
       microinstruction_list_for_ret_pop_rip_1_third_microinstructions__upper;

  Pull_Resistor pull_resistor_1 (.node(pull_resistor_1_node));
  microinstruction_list_for_ret__pop_rip microinstruction_list_for_ret_pop_rip_1 (
    .first_microinstructions(microinstruction_list_for_ret_pop_rip_1_first_microinstructions),
    .third_microinstructions(microinstruction_list_for_ret_pop_rip_1_third_microinstructions),
    .fifth_microinstructions(microinstruction_list_for_ret_pop_rip_1_fifth_microinstructions),
    .seventh_microinstructions(microinstruction_list_for_ret_pop_rip_1_seventh_microinstructions),
    .fourth_microinstructions__upper(microinstruction_list_for_ret_pop_rip_1_fourth_microinstructions__upper),
    .second_microinstructions(microinstruction_list_for_ret_pop_rip_1_second_microinstructions),
    .fourth_microinstructions(microinstruction_list_for_ret_pop_rip_1_fourth_microinstructions),
    .sixth_microinstructions(microinstruction_list_for_ret_pop_rip_1_sixth_microinstructions),
    .third_microinstructions__upper(microinstruction_list_for_ret_pop_rip_1_third_microinstructions__upper));
  assign pull_resistor_1_node = chip_select ? current_microinstruction : 7'bz;  // Controlled_Buffer controlled_buffer_1
  Pull_Resistor pull_resistor_2 (.node(microinstruction_list_for_ret_pop_rip_1_first_microinstructions));
  Pull_Resistor pull_resistor_3 (.node(microinstruction_list_for_ret_pop_rip_1_sixth_microinstructions));
  Pull_Resistor pull_resistor_4 (.node(microinstruction_list_for_ret_pop_rip_1_third_microinstructions));
  Pull_Resistor pull_resistor_5 (.node(microinstruction_list_for_ret_pop_rip_1_fifth_microinstructions));
  Pull_Resistor pull_resistor_6 (.node(microinstruction_list_for_ret_pop_rip_1_second_microinstructions));
  Pull_Resistor pull_resistor_7 (.node(microinstruction_list_for_ret_pop_rip_1_seventh_microinstructions));
  Pull_Resistor pull_resistor_8 (.node(microinstruction_list_for_ret_pop_rip_1_fourth_microinstructions));
  assign microinstruction_to_be_executed = pull_resistor_1_node[0] ? microinstruction_list_for_ret_pop_rip_1_first_microinstructions : 32'bz;  // Controlled_Buffer controlled_buffer_2
  assign microinstruction_to_be_executed = pull_resistor_1_node[1] ? microinstruction_list_for_ret_pop_rip_1_second_microinstructions : 32'bz;  // Controlled_Buffer controlled_buffer_3
  assign microinstruction_to_be_executed = pull_resistor_1_node[2] ? microinstruction_list_for_ret_pop_rip_1_third_microinstructions : 32'bz;  // Controlled_Buffer controlled_buffer_4
  assign microinstruction_to_be_executed = pull_resistor_1_node[3] ? microinstruction_list_for_ret_pop_rip_1_fourth_microinstructions : 32'bz;  // Controlled_Buffer controlled_buffer_5
  assign microinstruction_to_be_executed = pull_resistor_1_node[4] ? microinstruction_list_for_ret_pop_rip_1_fifth_microinstructions : 32'bz;  // Controlled_Buffer controlled_buffer_6
  assign microinstruction_to_be_executed = pull_resistor_1_node[5] ? microinstruction_list_for_ret_pop_rip_1_sixth_microinstructions : 32'bz;  // Controlled_Buffer controlled_buffer_7
  assign microinstruction_to_be_executed = pull_resistor_1_node[6] ? microinstruction_list_for_ret_pop_rip_1_seventh_microinstructions : 32'bz;  // Controlled_Buffer controlled_buffer_8
  assign microinstruction_to_be_executed__upper = pull_resistor_1_node[2] ? microinstruction_list_for_ret_pop_rip_1_third_microinstructions__upper : 32'bz;  // Controlled_Buffer controlled_buffer_9
  assign microinstruction_to_be_executed__upper = pull_resistor_1_node[3] ? microinstruction_list_for_ret_pop_rip_1_fourth_microinstructions__upper : 32'bz;  // Controlled_Buffer controlled_buffer_10
endmodule

module microinstruction_list_for_ret__pop_rip (
  output [31:0] first_microinstructions,
  output [31:0] third_microinstructions,
  output [31:0] fifth_microinstructions,
  output [31:0] seventh_microinstructions,
  output [31:0] fourth_microinstructions__upper,
  output [31:0] second_microinstructions,
  output [31:0] fourth_microinstructions,
  output [31:0] sixth_microinstructions,
  output [31:0] third_microinstructions__upper
);

  Pull_Resistor pull_resistor_1 (.node(fifth_microinstructions[31]));
  Pull_Resistor #(.pull(1)) pull_resistor_2 (.node(fifth_microinstructions[28]));

  assign {fifth_microinstructions[30:29], fifth_microinstructions[27:0]} = {{3{fifth_microinstructions[31]}}, fifth_microinstructions[28], {26{fifth_microinstructions[31]}}};
  assign first_microinstructions = {{11{fifth_microinstructions[31]}}, {2{fifth_microinstructions[28]}}, {6{fifth_microinstructions[31]}}, fifth_microinstructions[28], {6{fifth_microinstructions[31]}}, fifth_microinstructions[28], {5{fifth_microinstructions[31]}}};
  assign fourth_microinstructions = {{27{fifth_microinstructions[31]}}, fifth_microinstructions[28], fifth_microinstructions[31], fifth_microinstructions[28], {2{fifth_microinstructions[31]}}};
  assign fourth_microinstructions__upper = {{29{fifth_microinstructions[31]}}, {2{fifth_microinstructions[28]}}, fifth_microinstructions[31]};
  assign second_microinstructions = {{27{fifth_microinstructions[31]}}, fifth_microinstructions[28], {4{fifth_microinstructions[31]}}};
  assign seventh_microinstructions = {32{fifth_microinstructions[31]}};
  assign sixth_microinstructions = {32{fifth_microinstructions[31]}};
  assign third_microinstructions = {fifth_microinstructions[28], {10{fifth_microinstructions[31]}}, {2{fifth_microinstructions[28]}}, {19{fifth_microinstructions[31]}}};
  assign third_microinstructions__upper = {{31{fifth_microinstructions[31]}}, fifth_microinstructions[28]};
endmodule

module control_signal_decoder_for_call (
  input  [6:0] current_microinstruction,
  input  chip_select,
  output [31:0] microinstruction_to_be_executed,
  output [31:0] microinstruction_to_be_executed__upper
);

  wire [6:0] pull_resistor_1_node;
  wire [31:0] microinstruction_list_for_call_1_fifth_microinstructions,
       microinstruction_list_for_call_1_first_microinstructions,
       microinstruction_list_for_call_1_fourth_microinstructions,
       microinstruction_list_for_call_1_fourth_microinstructions__upper,
       microinstruction_list_for_call_1_second_microinstructions,
       microinstruction_list_for_call_1_seventh_microinstructions,
       microinstruction_list_for_call_1_sixth_microinstructions,
       microinstruction_list_for_call_1_sixth_microinstructions__upper,
       microinstruction_list_for_call_1_third_microinstructions,
       microinstruction_list_for_call_1_third_microinstructions__upper;

  Pull_Resistor pull_resistor_1 (.node(pull_resistor_1_node));
  microinstruction_list_for_call microinstruction_list_for_call_1 (
    .first_microinstructions(microinstruction_list_for_call_1_first_microinstructions),
    .third_microinstructions(microinstruction_list_for_call_1_third_microinstructions),
    .fifth_microinstructions(microinstruction_list_for_call_1_fifth_microinstructions),
    .seventh_microinstructions(microinstruction_list_for_call_1_seventh_microinstructions),
    .second_microinstructions(microinstruction_list_for_call_1_second_microinstructions),
    .fourth_microinstructions(microinstruction_list_for_call_1_fourth_microinstructions),
    .fourth_microinstructions__upper(microinstruction_list_for_call_1_fourth_microinstructions__upper),
    .sixth_microinstructions(microinstruction_list_for_call_1_sixth_microinstructions),
    .third_microinstructions__upper(microinstruction_list_for_call_1_third_microinstructions__upper),
    .sixth_microinstructions__upper(microinstruction_list_for_call_1_sixth_microinstructions__upper));
  assign pull_resistor_1_node = chip_select ? current_microinstruction : 7'bz;  // Controlled_Buffer controlled_buffer_1
  Pull_Resistor pull_resistor_2 (.node(microinstruction_list_for_call_1_first_microinstructions));
  Pull_Resistor pull_resistor_3 (.node(microinstruction_list_for_call_1_sixth_microinstructions));
  Pull_Resistor pull_resistor_4 (.node(microinstruction_list_for_call_1_third_microinstructions));
  Pull_Resistor pull_resistor_5 (.node(microinstruction_list_for_call_1_fifth_microinstructions));
  Pull_Resistor pull_resistor_6 (.node(microinstruction_list_for_call_1_second_microinstructions));
  Pull_Resistor pull_resistor_7 (.node(microinstruction_list_for_call_1_seventh_microinstructions));
  Pull_Resistor pull_resistor_8 (.node(microinstruction_list_for_call_1_fourth_microinstructions));
  assign microinstruction_to_be_executed = pull_resistor_1_node[0] ? microinstruction_list_for_call_1_first_microinstructions : 32'bz;  // Controlled_Buffer controlled_buffer_2
  assign microinstruction_to_be_executed = pull_resistor_1_node[1] ? microinstruction_list_for_call_1_second_microinstructions : 32'bz;  // Controlled_Buffer controlled_buffer_3
  assign microinstruction_to_be_executed = pull_resistor_1_node[2] ? microinstruction_list_for_call_1_third_microinstructions : 32'bz;  // Controlled_Buffer controlled_buffer_4
  assign microinstruction_to_be_executed = pull_resistor_1_node[3] ? microinstruction_list_for_call_1_fourth_microinstructions : 32'bz;  // Controlled_Buffer controlled_buffer_5
  assign microinstruction_to_be_executed = pull_resistor_1_node[4] ? microinstruction_list_for_call_1_fifth_microinstructions : 32'bz;  // Controlled_Buffer controlled_buffer_6
  assign microinstruction_to_be_executed = pull_resistor_1_node[5] ? microinstruction_list_for_call_1_sixth_microinstructions : 32'bz;  // Controlled_Buffer controlled_buffer_7
  assign microinstruction_to_be_executed = pull_resistor_1_node[6] ? microinstruction_list_for_call_1_seventh_microinstructions : 32'bz;  // Controlled_Buffer controlled_buffer_8
  assign microinstruction_to_be_executed__upper = pull_resistor_1_node[2] ? microinstruction_list_for_call_1_third_microinstructions__upper : 32'bz;  // Controlled_Buffer controlled_buffer_9
  assign microinstruction_to_be_executed__upper = pull_resistor_1_node[3] ? microinstruction_list_for_call_1_fourth_microinstructions__upper : 32'bz;  // Controlled_Buffer controlled_buffer_10
  assign microinstruction_to_be_executed__upper = pull_resistor_1_node[5] ? microinstruction_list_for_call_1_sixth_microinstructions__upper : 32'bz;  // Controlled_Buffer controlled_buffer_11
endmodule
module microinstruction_list_for_call (
  output [31:0] first_microinstructions,
  output [31:0] third_microinstructions,
  output [31:0] fifth_microinstructions,
  output [31:0] seventh_microinstructions,
  output [31:0] second_microinstructions,
  output [31:0] fourth_microinstructions,
  output [31:0] fourth_microinstructions__upper,
  output [31:0] sixth_microinstructions,
  output [31:0] third_microinstructions__upper,
  output [31:0] sixth_microinstructions__upper
);

  Pull_Resistor pull_resistor_1 (.node(fifth_microinstructions[31]));
  Pull_Resistor #(.pull(1)) pull_resistor_2 (.node(fifth_microinstructions[27]));

  assign {fifth_microinstructions[30:28], fifth_microinstructions[26:0]} = {{3{fifth_microinstructions[31]}}, fifth_microinstructions[27], {26{fifth_microinstructions[31]}}};
  assign first_microinstructions = {{11{fifth_microinstructions[31]}}, {2{fifth_microinstructions[27]}}, {6{fifth_microinstructions[31]}}, fifth_microinstructions[27], {6{fifth_microinstructions[31]}}, fifth_microinstructions[27], {5{fifth_microinstructions[31]}}};
  assign fourth_microinstructions = {{20{fifth_microinstructions[31]}}, fifth_microinstructions[27], {11{fifth_microinstructions[31]}}};
  assign fourth_microinstructions__upper = {{31{fifth_microinstructions[31]}}, fifth_microinstructions[27]};
  assign second_microinstructions = {{27{fifth_microinstructions[31]}}, fifth_microinstructions[27], {4{fifth_microinstructions[31]}}};
  assign seventh_microinstructions = {{9{fifth_microinstructions[31]}}, fifth_microinstructions[27], {17{fifth_microinstructions[31]}}, fifth_microinstructions[27], fifth_microinstructions[31], fifth_microinstructions[27], {2{fifth_microinstructions[31]}}};
  assign sixth_microinstructions = {fifth_microinstructions[27], {9{fifth_microinstructions[31]}}, fifth_microinstructions[27], {21{fifth_microinstructions[31]}}};
  assign sixth_microinstructions__upper = {{30{fifth_microinstructions[31]}}, fifth_microinstructions[27], fifth_microinstructions[31]};
  assign third_microinstructions = {{23{fifth_microinstructions[31]}}, fifth_microinstructions[27], {2{fifth_microinstructions[31]}}, fifth_microinstructions[27], {5{fifth_microinstructions[31]}}};
  assign third_microinstructions__upper = {{27{fifth_microinstructions[31]}}, fifth_microinstructions[27], {4{fifth_microinstructions[31]}}};
endmodule

module microinstruction_decoder_for_push_rbp (
  input  [6:0] current_microinstruction,
  input  chip_select,
  output [31:0] microinstruction_to_be_executed,
  output [31:0] microinstruction_to_be_executed__upper
);

  wire [6:0] pull_resistor_1_node;
  wire [31:0] microinstruction_list_for_push_rbp_1_fifth_microinstructions,
       microinstruction_list_for_push_rbp_1_first_microinstructions,
       microinstruction_list_for_push_rbp_1_fourth_microinstructions,
       microinstruction_list_for_push_rbp_1_fourth_microinstructions_upper,
       microinstruction_list_for_push_rbp_1_second_microinstructions,
       microinstruction_list_for_push_rbp_1_seventh_microinstructions,
       microinstruction_list_for_push_rbp_1_sixth_microinstructions,
       microinstruction_list_for_push_rbp_1_third_microinstructions,
       microinstruction_list_for_push_rbp_1_third_microinstructions__upper;

  Pull_Resistor pull_resistor_1 (.node(pull_resistor_1_node));
  microinstruction_list_for_push_rbp microinstruction_list_for_push_rbp_1 (
    .first_microinstructions(microinstruction_list_for_push_rbp_1_first_microinstructions),
    .third_microinstructions(microinstruction_list_for_push_rbp_1_third_microinstructions),
    .fifth_microinstructions(microinstruction_list_for_push_rbp_1_fifth_microinstructions),
    .seventh_microinstructions(microinstruction_list_for_push_rbp_1_seventh_microinstructions),
    .fourth_microinstructions_upper(microinstruction_list_for_push_rbp_1_fourth_microinstructions_upper),
    .second_microinstructions(microinstruction_list_for_push_rbp_1_second_microinstructions),
    .fourth_microinstructions(microinstruction_list_for_push_rbp_1_fourth_microinstructions),
    .sixth_microinstructions(microinstruction_list_for_push_rbp_1_sixth_microinstructions),
    .third_microinstructions__upper(microinstruction_list_for_push_rbp_1_third_microinstructions__upper));
  assign pull_resistor_1_node = chip_select ? current_microinstruction : 7'bz;  // Controlled_Buffer controlled_buffer_1
  Pull_Resistor pull_resistor_2 (.node(microinstruction_list_for_push_rbp_1_first_microinstructions));
  Pull_Resistor pull_resistor_3 (.node(microinstruction_list_for_push_rbp_1_sixth_microinstructions));
  Pull_Resistor pull_resistor_4 (.node(microinstruction_list_for_push_rbp_1_third_microinstructions));
  Pull_Resistor pull_resistor_5 (.node(microinstruction_list_for_push_rbp_1_fifth_microinstructions));
  Pull_Resistor pull_resistor_6 (.node(microinstruction_list_for_push_rbp_1_second_microinstructions));
  Pull_Resistor pull_resistor_7 (.node(microinstruction_list_for_push_rbp_1_seventh_microinstructions));
  Pull_Resistor pull_resistor_8 (.node(microinstruction_list_for_push_rbp_1_fourth_microinstructions));
  assign microinstruction_to_be_executed = pull_resistor_1_node[0] ? microinstruction_list_for_push_rbp_1_first_microinstructions : 32'bz;  // Controlled_Buffer controlled_buffer_2
  assign microinstruction_to_be_executed = pull_resistor_1_node[1] ? microinstruction_list_for_push_rbp_1_second_microinstructions : 32'bz;  // Controlled_Buffer controlled_buffer_3
  assign microinstruction_to_be_executed = pull_resistor_1_node[2] ? microinstruction_list_for_push_rbp_1_third_microinstructions : 32'bz;  // Controlled_Buffer controlled_buffer_4
  assign microinstruction_to_be_executed = pull_resistor_1_node[3] ? microinstruction_list_for_push_rbp_1_fourth_microinstructions : 32'bz;  // Controlled_Buffer controlled_buffer_5
  assign microinstruction_to_be_executed = pull_resistor_1_node[4] ? microinstruction_list_for_push_rbp_1_fifth_microinstructions : 32'bz;  // Controlled_Buffer controlled_buffer_6
  assign microinstruction_to_be_executed = pull_resistor_1_node[5] ? microinstruction_list_for_push_rbp_1_sixth_microinstructions : 32'bz;  // Controlled_Buffer controlled_buffer_7
  assign microinstruction_to_be_executed = pull_resistor_1_node[6] ? microinstruction_list_for_push_rbp_1_seventh_microinstructions : 32'bz;  // Controlled_Buffer controlled_buffer_8
  assign microinstruction_to_be_executed__upper = pull_resistor_1_node[2] ? microinstruction_list_for_push_rbp_1_third_microinstructions__upper : 32'bz;  // Controlled_Buffer controlled_buffer_9
  assign microinstruction_to_be_executed__upper = pull_resistor_1_node[3] ? microinstruction_list_for_push_rbp_1_fourth_microinstructions_upper : 32'bz;  // Controlled_Buffer controlled_buffer_10
endmodule

module microinstruction_list_for_push_rbp (
  output [31:0] first_microinstructions,
  output [31:0] third_microinstructions,
  output [31:0] fifth_microinstructions,
  output [31:0] seventh_microinstructions,
  output [31:0] fourth_microinstructions_upper,
  output [31:0] second_microinstructions,
  output [31:0] fourth_microinstructions,
  output [31:0] sixth_microinstructions,
  output [31:0] third_microinstructions__upper
);

  Pull_Resistor pull_resistor_1 (.node(fifth_microinstructions[31]));
  Pull_Resistor #(.pull(1)) pull_resistor_2 (.node(first_microinstructions[20]));

  assign fifth_microinstructions[30:0] = {31{fifth_microinstructions[31]}};
  assign {first_microinstructions[31:21], first_microinstructions[19:0]} = {{11{fifth_microinstructions[31]}}, first_microinstructions[20], {6{fifth_microinstructions[31]}}, first_microinstructions[20], {6{fifth_microinstructions[31]}}, first_microinstructions[20], {5{fifth_microinstructions[31]}}};
  assign fourth_microinstructions = {first_microinstructions[20], {9{fifth_microinstructions[31]}}, first_microinstructions[20], {21{fifth_microinstructions[31]}}};
  assign fourth_microinstructions_upper = {{23{fifth_microinstructions[31]}}, first_microinstructions[20], {8{fifth_microinstructions[31]}}};
  assign second_microinstructions = {{27{fifth_microinstructions[31]}}, first_microinstructions[20], {4{fifth_microinstructions[31]}}};
  assign seventh_microinstructions = {32{fifth_microinstructions[31]}};
  assign sixth_microinstructions = {32{fifth_microinstructions[31]}};
  assign third_microinstructions = {{4{fifth_microinstructions[31]}}, {2{first_microinstructions[20]}}, {26{fifth_microinstructions[31]}}};
  assign third_microinstructions__upper = {32{fifth_microinstructions[31]}};
endmodule

module microinstruction_list_for_mov_rsp__rbp (
  output [31:0] first_microinstructions,
  output [31:0] third_microinstructions,
  output [31:0] fifth_microinstructions,
  output [31:0] seventh_microinstructions,
  output [31:0] fourth_upper,
  output [31:0] second_microinstructions,
  output [31:0] fourth_microinstructions,
  output [31:0] sixth_microinstructions,
  output [31:0] third_microinstructions__upper
);

  Pull_Resistor pull_resistor_1 (.node(fifth_microinstructions[31]));
  Pull_Resistor #(.pull(1)) pull_resistor_2 (.node(first_microinstructions[20]));

  assign fifth_microinstructions[30:0] = {31{fifth_microinstructions[31]}};
  assign {first_microinstructions[31:21], first_microinstructions[19:0]} = {{11{fifth_microinstructions[31]}}, first_microinstructions[20], {6{fifth_microinstructions[31]}}, first_microinstructions[20], {6{fifth_microinstructions[31]}}, first_microinstructions[20], {5{fifth_microinstructions[31]}}};
  assign fourth_microinstructions = {32{fifth_microinstructions[31]}};
  assign fourth_upper = {32{fifth_microinstructions[31]}};
  assign second_microinstructions = {{27{fifth_microinstructions[31]}}, first_microinstructions[20], {4{fifth_microinstructions[31]}}};
  assign seventh_microinstructions = {32{fifth_microinstructions[31]}};
  assign sixth_microinstructions = {32{fifth_microinstructions[31]}};
  assign third_microinstructions = {{2{fifth_microinstructions[31]}}, first_microinstructions[20], {29{fifth_microinstructions[31]}}};
  assign third_microinstructions__upper = {{24{fifth_microinstructions[31]}}, first_microinstructions[20], {7{fifth_microinstructions[31]}}};
endmodule

module microinstruction_decoder_for_mov_rsp__rbp (
  input  [6:0] current_microinstruction,
  input  chip_select,
  output [31:0] microinstruction_to_be_executed,
  output [31:0] microinstruction_to_be_executed__upper
);

  wire [6:0] pull_resistor_1_node;
  wire [31:0] microinstruction_list_for_mov_rsp_rbp_1_fifth_microinstructions,
       microinstruction_list_for_mov_rsp_rbp_1_first_microinstructions,
       microinstruction_list_for_mov_rsp_rbp_1_fourth_microinstructions,
       microinstruction_list_for_mov_rsp_rbp_1_fourth_upper,
       microinstruction_list_for_mov_rsp_rbp_1_second_microinstructions,
       microinstruction_list_for_mov_rsp_rbp_1_seventh_microinstructions,
       microinstruction_list_for_mov_rsp_rbp_1_sixth_microinstructions,
       microinstruction_list_for_mov_rsp_rbp_1_third_microinstructions,
       microinstruction_list_for_mov_rsp_rbp_1_third_microinstructions__upper;

  Pull_Resistor pull_resistor_1 (.node(pull_resistor_1_node));
  microinstruction_list_for_mov_rsp__rbp microinstruction_list_for_mov_rsp_rbp_1 (
    .first_microinstructions(microinstruction_list_for_mov_rsp_rbp_1_first_microinstructions),
    .third_microinstructions(microinstruction_list_for_mov_rsp_rbp_1_third_microinstructions),
    .fifth_microinstructions(microinstruction_list_for_mov_rsp_rbp_1_fifth_microinstructions),
    .seventh_microinstructions(microinstruction_list_for_mov_rsp_rbp_1_seventh_microinstructions),
    .fourth_upper(microinstruction_list_for_mov_rsp_rbp_1_fourth_upper),
    .second_microinstructions(microinstruction_list_for_mov_rsp_rbp_1_second_microinstructions),
    .fourth_microinstructions(microinstruction_list_for_mov_rsp_rbp_1_fourth_microinstructions),
    .sixth_microinstructions(microinstruction_list_for_mov_rsp_rbp_1_sixth_microinstructions),
    .third_microinstructions__upper(microinstruction_list_for_mov_rsp_rbp_1_third_microinstructions__upper));
  assign pull_resistor_1_node = chip_select ? current_microinstruction : 7'bz;  // Controlled_Buffer controlled_buffer_1
  Pull_Resistor pull_resistor_2 (.node(microinstruction_list_for_mov_rsp_rbp_1_first_microinstructions));
  Pull_Resistor pull_resistor_3 (.node(microinstruction_list_for_mov_rsp_rbp_1_sixth_microinstructions));
  Pull_Resistor pull_resistor_4 (.node(microinstruction_list_for_mov_rsp_rbp_1_third_microinstructions));
  Pull_Resistor pull_resistor_5 (.node(microinstruction_list_for_mov_rsp_rbp_1_fifth_microinstructions));
  Pull_Resistor pull_resistor_6 (.node(microinstruction_list_for_mov_rsp_rbp_1_second_microinstructions));
  Pull_Resistor pull_resistor_7 (.node(microinstruction_list_for_mov_rsp_rbp_1_seventh_microinstructions));
  Pull_Resistor pull_resistor_8 (.node(microinstruction_list_for_mov_rsp_rbp_1_fourth_microinstructions));
  assign microinstruction_to_be_executed = pull_resistor_1_node[0] ? microinstruction_list_for_mov_rsp_rbp_1_first_microinstructions : 32'bz;  // Controlled_Buffer controlled_buffer_2
  assign microinstruction_to_be_executed = pull_resistor_1_node[1] ? microinstruction_list_for_mov_rsp_rbp_1_second_microinstructions : 32'bz;  // Controlled_Buffer controlled_buffer_3
  assign microinstruction_to_be_executed = pull_resistor_1_node[2] ? microinstruction_list_for_mov_rsp_rbp_1_third_microinstructions : 32'bz;  // Controlled_Buffer controlled_buffer_4
  assign microinstruction_to_be_executed = pull_resistor_1_node[3] ? microinstruction_list_for_mov_rsp_rbp_1_fourth_microinstructions : 32'bz;  // Controlled_Buffer controlled_buffer_5
  assign microinstruction_to_be_executed = pull_resistor_1_node[4] ? microinstruction_list_for_mov_rsp_rbp_1_fifth_microinstructions : 32'bz;  // Controlled_Buffer controlled_buffer_6
  assign microinstruction_to_be_executed = pull_resistor_1_node[5] ? microinstruction_list_for_mov_rsp_rbp_1_sixth_microinstructions : 32'bz;  // Controlled_Buffer controlled_buffer_7
  assign microinstruction_to_be_executed = pull_resistor_1_node[6] ? microinstruction_list_for_mov_rsp_rbp_1_seventh_microinstructions : 32'bz;  // Controlled_Buffer controlled_buffer_8
  assign microinstruction_to_be_executed__upper = pull_resistor_1_node[2] ? microinstruction_list_for_mov_rsp_rbp_1_third_microinstructions__upper : 32'bz;  // Controlled_Buffer controlled_buffer_9
  assign microinstruction_to_be_executed__upper = pull_resistor_1_node[3] ? microinstruction_list_for_mov_rsp_rbp_1_fourth_upper : 32'bz;  // Controlled_Buffer controlled_buffer_10
endmodule

module microinstruction_decoder_for_pop_rbp (
  input  [6:0] current_microinstruction,
  input  chip_select,
  output [31:0] microinstruction_to_be_executed,
  output [31:0] microinstruction_to_be_executed__upper
);

  wire [6:0] pull_resistor_1_node;
  wire [31:0] microinstruction_list_for_pop_rbp_1_fifth_microinstructions,
       microinstruction_list_for_pop_rbp_1_first_microinstructions,
       microinstruction_list_for_pop_rbp_1_fourth_microinstructions,
       microinstruction_list_for_pop_rbp_1_fourth_upper,
       microinstruction_list_for_pop_rbp_1_second_microinstructions,
       microinstruction_list_for_pop_rbp_1_seventh_microinstructions,
       microinstruction_list_for_pop_rbp_1_sixth_microinstructions,
       microinstruction_list_for_pop_rbp_1_third_microinstructions,
       microinstruction_list_for_pop_rbp_1_third_microinstructions__upper;

  Pull_Resistor pull_resistor_1 (.node(pull_resistor_1_node));
  microinstruction_list_for_pop_rbp microinstruction_list_for_pop_rbp_1 (
    .first_microinstructions(microinstruction_list_for_pop_rbp_1_first_microinstructions),
    .third_microinstructions(microinstruction_list_for_pop_rbp_1_third_microinstructions),
    .fifth_microinstructions(microinstruction_list_for_pop_rbp_1_fifth_microinstructions),
    .seventh_microinstructions(microinstruction_list_for_pop_rbp_1_seventh_microinstructions),
    .fourth_upper(microinstruction_list_for_pop_rbp_1_fourth_upper),
    .second_microinstructions(microinstruction_list_for_pop_rbp_1_second_microinstructions),
    .fourth_microinstructions(microinstruction_list_for_pop_rbp_1_fourth_microinstructions),
    .sixth_microinstructions(microinstruction_list_for_pop_rbp_1_sixth_microinstructions),
    .third_microinstructions__upper(microinstruction_list_for_pop_rbp_1_third_microinstructions__upper));
  assign pull_resistor_1_node = chip_select ? current_microinstruction : 7'bz;  // Controlled_Buffer controlled_buffer_1
  Pull_Resistor pull_resistor_2 (.node(microinstruction_list_for_pop_rbp_1_first_microinstructions));
  Pull_Resistor pull_resistor_3 (.node(microinstruction_list_for_pop_rbp_1_sixth_microinstructions));
  Pull_Resistor pull_resistor_4 (.node(microinstruction_list_for_pop_rbp_1_third_microinstructions));
  Pull_Resistor pull_resistor_5 (.node(microinstruction_list_for_pop_rbp_1_fifth_microinstructions));
  Pull_Resistor pull_resistor_6 (.node(microinstruction_list_for_pop_rbp_1_second_microinstructions));
  Pull_Resistor pull_resistor_7 (.node(microinstruction_list_for_pop_rbp_1_seventh_microinstructions));
  Pull_Resistor pull_resistor_8 (.node(microinstruction_list_for_pop_rbp_1_fourth_microinstructions));
  assign microinstruction_to_be_executed = pull_resistor_1_node[0] ? microinstruction_list_for_pop_rbp_1_first_microinstructions : 32'bz;  // Controlled_Buffer controlled_buffer_2
  assign microinstruction_to_be_executed = pull_resistor_1_node[1] ? microinstruction_list_for_pop_rbp_1_second_microinstructions : 32'bz;  // Controlled_Buffer controlled_buffer_3
  assign microinstruction_to_be_executed = pull_resistor_1_node[2] ? microinstruction_list_for_pop_rbp_1_third_microinstructions : 32'bz;  // Controlled_Buffer controlled_buffer_4
  assign microinstruction_to_be_executed = pull_resistor_1_node[3] ? microinstruction_list_for_pop_rbp_1_fourth_microinstructions : 32'bz;  // Controlled_Buffer controlled_buffer_5
  assign microinstruction_to_be_executed = pull_resistor_1_node[4] ? microinstruction_list_for_pop_rbp_1_fifth_microinstructions : 32'bz;  // Controlled_Buffer controlled_buffer_6
  assign microinstruction_to_be_executed = pull_resistor_1_node[5] ? microinstruction_list_for_pop_rbp_1_sixth_microinstructions : 32'bz;  // Controlled_Buffer controlled_buffer_7
  assign microinstruction_to_be_executed = pull_resistor_1_node[6] ? microinstruction_list_for_pop_rbp_1_seventh_microinstructions : 32'bz;  // Controlled_Buffer controlled_buffer_8
  assign microinstruction_to_be_executed__upper = pull_resistor_1_node[2] ? microinstruction_list_for_pop_rbp_1_third_microinstructions__upper : 32'bz;  // Controlled_Buffer controlled_buffer_9
  assign microinstruction_to_be_executed__upper = pull_resistor_1_node[3] ? microinstruction_list_for_pop_rbp_1_fourth_upper : 32'bz;  // Controlled_Buffer controlled_buffer_10
endmodule

module microinstruction_list_for_pop_rbp (
  output [31:0] first_microinstructions,
  output [31:0] third_microinstructions,
  output [31:0] fifth_microinstructions,
  output [31:0] seventh_microinstructions,
  output [31:0] fourth_upper,
  output [31:0] second_microinstructions,
  output [31:0] fourth_microinstructions,
  output [31:0] sixth_microinstructions,
  output [31:0] third_microinstructions__upper
);

  Pull_Resistor pull_resistor_1 (.node(fifth_microinstructions[31]));
  Pull_Resistor #(.pull(1)) pull_resistor_2 (.node(first_microinstructions[20]));

  assign fifth_microinstructions[30:0] = {31{fifth_microinstructions[31]}};
  assign {first_microinstructions[31:21], first_microinstructions[19:0]} = {{11{fifth_microinstructions[31]}}, first_microinstructions[20], {6{fifth_microinstructions[31]}}, first_microinstructions[20], {6{fifth_microinstructions[31]}}, first_microinstructions[20], {5{fifth_microinstructions[31]}}};
  assign fourth_microinstructions = {{3{fifth_microinstructions[31]}}, first_microinstructions[20], fifth_microinstructions[31], first_microinstructions[20], {26{fifth_microinstructions[31]}}};
  assign fourth_upper = {32{fifth_microinstructions[31]}};
  assign second_microinstructions = {{27{fifth_microinstructions[31]}}, first_microinstructions[20], {4{fifth_microinstructions[31]}}};
  assign seventh_microinstructions = {32{fifth_microinstructions[31]}};
  assign sixth_microinstructions = {32{fifth_microinstructions[31]}};
  assign third_microinstructions = {first_microinstructions[20], {10{fifth_microinstructions[31]}}, {2{first_microinstructions[20]}}, {19{fifth_microinstructions[31]}}};
  assign third_microinstructions__upper = {{24{fifth_microinstructions[31]}}, first_microinstructions[20], {7{fifth_microinstructions[31]}}};
endmodule
